// Logisim project s-mips.circ as structural Verilog: 43 circuits, main circuit S-MIPS Board
module S_MIPS_Board (
  output halt
);

  wire button_1_out, CLK, CS, d_ff_1_q, R_W, Reset_out, RST, TTY_EN;
  wire [2:0] KDB;
  wire [3:0] Mask, ram_1_read_time, ram_1_write_time;
  wire [6:0] KDB_DATA, TTY_DATA;
  wire [15:0] Addr;
  wire [31:0] ram_1_data_out_0, ram_1_data_out_1, ram_1_data_out_2, ram_1_data_out_3, s_mips_1_ram_in_0,
       s_mips_1_ram_in_1, s_mips_1_ram_in_2, s_mips_1_ram_in_3;

  TTY #(.rows(25), .cols(80)) tty_1 (.data(TTY_DATA), .clk(CLK), .we(TTY_EN), .clr(RST));
  RAM ram_1 (
    .Address(Addr), .Data_Out_0(ram_1_data_out_0), .Data_Out_1(ram_1_data_out_1),
    .Data_Out_2(ram_1_data_out_2), .Data_Out_3(ram_1_data_out_3), .Data_In_0(s_mips_1_ram_in_0),
    .Data_In_1(s_mips_1_ram_in_1), .Data_In_2(s_mips_1_ram_in_2), .Data_In_3(s_mips_1_ram_in_3), .Mask(Mask),
    .nRead_Write(R_W), .Chip_Select(CS), .Read_Time(ram_1_read_time), .Reset(button_1_out),
    .Write_Time(ram_1_write_time));
  Button button_1 (.out(button_1_out));
  Keyboard #(.buflen(64)) keyboard_1 (.clk(CLK), .re(KDB[0]), .avail(KDB[2]), .data(KDB_DATA));  // open: clr
  S_MIPS s_mips_1 (
    .Kbd_Enable(KDB[0]), .Address(Addr), .Kbd_Clear(KDB[1]), .Kbd_Available(KDB[2]),
    .RAM_In_0(s_mips_1_ram_in_0), .Kbd_ASCII_Data(KDB_DATA), .RAM_In_1(s_mips_1_ram_in_1),
    .TTY_Enable(TTY_EN), .RAM_In_2(s_mips_1_ram_in_2), .RAM_In_3(s_mips_1_ram_in_3),
    .TTY_ASCII_Data(TTY_DATA), .Reset(RST), .RAM_Out_0(ram_1_data_out_0), .Clock(CLK),
    .RAM_Out_1(ram_1_data_out_1), .Stop(halt), .RAM_Out_2(ram_1_data_out_2), .RAM_Out_3(ram_1_data_out_3),
    .Mask(Mask), .Read_Time(ram_1_read_time), .Write_Time(ram_1_write_time), .nRead_Write(R_W),
    .Chip_Select(CS));
  D_Flip_Flop d_ff_1 (.clk(CLK), .D(1'b1), .Q(d_ff_1_q), .reset(Reset_out));  // open: Qn, preset, en
  Button Reset (.out(Reset_out));
  Clock clock_1 (.out(CLK));
  D_Flip_Flop d_ff_2 (.clk(CLK), .D(d_ff_1_q), .Qn(RST), .reset(Reset_out));  // open: Q, preset, en

  // Notes on the sheet:
  //   NO MODIFICAR
  //   Keyboard
endmodule

module RAM (
  input  [15:0] Address,
  input  [31:0] Data_In_0,
  input  [31:0] Data_In_1,
  input  [31:0] Data_In_2,
  input  [31:0] Data_In_3,
  input  [3:0] Mask,
  input  nRead_Write,
  input  Chip_Select,
  input  Reset,
  output [31:0] Data_Out_0,
  output [31:0] Data_Out_1,
  output [31:0] Data_Out_2,
  output [31:0] Data_Out_3,
  output [3:0] Read_Time,
  output [3:0] Write_Time
);

  wire and_2_out, and_3_out, and_4_out, and_5_out, and_6_out, and_7_out, and_8_out, and_9_out, Changed, CLK,
       comparator_2_eq, comparator_3_eq, comparator_4_eq, comparator_5_eq, comparator_6_eq, Count,
       demultiplexer_3_out0, Idle, Idle_q, Load, Load0, Load1, nand_1_out, or_1_out, or_2_out, or_3_out,
       or_4_out, or_5_out, or_6_out, or_7_out, or_8_out, or_9_out, or_10_out, Proc_q, Update_Mem, Zero_Time;
  wire [3:0] counter_1_q, multiplexer_1_out, subtractor_1_out;
  wire [31:0] register_1_q, register_2_q, register_3_q, register_4_q, register_5_q;

  // Probe on 4'b0011
  // Probe on 4'b0101
  Multiplexer #(.width(4), .enable("false")) multiplexer_1 (
    .in0(4'b0011), .in1(4'b0101), .out(multiplexer_1_out), .sel(nRead_Write));
  or or_1 (or_1_out, Idle, Update_Mem);
  or or_2 (or_2_out, ~Chip_Select, Reset);  // OR_Gate
  Subtractor #(.width(4)) subtractor_1 (.a(multiplexer_1_out), .b(4'b0010), .out(subtractor_1_out));  // open: bin, bout
  D_Flip_Flop u_Idle (.clk(CLK), .D(or_1_out), .Q(Idle_q), .preset(or_2_out));  // open: Qn, en, reset
  Demultiplexer #(.enable("false")) demultiplexer_1 (.out0(Idle), .out1(Load0), .in(Idle_q), .sel(Changed));
  // Probe on counter_1_q
  Counter #(.width(4), .max('hf)) counter_1 (
    .load(Load), .D(subtractor_1_out), .count(Count), .Q(counter_1_q), .clk(CLK), .clr(or_3_out));  // open: carry
  or or_3 (or_3_out, ~Chip_Select, Reset);  // OR_Gate
  Comparator #(.width(4), .mode("unsigned")) comparator_1 (
    .a(4'b0000), .b(counter_1_q), .eq(Zero_Time));  // open: gt, lt
  or or_4 (or_4_out, Count, Load0, Load1);
  Register #(.width(32)) register_1 (.D(Data_In_0), .en(Chip_Select), .Q(register_1_q), .clk(CLK), .clr(or_5_out));
  or or_5 (or_5_out, ~Chip_Select, Reset);  // OR_Gate
  Register #(.width(32)) register_2 (.D(Data_In_1), .en(Chip_Select), .Q(register_2_q), .clk(CLK), .clr(or_6_out));
  or or_6 (or_6_out, ~Chip_Select, Reset);  // OR_Gate
  Register #(.width(32)) register_3 (.D(Data_In_2), .en(Chip_Select), .Q(register_3_q), .clk(CLK), .clr(or_7_out));
  or or_7 (or_7_out, ~Chip_Select, Reset);  // OR_Gate
  Register #(.width(32)) register_4 (.D(Data_In_3), .en(Chip_Select), .Q(register_4_q), .clk(CLK), .clr(or_8_out));
  or or_8 (or_8_out, ~Chip_Select, Reset);  // OR_Gate
  Register #(.width(32)) register_5 (
    .D({{11{1'b1}}, nRead_Write, Mask, Address}), .en(Chip_Select), .Q(register_5_q), .clk(CLK),
    .clr(or_9_out));
  or or_9 (or_9_out, ~Chip_Select, Reset);  // OR_Gate
  D_Flip_Flop Proc (.clk(CLK), .D(or_4_out), .Q(Proc_q), .reset(or_10_out));  // open: Qn, preset, en
  or or_10 (or_10_out, ~Chip_Select, Reset);  // OR_Gate
  Demultiplexer #(.enable("false")) demultiplexer_2 (
    .out0(Count), .out1(Update_Mem), .in(demultiplexer_3_out0), .sel(Zero_Time));
  Demultiplexer #(.enable("false")) demultiplexer_3 (
    .out0(demultiplexer_3_out0), .out1(Load1), .in(Proc_q), .sel(Changed));
  Clock clock_1 (.out(CLK));
  Comparator #(.width(32)) comparator_2 (.a(register_1_q), .b(Data_In_0), .eq(comparator_2_eq));  // open: gt, lt
  Comparator #(.width(32)) comparator_3 (.a(register_2_q), .b(Data_In_1), .eq(comparator_3_eq));  // open: gt, lt
  Comparator #(.width(32)) comparator_4 (.a(register_3_q), .b(Data_In_2), .eq(comparator_4_eq));  // open: gt, lt
  Comparator #(.width(32)) comparator_5 (.a(register_4_q), .b(Data_In_3), .eq(comparator_5_eq));  // open: gt, lt
  Comparator #(.width(32)) comparator_6 (
    .a(register_5_q), .b({{11{1'b1}}, nRead_Write, Mask, Address}), .eq(comparator_6_eq));  // open: gt, lt
  nand nand_1 (nand_1_out, comparator_6_eq, comparator_2_eq, comparator_3_eq, comparator_4_eq, comparator_5_eq);
  and and_1 (Changed, nand_1_out, Chip_Select);
  or or_11 (Load, Count, Load1, Load0);
  and and_2 (and_2_out, Mask[0], Update_Mem, nRead_Write);
  and and_3 (and_3_out, Mask[1], Update_Mem, nRead_Write);
  and and_4 (and_4_out, Mask[2], Update_Mem, nRead_Write);
  and and_5 (and_5_out, Mask[3], Update_Mem, nRead_Write);
  // Probe on Data_Out_0
  RAM_part #(.addrWidth(16), .dataWidth(32), .bus("separate")) ram_1 (
    .addr(Address), .din(Data_In_0), .data(Data_Out_0), .str(and_2_out), .sel(Chip_Select), .clk(CLK),
    .ld(and_6_out), .clr(Reset));
  and and_6 (and_6_out, ~nRead_Write, Idle);  // AND_Gate
  RAM_part #(.addrWidth(16), .dataWidth(32), .bus("separate")) ram_2 (
    .addr(Address), .din(Data_In_1), .data(Data_Out_1), .str(and_3_out), .sel(Chip_Select), .clk(CLK),
    .ld(and_7_out), .clr(Reset));
  and and_7 (and_7_out, ~nRead_Write, Idle);  // AND_Gate
  RAM_part #(.addrWidth(16), .dataWidth(32), .bus("separate")) ram_3 (
    .addr(Address), .din(Data_In_2), .data(Data_Out_2), .str(and_4_out), .sel(Chip_Select), .clk(CLK),
    .ld(and_8_out), .clr(Reset));
  and and_8 (and_8_out, ~nRead_Write, Idle);  // AND_Gate
  RAM_part #(.addrWidth(16), .dataWidth(32), .bus("separate")) ram_4 (
    .addr(Address), .din(Data_In_3), .data(Data_Out_3), .str(and_5_out), .sel(Chip_Select), .clk(CLK),
    .ld(and_9_out), .clr(Reset));
  and and_9 (and_9_out, ~nRead_Write, Idle);  // AND_Gate
  // Probe on Data_Out_1
  // Probe on Data_Out_2
  // Probe on Data_Out_3

  assign Read_Time = 4'b0011;
  assign Write_Time = 4'b0101;

  // Other names for the same wires on the sheet: M0 = Mask[0]; M1 = Mask[1]; M2 = Mask[2]; M3 = Mask[3];
  //   RW = nRead_Write; CLR = Reset; CS = Chip_Select; Load2 = Count

  // Notes on the sheet:
  //   NO MODIFICAR
  //   excepto quizás los valores RT y WT
  //   BANK0
  //   BANK1
  //   BANK2
  //   BANK3
endmodule

module S_MIPS (
  input  Kbd_Available,
  input  [6:0] Kbd_ASCII_Data,
  input  [31:0] RAM_Out_0,
  input  [31:0] RAM_Out_1,
  input  Reset,
  input  [31:0] RAM_Out_2,
  input  Clock,
  input  [31:0] RAM_Out_3,
  input  [3:0] Read_Time,
  input  [3:0] Write_Time,
  output Kbd_Enable,
  output [15:0] Address,
  output Kbd_Clear,
  output TTY_Enable,
  output [6:0] TTY_ASCII_Data,
  output Stop,
  output [31:0] RAM_In_0,
  output [31:0] RAM_In_1,
  output [31:0] RAM_In_2,
  output [31:0] RAM_In_3,
  output [3:0] Mask,
  output nRead_Write,
  output Chip_Select
);

  wire _1, _1_1, and_1_out, and_2_out, and_3_out, and_4_out, and_5_out, beq, bgtz, blez, bltz, bne, C, CS1,
       CS2, d_ff_1_q, d_ff_2_q, d_ff_3_q, d_ff_4_q, d_ff_5_q, d_ff_8_q, DECSP, demultiplexer_1_out0,
       demultiplexer_2_out0, demultiplexer_3_out0, demultiplexer_4_out0, demultiplexer_5_out0,
       demultiplexer_6_out0, demultiplexer_7_out0, demultiplexer_9_out0, EN_Instruc, ENHiLo, ENMR, ENMR1,
       ENMR2, ENMR3, ENMRFC, ENMW, ENMW1, ENMW2, ENPC, ENPC1, ENPC2, ENPC3, ENPC4, ENPC5, ENPC7, FR, INC_PC,
       InCache, j, jr, kbd_t, lw, minus_R_W_RF, minus_R_W_RF_OnlyCicle, N, O, or_2_out, or_3_out, or_4_out,
       or_5_out, or_6_out, or_7_out, or_8_out, or_9_out, or_11_out, or_12_out, or_13_out, or_14_out,
       or_15_out, or_17_out, pop, push, ReadyMR, ReadyMW, rnd_t, S_AddrMW, S_AddrMW2, S_B_ALU, S_BA_RF,
       S_InputMW, STARTlw_2_q, STARTPop_q, STARTPush_q, STARTsw_q, STARTtty_q, sw, tty, U, WaitMW_q, WRITE,
       WRITE1, WRITE2, WriteRAM2, Z;
  wire [0:0] S_AddrMR2;
  wire [1:0] S_AddrMR, S_DA_RF;
  wire [1:1] S_AddrMR4;
  wire [2:0] FS, S_ID_RF;
  wire [3:0] MaskC;
  wire [4:0] mux2_5bits_1_out_4, mux4_5bits_1_out_6, Rd, Rs, Rt;
  wire [15:0] ADDRC, k, RAM_A_MR, RAM_A_MW;
  wire [19:0] ADDR_READ, ADDR_WRITE, lw_sw_Value, mux2_20bits_2_out_4, PC_in, PC_out;
  wire [25:0] Jump;
  wire [31:0] _00, _01, _02, _03, ALU, B, C_ID, Hi, K_32, Kbd, Lo, mux2_2_out_4, mux2_3_out_4, mux8_1_out_10,
       RAM, RAM_R, Rnd;
  wire [31:7] A;

  and and_1 (and_1_out, ENMR, ~d_ff_2_q, ~d_ff_3_q);  // AND_Gate
  and and_2 (and_2_out, ~d_ff_1_q, ~d_ff_2_q, ReadyMR);  // AND_Gate
  MUX2_16bits mux2_16bits_1 (.in_1(RAM_A_MR), .in_2(RAM_A_MW), .out_4(Address), .in_3(nRead_Write));
  MUX4_20bits mux4_20bits_1 (
    .in_1(PC_out), .in_2(B[19:0]), .in_3(lw_sw_Value), .in_4(lw_sw_Value), .out_6(ADDR_READ), .in_5(S_AddrMR));
  MUX2_20bits mux2_20bits_1 (.in_1(B[19:0]), .in_2(lw_sw_Value), .out_4(ADDR_WRITE), .in_3(S_AddrMW));
  or or_1 (Chip_Select, CS1, CS2);
  D_Flip_Flop d_ff_1 (.clk(Clock), .D(and_1_out), .Q(d_ff_1_q), .reset(Reset));  // open: Qn, preset, en
  D_Flip_Flop d_ff_2 (.clk(Clock), .D(and_3_out), .Q(d_ff_2_q), .reset(Reset));  // open: Qn, preset, en
  and and_3 (and_3_out, ENMW, ~d_ff_1_q, ~d_ff_3_q);  // AND_Gate
  D_Flip_Flop d_ff_3 (.clk(Clock), .D(and_2_out), .Q(d_ff_3_q), .reset(Reset));  // open: Qn, preset, en
  or or_2 (or_2_out, ReadyMR, ENMW);
  D_Flip_Flop d_ff_4 (.clk(Clock), .D(ENMR), .Q(d_ff_4_q), .reset(Reset));  // open: Qn, preset, en
  or or_3 (or_3_out, d_ff_1_q, d_ff_2_q, d_ff_3_q);
  and and_4 (and_4_out, ~InCache, or_4_out);  // AND_Gate
  or or_4 (or_4_out, d_ff_4_q, d_ff_5_q);
  D_Flip_Flop #(.trigger("falling")) d_ff_5 (
    .clk(Reset), .D(1'b1), .Q(d_ff_5_q), .reset(ReadyMR));  // open: Qn, preset, en
  Register #(.width(20)) PC (.D(PC_in), .en(ENPC), .Q(PC_out), .clk(Clock), .clr(Reset));
  Cache cache_1 (
    .minus_R_W(or_2_out), .CLK(Clock), .CLR(Reset), .I0(RAM_Out_0), .I1(RAM_Out_1), .I2(RAM_Out_2),
    .I3(RAM_Out_3), .ADDRIN(mux2_20bits_2_out_4), .O0(_00), .O1(_01), .O2(_02), .O3(_03), .Ready(InCache),
    .Mask(4'b1111), .out_18(RAM), .Dirty(ENMRFC), .EN(or_3_out), .Clear_Dirty(ReadyMW), .ADDR_out(ADDRC),
    .MASK_2(MaskC), .Write_RAM(ENMW), .Input_To_RAM(mux2_2_out_4));
  Memory_Writer_Cache memory_writer_cache_1 (
    .Data0(RAM_In_0), .Data1(RAM_In_1), .Data2(RAM_In_2), .Data3(RAM_In_3), .ADDR_2(RAM_A_MW),
    .READY(ReadyMW), .Mask_2(Mask), .I0(_00), .I1(_01), .I2(_02), .I3(_03), .ADDR(ADDRC), .WT(Write_Time),
    .CS(CS2), .minus_R_W(nRead_Write), .CLK(Clock), .EN(ENMRFC), .Clear(Reset), .Mask(MaskC));
  MemoryReader memoryreader_1 (
    .ADDR_2(RAM_A_MR), .READY(ReadyMR), .Data0(RAM_Out_0), .Data1(RAM_Out_1), .Data2(RAM_Out_2),
    .Data3(RAM_Out_3), .ADDR(ADDR_READ), .RT(Read_Time), .CS(CS1), .CLK(Clock), .EN(and_4_out), .Clear(Reset));
  or or_5 (or_5_out, S_AddrMR[0], S_AddrMR[1]);
  Random #(.width(32)) random_1 (.clk(Clock), .next(rnd_t), .out(Rnd));  // open: clr
  MUX2 mux2_1 (.in_1({32{1'b1}}), .in_2({{25{1'b0}}, Kbd_ASCII_Data}), .out_4(Kbd), .in_3(Kbd_Available));
  D_Flip_Flop d_ff_6 (.clk(Clock), .D(and_5_out), .Q(EN_Instruc), .reset(Reset));  // open: Qn, preset, en
  and and_5 (and_5_out, InCache, ~or_6_out);  // AND_Gate
  or or_6 (or_6_out, WRITE, or_5_out);
  MUX2_20bits mux2_20bits_2 (.in_1(ADDR_READ), .in_2(ADDR_WRITE), .out_4(mux2_20bits_2_out_4), .in_3(WRITE));
  MUX2 mux2_2 (.in_1({A, TTY_ASCII_Data}), .in_2(B), .out_4(mux2_2_out_4), .in_3(S_InputMW));
  D_Flip_Flop #(.trigger("falling")) d_ff_7 (
    .clk(Clock), .D(d_ff_8_q), .Q(ENMR3), .reset(Reset));  // open: Qn, preset, en
  D_Flip_Flop #(.trigger("falling")) d_ff_8 (
    .clk(Clock), .D(ENPC), .Q(d_ff_8_q), .reset(Reset));  // open: Qn, preset, en
  // Probe on RAM_R
  MUX8 mux8_1 (
    .in_1(ALU), .in_2(Hi), .in_3(Lo), .in_4(RAM_R), .in_5(C_ID), .in_7(Rnd), .in_8(Kbd), .in_9(Kbd),
    .out_10(mux8_1_out_10), .in_6(S_ID_RF));
  or or_7 (or_7_out, minus_R_W_RF, minus_R_W_RF_OnlyCicle);
  or or_8 (or_8_out, demultiplexer_1_out0, ENPC1);
  or or_9 (or_9_out, demultiplexer_2_out0, ENPC3);
  MUX4_5bits mux4_5bits_1 (
    .in_1(Rd), .in_2(Rt), .in_3({5{1'b1}}), .in_4({5{1'b1}}), .out_6(mux4_5bits_1_out_6), .in_5(S_DA_RF));
  REGFILE regfile_1 (
    .R_W(or_7_out), .INPUT(mux8_1_out_10), .CLK(Clock), .A({A, TTY_ASCII_Data}), .DA(mux4_5bits_1_out_6),
    .AA(Rs), .BA(mux2_5bits_1_out_4), .B(B), .Clear(Reset), .INCSP(ENPC3), .DECSP(DECSP));
  Estados estados_1 (
    .in_3(RAM_R), .IncPC(INC_PC), .minus_R_W(minus_R_W_RF_OnlyCicle), .ENHiLo(ENHiLo), .Rs(Rs), .Rt(Rt),
    .K(k), .Rd(Rd), .U(U), .Jump(Jump), .j(j), .S_B(S_B_ALU), .cte(K_32), .O(O), .Z(Z), .S(N), .C(C),
    .FS(FS), .C_ID(C_ID), .SDA(S_DA_RF), .halt(Stop), .tty(tty), .rnd(rnd_t), .kbd(kbd_t), .pop(pop),
    .push(push), .bne(bne), .blez(blez), .bgtz(bgtz), .bltz(bltz), .beq(beq), .sw(sw), .lw(lw), .jr(jr),
    .S_ID(S_ID_RF), .S_BA(S_BA_RF), .EN(EN_Instruc), .IncPC_1ciclo(ENPC7), .CLK(Clock), .Clear(Reset));
  D_Flip_Flop STARTPush (.clk(Clock), .D(or_8_out), .Q(STARTPush_q), .preset(Reset));  // open: Qn, en, reset
  D_Flip_Flop STARTPop (.clk(Clock), .D(or_9_out), .Q(STARTPop_q), .preset(Reset));  // open: Qn, en, reset
  MUX2_5bits mux2_5bits_1 (.in_1(Rt), .in_2({5{1'b1}}), .out_4(mux2_5bits_1_out_4), .in_3(S_BA_RF));
  BranchControlUnity branchcontrolunity_1 (
    .PC_In(PC_out), .INC(INC_PC), .beq(beq), .bne(bne), .blez(blez), .bgtz(bgtz), .bltz(bltz), .j(j),
    .jr(jr), .Rs({A, TTY_ASCII_Data}), .Rt(B), .InmediateDestiny(Jump), .offset(k), .PC_Out(PC_in));
  Demultiplexer #(.enable("false")) demultiplexer_1 (
    .out0(demultiplexer_1_out0), .out1(DECSP), .in(STARTPush_q), .sel(push));
  Demultiplexer #(.enable("false")) demultiplexer_2 (
    .out0(demultiplexer_2_out0), .out1(ENMR1), .in(STARTPop_q), .sel(pop));
  D_Flip_Flop STARTlw (.clk(Clock), .D(DECSP), .Q(ENMW1), .reset(Reset));  // open: Qn, preset, en
  or or_10 (WRITE1, demultiplexer_3_out0, ENMW1);
  or or_11 (or_11_out, demultiplexer_4_out0, ENMR1);
  Demultiplexer #(.enable("false")) demultiplexer_3 (
    .out0(demultiplexer_3_out0), .out1(ENPC1), .in(WaitMW_q), .sel(FR));
  D_Flip_Flop WaitMW (.clk(Clock), .D(WRITE1), .Q(WaitMW_q), .reset(Reset));  // open: Qn, preset, en
  D_Flip_Flop WaitMR (.clk(Clock), .D(or_11_out), .Q(S_AddrMR2[0]), .reset(Reset));  // open: Qn, preset, en
  D_Flip_Flop WaitMR_2 (.clk(Clock), .D(InCache), .Q(FR));  // open: Qn, preset, en, reset
  or or_12 (or_12_out, demultiplexer_5_out0, ENPC5);
  Demultiplexer #(.enable("false")) demultiplexer_4 (
    .out0(demultiplexer_4_out0), .out1(ENPC3), .in(S_AddrMR2[0]), .sel(FR));
  ALU alu_1 (
    .out(ALU), .EN_Hi_Lo(ENHiLo), .CLK(Clock), .Hi(Hi), .Lo(Lo), .FS(FS), .C(C), .N(N), .Unsigned(U),
    .A({A, TTY_ASCII_Data}), .B(mux2_3_out_4), .Z(Z), .Overflow(O), .Clear(Reset));
  D_Flip_Flop STARTtty (.clk(Clock), .D(or_12_out), .Q(STARTtty_q), .preset(Reset));  // open: Qn, en, reset
  MUX2 mux2_3 (.in_1(B), .in_2(K_32), .out_4(mux2_3_out_4), .in_3(S_B_ALU));
  Demultiplexer #(.enable("false")) demultiplexer_5 (
    .out0(demultiplexer_5_out0), .out1(TTY_Enable), .in(STARTtty_q), .sel(tty));
  or or_13 (or_13_out, demultiplexer_6_out0, ENPC2);
  or or_14 (or_14_out, demultiplexer_7_out0, ENPC4);
  D_Flip_Flop STARTsw (.clk(Clock), .D(or_13_out), .Q(STARTsw_q), .preset(Reset));  // open: Qn, en, reset
  D_Flip_Flop STARTlw_2 (.clk(Clock), .D(or_14_out), .Q(STARTlw_2_q), .preset(Reset));  // open: Qn, en, reset
  Register #(.width(20)) register_1 (.D(ALU[19:0]), .en(or_15_out), .Q(lw_sw_Value), .clk(Clock), .clr(Reset));
  or or_15 (or_15_out, sw, lw);
  Demultiplexer #(.enable("false")) demultiplexer_6 (
    .out0(demultiplexer_6_out0), .out1(_1_1), .in(STARTsw_q), .sel(sw));
  Demultiplexer #(.enable("false")) demultiplexer_7 (
    .out0(demultiplexer_7_out0), .out1(_1), .in(STARTlw_2_q), .sel(lw));
  D_Flip_Flop WaitCiclo (.clk(Clock), .D(TTY_Enable), .Q(ENPC5));  // open: Qn, preset, en, reset
  D_Flip_Flop STARTlw_3 (.clk(Clock), .D(_1_1), .Q(ENMW2), .reset(Reset));  // open: Qn, preset, en
  D_Flip_Flop STARTlw_4 (.clk(Clock), .D(_1), .Q(ENMR2), .reset(Reset));  // open: Qn, preset, en
  or or_16 (WRITE2, WriteRAM2, ENMW2);
  or or_17 (or_17_out, demultiplexer_9_out0, ENMR2);
  or or_18 (minus_R_W_RF, ENPC3, ENPC4);
  or or_19 (ENMR, ENMR1, ENMR2, ENMR3);
  or or_20 (ENMW, ENMW1, ENMW2);
  assign S_AddrMR = {1'b0, ENMR1} | {1'b0, S_AddrMR2[0]} | {ENMR2, 1'b0} | {S_AddrMR4[1], 1'b0};  // OR_Gate or_21, 2 bits wide
  or or_22 (S_InputMW, ENMW2, S_AddrMW2);
  or or_23 (S_AddrMW, ENMW2, S_AddrMW2);
  D_Flip_Flop WaitMW_2 (.clk(Clock), .D(WRITE2), .Q(S_AddrMW2), .reset(Reset));  // open: Qn, preset, en
  D_Flip_Flop WaitMR_3 (.clk(Clock), .D(or_17_out), .Q(S_AddrMR4[1]), .reset(Reset));  // open: Qn, preset, en
  or or_24 (ENPC, ENPC1, ENPC2, ENPC3, ENPC4, ENPC5, 1'b0, ENPC7);
  Demultiplexer #(.enable("false")) demultiplexer_8 (.out0(WriteRAM2), .out1(ENPC2), .in(S_AddrMW2), .sel(FR));
  Demultiplexer #(.enable("false")) demultiplexer_9 (
    .out0(demultiplexer_9_out0), .out1(ENPC4), .in(S_AddrMR4[1]), .sel(FR));
  or or_25 (WRITE, WRITE1, WRITE2);
  ResolverRAMValue resolverramvalue_1 (.in_1(RAM), .out_2(RAM_R));

  assign Kbd_Clear = 1'b0;
  assign Kbd_Enable = 1'b0;

  // Other names for the same wires on the sheet: A[6:0] = TTY_ASCII_Data; TTY_DATA[6:0] = TTY_ASCII_Data; CLK = Clock;
  //   CLR = Reset; CS = Chip_Select; minus_R_W_RF_2 = ENPC4; halt = Stop; INCSP = ENPC3; minus_R_W_RF_1 = ENPC3;
  //   KBD_AVAIL = Kbd_Available; KBD_DATA[6:0] = Kbd_ASCII_Data; KBD_DATA_32[6:0] = Kbd_ASCII_Data;
  //   RAM_A[15:0] = Address; RAM_INPUT_0[31:0] = RAM_In_0; RAM_INPUT_1[31:0] = RAM_In_1; RAM_INPUT_2[31:0] = RAM_In_2;
  //   RAM_INPUT_3[31:0] = RAM_In_3; RAM_MASK[3:0] = Mask; RAM_OUTPUT_0[31:0] = RAM_Out_0;
  //   RAM_OUTPUT_1[31:0] = RAM_Out_1; RAM_OUTPUT_2[31:0] = RAM_Out_2; RAM_OUTPUT_3[31:0] = RAM_Out_3;
  //   RW = nRead_Write; S_AddrMR1[0] = ENMR1; S_AddrMR3[1] = ENMR2; S_AddrMW1 = ENMW2; S_InputMW1 = ENMW2;
  //   S_InputMW2 = S_AddrMW2; SP_ADDR[19:0] = B[19:0]

  // Notes on the sheet:
  //   RAM ADDRESS
  //   DATA FROM RAM
  //   DATA TO RAM
  //   DATA WRITE MASK
  //   RAM TIMING
  //   RAM CONTROL
  //   KEYBOARD
  //   TTY
  //   SEQUENCING
  //   Esto lo tienen que borrar:
  //   Push State Machine
  //   Pop State Machine
  //   tty State Machine
  //   sw State Machine
  //   lw State Machine
endmodule

module REGFILE (
  input  R_W,
  input  [4:0] DA,
  input  [4:0] AA,
  input  [4:0] BA,
  input  [31:0] INPUT,
  input  CLK,
  input  INCSP,
  input  Clear,
  input  DECSP,
  output [31:0] A,
  output [31:0] B
);

  wire or_2_out, R0_en, R1_en, R2_en, R3_en, R4_en, R5_en, R6_en, R7_en, R8_en, R9_en, R10_en, R11_en,
       R12_en, R13_en, R14_en, R15_en, R16_en, R17_en, R18_en, R19_en, R20_en, R21_en, R22_en, R23_en,
       R24_en, R25_en, R26_en, R27_en, R28_en, R29_en, R30_en, R31_en;
  wire [0:0] or_1_out;
  wire [31:0] mux2_1_out_4, mux4_1_out_6, R1_out, R2_out, R3_out, R4_out, R5_out, R6_out, R7_out, R8_out,
       R9_out, R10_out, R11_out, R12_out, R13_out, R14_out, R15_out, R16_out, R17_out, R18_out, R19_out,
       R20_out, R21_out, R22_out, R23_out, R24_out, R25_out, R26_out, R27_out, R28_out, R29_out, R30_out,
       R31_out, SP__4;

  Demultiplexer #(.select(5), .enable("false")) demultiplexer_1 (
    .out0(R0_en), .out1(R1_en), .out2(R2_en), .out3(R3_en), .out4(R4_en), .out5(R5_en), .out6(R6_en),
    .out7(R7_en), .out8(R8_en), .out9(R9_en), .out10(R10_en), .out11(R11_en), .out12(R12_en), .out13(R13_en),
    .out14(R14_en), .out15(R15_en), .out16(R16_en), .out17(R17_en), .out18(R18_en), .out19(R19_en),
    .out20(R20_en), .out21(R21_en), .out22(R22_en), .out23(R23_en), .out24(R24_en), .out25(R25_en),
    .out26(R26_en), .out27(R27_en), .out28(R28_en), .out29(R29_en), .out30(R30_en), .out31(R31_en), .in(R_W),
    .sel(DA));
  Register #(.width(32)) R4 (.D(INPUT), .en(R4_en), .Q(R4_out), .clk(CLK), .clr(Clear));
  Register #(.width(32)) R8 (.D(INPUT), .en(R8_en), .Q(R8_out), .clk(CLK), .clr(Clear));
  Register #(.width(32)) R12 (.D(INPUT), .en(R12_en), .Q(R12_out), .clk(CLK), .clr(Clear));
  Register #(.width(32)) R16 (.D(INPUT), .en(R16_en), .Q(R16_out), .clk(CLK), .clr(Clear));
  Register #(.width(32)) R20 (.D(INPUT), .en(R20_en), .Q(R20_out), .clk(CLK), .clr(Clear));
  Register #(.width(32)) R24 (.D(INPUT), .en(R24_en), .Q(R24_out), .clk(CLK), .clr(Clear));
  Register #(.width(32)) R28 (.D(INPUT), .en(R28_en), .Q(R28_out), .clk(CLK), .clr(Clear));
  MUX2 mux2_1 (.in_1(32'h4), .in_2(32'hfffffffc), .out_4(mux2_1_out_4), .in_3(DECSP));
  Register #(.width(32)) R1 (.D(INPUT), .en(R1_en), .Q(R1_out), .clk(CLK), .clr(Clear));
  Register #(.width(32)) R5 (.D(INPUT), .en(R5_en), .Q(R5_out), .clk(CLK), .clr(Clear));
  Register #(.width(32)) R9 (.D(INPUT), .en(R9_en), .Q(R9_out), .clk(CLK), .clr(Clear));
  Register #(.width(32)) R13 (.D(INPUT), .en(R13_en), .Q(R13_out), .clk(CLK), .clr(Clear));
  Register #(.width(32)) R17 (.D(INPUT), .en(R17_en), .Q(R17_out), .clk(CLK), .clr(Clear));
  Register #(.width(32)) R21 (.D(INPUT), .en(R21_en), .Q(R21_out), .clk(CLK), .clr(Clear));
  Register #(.width(32)) R25 (.D(INPUT), .en(R25_en), .Q(R25_out), .clk(CLK), .clr(Clear));
  Register #(.width(32)) R29 (.D(INPUT), .en(R29_en), .Q(R29_out), .clk(CLK), .clr(Clear));
  Adder #(.width(32)) adder_1 (.a(R31_out), .b(mux2_1_out_4), .out(SP__4));  // open: cin, cout
  Register #(.width(32)) R2 (.D(INPUT), .en(R2_en), .Q(R2_out), .clk(CLK), .clr(Clear));
  Register #(.width(32)) R6 (.D(INPUT), .en(R6_en), .Q(R6_out), .clk(CLK), .clr(Clear));
  Register #(.width(32)) R10 (.D(INPUT), .en(R10_en), .Q(R10_out), .clk(CLK), .clr(Clear));
  Register #(.width(32)) R14 (.D(INPUT), .en(R14_en), .Q(R14_out), .clk(CLK), .clr(Clear));
  Register #(.width(32)) R18 (.D(INPUT), .en(R18_en), .Q(R18_out), .clk(CLK), .clr(Clear));
  Register #(.width(32)) R22 (.D(INPUT), .en(R22_en), .Q(R22_out), .clk(CLK), .clr(Clear));
  Register #(.width(32)) R26 (.D(INPUT), .en(R26_en), .Q(R26_out), .clk(CLK), .clr(Clear));
  Register #(.width(32)) R30 (.D(INPUT), .en(R30_en), .Q(R30_out), .clk(CLK), .clr(Clear));
  MUX4 mux4_1 (
    .in_1(INPUT), .in_2(SP__4), .in_3({32{1'b1}}), .in_4({32{1'b1}}), .out_6(mux4_1_out_6),
    .in_5({Clear, or_1_out[0]}));
  or or_1 (or_1_out[0], INCSP, DECSP);
  Register #(.width(32)) R3 (.D(INPUT), .en(R3_en), .Q(R3_out), .clk(CLK), .clr(Clear));
  Register #(.width(32)) R7 (.D(INPUT), .en(R7_en), .Q(R7_out), .clk(CLK), .clr(Clear));
  Register #(.width(32)) R11 (.D(INPUT), .en(R11_en), .Q(R11_out), .clk(CLK), .clr(Clear));
  Register #(.width(32)) R15 (.D(INPUT), .en(R15_en), .Q(R15_out), .clk(CLK), .clr(Clear));
  Register #(.width(32)) R19 (.D(INPUT), .en(R19_en), .Q(R19_out), .clk(CLK), .clr(Clear));
  Register #(.width(32)) R23 (.D(INPUT), .en(R23_en), .Q(R23_out), .clk(CLK), .clr(Clear));
  Register #(.width(32)) R27 (.D(INPUT), .en(R27_en), .Q(R27_out), .clk(CLK), .clr(Clear));
  or or_2 (or_2_out, or_1_out[0], Clear, R31_en);
  Register #(.width(32)) R31 (.D(mux4_1_out_6), .en(or_2_out), .Q(R31_out), .clk(CLK));  // open: clr
  MUX32 mux32_1 (
    .in_1({32{1'b0}}), .in_2(R1_out), .in_3(R2_out), .in_4(R3_out), .in_5(R4_out), .in_6(R5_out),
    .in_7(R6_out), .in_8(R7_out), .in_9(R8_out), .in_10(R9_out), .in_11(R10_out), .in_12(R11_out),
    .in_13(R12_out), .in_14(R13_out), .in_15(R14_out), .in_16(R15_out), .in_17(R16_out), .in_18(R17_out),
    .in_19(R18_out), .in_20(R19_out), .in_21(R20_out), .in_22(R21_out), .in_23(R22_out), .in_24(R23_out),
    .in_25(R24_out), .in_26(R25_out), .in_27(R26_out), .in_28(R27_out), .in_29(R28_out), .in_30(R29_out),
    .in_31(R30_out), .in_32(R31_out), .in_33(AA), .out_34(A));
  MUX32 mux32_2 (
    .in_1({32{1'b0}}), .in_2(R1_out), .in_3(R2_out), .in_4(R3_out), .in_5(R4_out), .in_6(R5_out),
    .in_7(R6_out), .in_8(R7_out), .in_9(R8_out), .in_10(R9_out), .in_11(R10_out), .in_12(R11_out),
    .in_13(R12_out), .in_14(R13_out), .in_15(R14_out), .in_16(R15_out), .in_17(R16_out), .in_18(R17_out),
    .in_19(R18_out), .in_20(R19_out), .in_21(R20_out), .in_22(R21_out), .in_23(R22_out), .in_24(R23_out),
    .in_25(R24_out), .in_26(R25_out), .in_27(R26_out), .in_28(R27_out), .in_29(R28_out), .in_30(R29_out),
    .in_31(R30_out), .in_32(R31_out), .in_33(BA), .out_34(B));

  // Other names for the same wires on the sheet: IN[31:0] = INPUT
endmodule

module ALU (
  input  [2:0] FS,
  input  EN_Hi_Lo,
  input  CLK,
  input  Clear,
  input  Unsigned,
  input  [31:0] A,
  input  [31:0] B,
  output C,
  output [31:0] Lo,
  output Overflow,
  output [31:0] Hi,
  output [31:0] out,
  output N,
  output Z
);

  wire adder_2_cout, adder_4_cout, adder_6_cout, and_5_out, C_minus, C_plus, Negative, SelectADiv, SelectBDiv;
  wire [31:0] adder_2_out, adder_3_out, adder_4_out, adder_5_out, \and , C2A, C2B, divider_1_rem, DivLoS,
       DivLoU, Hi_t, Lo_t, MultHiS, MultHiU, MultLoS, MultLoU, mux2_1_out_4, mux2_2_out_4, mux2_3_out_4,
       mux2_4_out_4, mux2_7_out_4, mux2_8_out_4, negator_3_out, negator_4_out, not_1_out, \or , rem, rest,
       sum, \xor ;

  and and_1 (SelectADiv, A[31], ~Unsigned);  // AND_Gate
  and and_2 (SelectBDiv, B[31], ~Unsigned);  // AND_Gate
  xor xor_1 (Negative, A[31], B[31]);
  Negator #(.width(32)) negator_1 (.in(A), .out(C2A));
  Negator #(.width(32)) negator_2 (.in(B), .out(C2B));
  Adder #(.width(32)) adder_1 (.a(A), .b(B), .out(sum), .cout(C_plus));  // open: cin
  Subtractor #(.width(32)) subtractor_1 (.a(A), .b(B), .out(rest), .bout(C_minus));  // open: bin
  assign \and  = A & B;  // AND_Gate and_3, 32 bits wide
  assign \or  = A | B;  // OR_Gate or_1, 32 bits wide
  assign \xor  = A ^ B;  // XOR_Gate xor_2, 32 bits wide
  and and_4 (Overflow, A[31], ~rest[31], ~B[31]);  // AND_Gate
  assign not_1_out = ~\or ;  // NOT_Gate not_1, 32 bits wide
  MUX2 mux2_1 (.in_1(A), .in_2({1'b0, A[31:1]}), .out_4(mux2_1_out_4), .in_3(Unsigned));
  MUX2 mux2_2 (.in_1(B), .in_2({1'b0, B[31:1]}), .out_4(mux2_2_out_4), .in_3(Unsigned));
  Multiplexer #(.enable("false")) multiplexer_1 (.in0(C_plus), .in1(C_minus), .out(C), .sel(FS[0]));
  MUX8 mux8_1 (
    .in_1(sum), .in_2(rest), .in_3(\and ), .in_4(\or ), .in_5(not_1_out), .in_7(\xor ), .in_8({32{1'b0}}),
    .in_9({32{1'b0}}), .out_10({N, out[30:0]}), .in_6(FS));
  Multiplier #(.width(32)) multiplier_1 (
    .a(mux2_1_out_4), .b(mux2_2_out_4), .out(MultLoS), .cout(MultHiS));  // open: cin
  MUX2 mux2_3 (.in_1(A), .in_2(C2A), .out_4(mux2_3_out_4), .in_3(SelectADiv));
  MUX2 mux2_4 (.in_1(B), .in_2(C2B), .out_4(mux2_4_out_4), .in_3(SelectBDiv));
  Divider #(.width(32)) divider_1 (
    .a(mux2_3_out_4), .b(mux2_4_out_4), .out(DivLoU), .rem(divider_1_rem));  // open: upper
  Negator #(.width(32)) negator_3 (.in(divider_1_rem), .out(negator_3_out));
  MUX2 mux2_5 (.in_1(divider_1_rem), .in_2(negator_3_out), .out_4(rem), .in_3(A[31]));
  nor nor_1 (Z, N, out[30], out[29], out[28], out[27], out[26], out[25], out[24], out[23], out[22], out[21], out[20], out[19], out[18], out[17], out[16], out[15], out[14], out[13], out[12], out[11], out[10], out[9], out[8], out[7], out[6], out[5], out[4], out[3], out[2], out[1], out[0]);
  Negator #(.width(32)) negator_4 (.in(DivLoU), .out(negator_4_out));
  MUX2 mux2_6 (.in_1(DivLoU), .in_2(negator_4_out), .out_4(DivLoS), .in_3(Negative));
  Register #(.width(32)) u_Hi (.D(Hi_t), .en(EN_Hi_Lo), .Q(Hi), .clk(CLK), .clr(Clear));
  MUX4 mux4_1 (.in_1(DivLoS), .in_2(DivLoU), .in_3(MultLoS), .in_4(MultLoU), .out_6(Lo_t), .in_5({FS[0], Unsigned}));
  Register #(.width(32)) u_Lo (.D(Lo_t), .en(EN_Hi_Lo), .Q(Lo), .clk(CLK), .clr(Clear));
  MUX2 mux2_7 (.in_1({32{1'b0}}), .in_2({B[31:1], 1'b0}), .out_4(mux2_7_out_4), .in_3(A[0]));
  Adder #(.width(32)) adder_2 (
    .a({MultLoS[29:0], 2'b00}), .b(mux2_7_out_4), .out(adder_2_out), .cin(1'b0), .cout(adder_2_cout));
  MUX2 mux2_8 (.in_1({32{1'b0}}), .in_2({A[31:1], 1'b0}), .out_4(mux2_8_out_4), .in_3(B[0]));
  Adder #(.width(32)) adder_3 (
    .a({MultHiS[29:0], MultLoS[31:30]}), .b({32{1'b0}}), .out(adder_3_out), .cin(adder_2_cout));  // open: cout
  Adder #(.width(32)) adder_4 (.a(adder_2_out), .b(mux2_8_out_4), .out(adder_4_out), .cin(1'b0), .cout(adder_4_cout));
  Adder #(.width(32)) adder_5 (.a(adder_3_out), .b({32{1'b0}}), .out(adder_5_out), .cin(adder_4_cout));  // open: cout
  MUX4 mux4_2 (.in_1(rem), .in_2(rem), .in_3(MultHiS), .in_4(MultHiU), .out_6(Hi_t), .in_5({FS[0], Unsigned}));
  and and_5 (and_5_out, A[0], B[0]);
  Adder #(.width(32)) adder_6 (.a(adder_4_out), .b({32{1'b0}}), .out(MultLoU), .cin(and_5_out), .cout(adder_6_cout));
  Adder #(.width(32)) adder_7 (.a(adder_5_out), .b({32{1'b0}}), .out(MultHiU), .cin(adder_6_cout));  // open: cout

  assign out[31] = N;

  // Other names for the same wires on the sheet: Mult = FS[0]; _2_A_2[31:1] = A[31:1]; A_2[30:0] = A[31:1];
  //   minus_A = A[31]; _2_B_2[31:1] = B[31:1]; B_2[30:0] = B[31:1]; minus_B = B[31]
endmodule

module BranchControlUnity (
  input  [19:0] PC_In,
  input  INC,
  input  beq,
  input  bne,
  input  blez,
  input  bgtz,
  input  bltz,
  input  j,
  input  jr,
  input  [31:0] Rs,
  input  [31:0] Rt,
  input  [25:0] InmediateDestiny,
  input  [15:0] offset,
  output [19:0] PC_Out
);

  wire _0_t, _0_t_t, _0_t_t_t, not_1_out, or_1_out, or_2_out, or_4_out, tunnel, tunnel_t;
  wire [2:0] Select;
  wire [19:0] beq_Value, bgtz_Value, blez_Value, bltz_Value, bne_Value, PC_4, PC_4_4_offset;
  wire [31:0] xor_1_out;

  or or_1 (or_1_out, beq, bne, blez, bgtz, bltz, j, jr);
  not not_1 (not_1_out, or_1_out);
  or or_2 (or_2_out, not_1_out, INC);
  Priority_Encoder priority_encoder_1 (
    .in0(or_2_out), .in1(beq), .in2(bne), .in3(blez), .in4(bgtz), .in5(bltz), .in6(j), .in7(jr), .out(Select));  // open: en_in, gs, en_out
  assign xor_1_out = Rs ^ Rt;  // XOR_Gate xor_1, 32 bits wide
  or or_3 (tunnel, xor_1_out[31], xor_1_out[30], xor_1_out[29], xor_1_out[28], xor_1_out[27], xor_1_out[26], xor_1_out[25], xor_1_out[24], xor_1_out[23], xor_1_out[22], xor_1_out[21], xor_1_out[20], xor_1_out[19], xor_1_out[18], xor_1_out[17], xor_1_out[16], xor_1_out[15], xor_1_out[14], xor_1_out[13], xor_1_out[12], xor_1_out[11], xor_1_out[10], xor_1_out[9], xor_1_out[8], xor_1_out[7], xor_1_out[6], xor_1_out[5], xor_1_out[4], xor_1_out[3], xor_1_out[2], xor_1_out[1], xor_1_out[0]);
  not not_2 (tunnel_t, tunnel);
  Adder #(.width(20)) adder_1 (.a(PC_In), .b(20'h4), .out(PC_4));  // open: cin, cout
  Adder #(.width(20)) adder_2 (
    .a(PC_4), .b({{3{offset[15]}}, offset[14:0], 2'b00}), .out(PC_4_4_offset));  // open: cin, cout
  MUX8_20bits mux8_20bits_1 (
    .in_1(PC_4), .in_2(beq_Value), .in_3(bne_Value), .in_4(blez_Value), .in_5(bgtz_Value), .in_7(bltz_Value),
    .in_8({InmediateDestiny[17:0], 2'b00}), .in_9(Rs[19:0]), .out_10(PC_Out), .in_6(Select));
  and and_1 (_0_t_t_t, ~Rs[31], ~_0_t_t);  // AND_Gate
  not not_3 (_0_t, _0_t_t_t);
  or or_4 (or_4_out, Rs[31], Rs[30], Rs[29], Rs[28], Rs[27], Rs[26], Rs[25], Rs[24], Rs[23], Rs[22], Rs[21], Rs[20], Rs[19], Rs[18], Rs[17], Rs[16], Rs[15], Rs[14], Rs[13], Rs[12], Rs[11], Rs[10], Rs[9], Rs[8], Rs[7], Rs[6], Rs[5], Rs[4], Rs[3], Rs[2], Rs[1], Rs[0]);
  not not_4 (_0_t_t, or_4_out);
  MUX2_20bits mux2_20bits_1 (.in_1(PC_4), .in_2(PC_4_4_offset), .out_4(beq_Value), .in_3(tunnel_t));
  MUX2_20bits mux2_20bits_2 (.in_1(PC_4), .in_2(PC_4_4_offset), .out_4(bne_Value), .in_3(tunnel));
  MUX2_20bits mux2_20bits_3 (.in_1(PC_4), .in_2(PC_4_4_offset), .out_4(blez_Value), .in_3(_0_t));
  MUX2_20bits mux2_20bits_4 (.in_1(PC_4), .in_2(PC_4_4_offset), .out_4(bgtz_Value), .in_3(_0_t_t_t));
  MUX2_20bits mux2_20bits_5 (.in_1(PC_4), .in_2(PC_4_4_offset), .out_4(bltz_Value), .in_3(Rs[31]));

  // Other names for the same wires on the sheet: _4_offset[19:2] = {{3{offset[15]}}, offset[14:0]};
  //   j_Value[19:2] = InmediateDestiny[17:0]; jr_Value[19:0] = Rs[19:0]; _0 = Rs[31]
endmodule

module MUX2 (
  input  [31:0] in_1,
  input  [31:0] in_2,
  input  in_3,
  output [31:0] out_4
);

  wire decoder_1_out0, decoder_1_out1;

  Decoder #(.enable("false")) decoder_1 (.out0(decoder_1_out0), .out1(decoder_1_out1), .sel(in_3));
  Transistor #(.\type ("n"), .width(32)) transistor_1 (.in(in_1), .out(out_4), .gate(decoder_1_out0));
  Transistor #(.\type ("n"), .gate("br"), .width(32)) transistor_2 (.in(in_2), .out(out_4), .gate(decoder_1_out1));
endmodule

module MUX2_3bits (
  input  [2:0] in_1,
  input  [2:0] in_2,
  input  in_3,
  output [2:0] out_4
);

  wire a0, a1;

  Decoder #(.enable("false")) decoder_1 (.out0(a0), .out1(a1), .sel(in_3));
  Transistor #(.\type ("n"), .width(3)) transistor_1 (.in(in_1), .out(out_4), .gate(a0));
  Transistor #(.\type ("n"), .gate("br"), .width(3)) transistor_2 (.in(in_2), .out(out_4), .gate(a1));
endmodule

module MUX2_5bits (
  input  [4:0] in_1,
  input  [4:0] in_2,
  input  in_3,
  output [4:0] out_4
);

  wire a0, a1;

  Decoder #(.enable("false")) decoder_1 (.out0(a0), .out1(a1), .sel(in_3));
  Transistor #(.\type ("n"), .width(5)) transistor_1 (.in(in_1), .out(out_4), .gate(a0));
  Transistor #(.\type ("n"), .gate("br"), .width(5)) transistor_2 (.in(in_2), .out(out_4), .gate(a1));
endmodule

module MUX2_16bits (
  input  [15:0] in_1,
  input  [15:0] in_2,
  input  in_3,
  output [15:0] out_4
);

  wire decoder_1_out0, decoder_1_out1;

  Decoder #(.enable("false")) decoder_1 (.out0(decoder_1_out0), .out1(decoder_1_out1), .sel(in_3));
  Transistor #(.\type ("n"), .width(16)) transistor_1 (.in(in_1), .out(out_4), .gate(decoder_1_out0));
  Transistor #(.\type ("n"), .gate("br"), .width(16)) transistor_2 (.in(in_2), .out(out_4), .gate(decoder_1_out1));
endmodule

module MUX2_20bits (
  input  [19:0] in_1,
  input  [19:0] in_2,
  input  in_3,
  output [19:0] out_4
);

  wire decoder_1_out0, decoder_1_out1;

  Decoder #(.enable("false")) decoder_1 (.out0(decoder_1_out0), .out1(decoder_1_out1), .sel(in_3));
  Transistor #(.\type ("n"), .width(20)) transistor_1 (.in(in_1), .out(out_4), .gate(decoder_1_out0));
  Transistor #(.\type ("n"), .gate("br"), .width(20)) transistor_2 (.in(in_2), .out(out_4), .gate(decoder_1_out1));
endmodule

module MUX4 (
  input  [31:0] in_1,
  input  [31:0] in_2,
  input  [31:0] in_3,
  input  [31:0] in_4,
  input  [1:0] in_5,
  output [31:0] out_6
);

  wire a0, a1, a2, a3;

  Decoder #(.select(2), .enable("false")) decoder_1 (.out0(a0), .out1(a1), .out2(a2), .out3(a3), .sel(in_5));
  Transistor #(.\type ("n"), .width(32)) transistor_1 (.in(in_1), .out(out_6), .gate(a0));
  Transistor #(.\type ("n"), .gate("br"), .width(32)) transistor_2 (.in(in_2), .out(out_6), .gate(a1));
  Transistor #(.\type ("n"), .width(32)) transistor_3 (.in(in_3), .out(out_6), .gate(a2));
  Transistor #(.\type ("n"), .gate("br"), .width(32)) transistor_4 (.in(in_4), .out(out_6), .gate(a3));
endmodule

module MUX4_3bits (
  input  [2:0] in_1,
  input  [2:0] in_2,
  input  [2:0] in_3,
  input  [2:0] in_4,
  input  [1:0] in_5,
  output [2:0] out_6
);

  wire a0, a1, a2, a3;

  Decoder #(.select(2), .enable("false")) decoder_1 (.out0(a0), .out1(a1), .out2(a2), .out3(a3), .sel(in_5));
  Transistor #(.\type ("n"), .width(3)) transistor_1 (.in(in_1), .out(out_6), .gate(a0));
  Transistor #(.\type ("n"), .gate("br"), .width(3)) transistor_2 (.in(in_2), .out(out_6), .gate(a1));
  Transistor #(.\type ("n"), .width(3)) transistor_3 (.in(in_3), .out(out_6), .gate(a2));
  Transistor #(.\type ("n"), .gate("br"), .width(3)) transistor_4 (.in(in_4), .out(out_6), .gate(a3));
endmodule

module MUX4_5bits (
  input  [4:0] in_1,
  input  [4:0] in_2,
  input  [4:0] in_3,
  input  [4:0] in_4,
  input  [1:0] in_5,
  output [4:0] out_6
);

  wire a0, a1, a2, a3;

  Decoder #(.select(2), .enable("false")) decoder_1 (.out0(a0), .out1(a1), .out2(a2), .out3(a3), .sel(in_5));
  Transistor #(.\type ("n"), .width(5)) transistor_1 (.in(in_1), .out(out_6), .gate(a0));
  Transistor #(.\type ("n"), .gate("br"), .width(5)) transistor_2 (.in(in_2), .out(out_6), .gate(a1));
  Transistor #(.\type ("n"), .width(5)) transistor_3 (.in(in_3), .out(out_6), .gate(a2));
  Transistor #(.\type ("n"), .gate("br"), .width(5)) transistor_4 (.in(in_4), .out(out_6), .gate(a3));
endmodule

module MUX4_20bits (
  input  [19:0] in_1,
  input  [19:0] in_2,
  input  [19:0] in_3,
  input  [19:0] in_4,
  input  [1:0] in_5,
  output [19:0] out_6
);

  wire a0, a1, a2, a3;

  Decoder #(.select(2), .enable("false")) decoder_1 (.out0(a0), .out1(a1), .out2(a2), .out3(a3), .sel(in_5));
  Transistor #(.\type ("n"), .width(20)) transistor_1 (.in(in_1), .out(out_6), .gate(a0));
  Transistor #(.\type ("n"), .gate("br"), .width(20)) transistor_2 (.in(in_2), .out(out_6), .gate(a1));
  Transistor #(.\type ("n"), .width(20)) transistor_3 (.in(in_3), .out(out_6), .gate(a2));
  Transistor #(.\type ("n"), .gate("br"), .width(20)) transistor_4 (.in(in_4), .out(out_6), .gate(a3));
endmodule

module MUX8 (
  input  [31:0] in_1,
  input  [31:0] in_2,
  input  [31:0] in_3,
  input  [31:0] in_4,
  input  [31:0] in_5,
  input  [2:0] in_6,
  input  [31:0] in_7,
  input  [31:0] in_8,
  input  [31:0] in_9,
  output [31:0] out_10
);

  wire a0, a1, a2, a3, a4, a5, a6, a7;

  Transistor #(.\type ("n"), .gate("br"), .width(32)) transistor_1 (.in(in_1), .out(out_10), .gate(a0));
  Transistor #(.\type ("n"), .gate("br"), .width(32)) transistor_2 (.in(in_2), .out(out_10), .gate(a1));
  Transistor #(.\type ("n"), .gate("br"), .width(32)) transistor_3 (.in(in_3), .out(out_10), .gate(a2));
  Transistor #(.\type ("n"), .gate("br"), .width(32)) transistor_4 (.in(in_4), .out(out_10), .gate(a3));
  Transistor #(.\type ("n"), .gate("br"), .width(32)) transistor_5 (.in(in_5), .out(out_10), .gate(a4));
  Transistor #(.\type ("n"), .gate("br"), .width(32)) transistor_6 (.in(in_7), .out(out_10), .gate(a5));
  Transistor #(.\type ("n"), .gate("br"), .width(32)) transistor_7 (.in(in_8), .out(out_10), .gate(a6));
  Transistor #(.\type ("n"), .gate("br"), .width(32)) transistor_8 (.in(in_9), .out(out_10), .gate(a7));
  Decoder #(.select(3), .enable("false")) decoder_1 (
    .out0(a0), .out1(a1), .out2(a2), .out3(a3), .out4(a4), .out5(a5), .out6(a6), .out7(a7), .sel(in_6));

  // Other names for the same wires on the sheet: out[31:0] = out_10
endmodule

module MUX8_20bits (
  input  [19:0] in_1,
  input  [19:0] in_2,
  input  [19:0] in_3,
  input  [19:0] in_4,
  input  [19:0] in_5,
  input  [2:0] in_6,
  input  [19:0] in_7,
  input  [19:0] in_8,
  input  [19:0] in_9,
  output [19:0] out_10
);

  wire a0, a1, a2, a3, a4, a5, a6, a7;

  Transistor #(.\type ("n"), .gate("br"), .width(20)) transistor_1 (.in(in_1), .out(out_10), .gate(a0));
  Transistor #(.\type ("n"), .gate("br"), .width(20)) transistor_2 (.in(in_2), .out(out_10), .gate(a1));
  Transistor #(.\type ("n"), .gate("br"), .width(20)) transistor_3 (.in(in_3), .out(out_10), .gate(a2));
  Transistor #(.\type ("n"), .gate("br"), .width(20)) transistor_4 (.in(in_4), .out(out_10), .gate(a3));
  Transistor #(.\type ("n"), .gate("br"), .width(20)) transistor_5 (.in(in_5), .out(out_10), .gate(a4));
  Transistor #(.\type ("n"), .gate("br"), .width(20)) transistor_6 (.in(in_7), .out(out_10), .gate(a5));
  Transistor #(.\type ("n"), .gate("br"), .width(20)) transistor_7 (.in(in_8), .out(out_10), .gate(a6));
  Transistor #(.\type ("n"), .gate("br"), .width(20)) transistor_8 (.in(in_9), .out(out_10), .gate(a7));
  Decoder #(.select(3), .enable("false")) decoder_1 (
    .out0(a0), .out1(a1), .out2(a2), .out3(a3), .out4(a4), .out5(a5), .out6(a6), .out7(a7), .sel(in_6));

  // Other names for the same wires on the sheet: out[19:0] = out_10
endmodule

module MUX16 (
  input  [31:0] in_1,
  input  [31:0] in_2,
  input  [31:0] in_3,
  input  [31:0] in_4,
  input  [31:0] in_5,
  input  [31:0] in_6,
  input  [3:0] in_7,
  input  [31:0] in_8,
  input  [31:0] in_9,
  input  [31:0] in_10,
  input  [31:0] in_11,
  input  [31:0] in_12,
  input  [31:0] in_13,
  input  [31:0] in_14,
  input  [31:0] in_15,
  input  [31:0] in_16,
  input  [31:0] in_17,
  output [31:0] out_18
);

  wire a0, a1, a2, a3, a4, a5, a6, a7, a8, a9, a10, a11, a12, a13, a14, a15;

  Transistor #(.\type ("n"), .gate("br"), .width(32)) transistor_1 (.in(in_1), .out(out_18), .gate(a0));
  Transistor #(.\type ("n"), .gate("br"), .width(32)) transistor_2 (.in(in_2), .out(out_18), .gate(a1));
  Transistor #(.\type ("n"), .gate("br"), .width(32)) transistor_3 (.in(in_3), .out(out_18), .gate(a2));
  Transistor #(.\type ("n"), .gate("br"), .width(32)) transistor_4 (.in(in_4), .out(out_18), .gate(a3));
  Transistor #(.\type ("n"), .gate("br"), .width(32)) transistor_5 (.in(in_5), .out(out_18), .gate(a4));
  Transistor #(.\type ("n"), .gate("br"), .width(32)) transistor_6 (.in(in_6), .out(out_18), .gate(a5));
  Transistor #(.\type ("n"), .gate("br"), .width(32)) transistor_7 (.in(in_8), .out(out_18), .gate(a6));
  Transistor #(.\type ("n"), .gate("br"), .width(32)) transistor_8 (.in(in_9), .out(out_18), .gate(a7));
  Transistor #(.\type ("n"), .gate("br"), .width(32)) transistor_9 (.in(in_10), .out(out_18), .gate(a8));
  Transistor #(.\type ("n"), .gate("br"), .width(32)) transistor_10 (.in(in_11), .out(out_18), .gate(a9));
  Transistor #(.\type ("n"), .gate("br"), .width(32)) transistor_11 (.in(in_12), .out(out_18), .gate(a10));
  Transistor #(.\type ("n"), .gate("br"), .width(32)) transistor_12 (.in(in_13), .out(out_18), .gate(a11));
  Transistor #(.\type ("n"), .gate("br"), .width(32)) transistor_13 (.in(in_14), .out(out_18), .gate(a12));
  Transistor #(.\type ("n"), .gate("br"), .width(32)) transistor_14 (.in(in_15), .out(out_18), .gate(a13));
  Transistor #(.\type ("n"), .gate("br"), .width(32)) transistor_15 (.in(in_16), .out(out_18), .gate(a14));
  Transistor #(.\type ("n"), .gate("br"), .width(32)) transistor_16 (.in(in_17), .out(out_18), .gate(a15));
  Decoder #(.select(4), .enable("false")) decoder_1 (
    .out0(a0), .out1(a1), .out2(a2), .out3(a3), .out4(a4), .out5(a5), .out6(a6), .out7(a7), .out8(a8),
    .out9(a9), .out10(a10), .out11(a11), .out12(a12), .out13(a13), .out14(a14), .out15(a15), .sel(in_7));

  // Other names for the same wires on the sheet: out[31:0] = out_18
endmodule

module MUX16_12bits (
  input  [11:0] in_1,
  input  [11:0] in_2,
  input  [11:0] in_3,
  input  [11:0] in_4,
  input  [11:0] in_5,
  input  [11:0] in_6,
  input  [3:0] in_7,
  input  [11:0] in_8,
  input  [11:0] in_9,
  input  [11:0] in_10,
  input  [11:0] in_11,
  input  [11:0] in_12,
  input  [11:0] in_13,
  input  [11:0] in_14,
  input  [11:0] in_15,
  input  [11:0] in_16,
  input  [11:0] in_17,
  output [11:0] out_18
);

  wire a0, a1, a2, a3, a4, a5, a6, a7, a8, a9, a10, a11, a12, a13, a14, a15;

  Transistor #(.\type ("n"), .gate("br"), .width(12)) transistor_1 (.in(in_1), .out(out_18), .gate(a0));
  Transistor #(.\type ("n"), .gate("br"), .width(12)) transistor_2 (.in(in_2), .out(out_18), .gate(a1));
  Transistor #(.\type ("n"), .gate("br"), .width(12)) transistor_3 (.in(in_3), .out(out_18), .gate(a2));
  Transistor #(.\type ("n"), .gate("br"), .width(12)) transistor_4 (.in(in_4), .out(out_18), .gate(a3));
  Transistor #(.\type ("n"), .gate("br"), .width(12)) transistor_5 (.in(in_5), .out(out_18), .gate(a4));
  Transistor #(.\type ("n"), .gate("br"), .width(12)) transistor_6 (.in(in_6), .out(out_18), .gate(a5));
  Transistor #(.\type ("n"), .gate("br"), .width(12)) transistor_7 (.in(in_8), .out(out_18), .gate(a6));
  Transistor #(.\type ("n"), .gate("br"), .width(12)) transistor_8 (.in(in_9), .out(out_18), .gate(a7));
  Transistor #(.\type ("n"), .gate("br"), .width(12)) transistor_9 (.in(in_10), .out(out_18), .gate(a8));
  Transistor #(.\type ("n"), .gate("br"), .width(12)) transistor_10 (.in(in_11), .out(out_18), .gate(a9));
  Transistor #(.\type ("n"), .gate("br"), .width(12)) transistor_11 (.in(in_12), .out(out_18), .gate(a10));
  Transistor #(.\type ("n"), .gate("br"), .width(12)) transistor_12 (.in(in_13), .out(out_18), .gate(a11));
  Transistor #(.\type ("n"), .gate("br"), .width(12)) transistor_13 (.in(in_14), .out(out_18), .gate(a12));
  Transistor #(.\type ("n"), .gate("br"), .width(12)) transistor_14 (.in(in_15), .out(out_18), .gate(a13));
  Transistor #(.\type ("n"), .gate("br"), .width(12)) transistor_15 (.in(in_16), .out(out_18), .gate(a14));
  Transistor #(.\type ("n"), .gate("br"), .width(12)) transistor_16 (.in(in_17), .out(out_18), .gate(a15));
  Decoder #(.select(4), .enable("false")) decoder_1 (
    .out0(a0), .out1(a1), .out2(a2), .out3(a3), .out4(a4), .out5(a5), .out6(a6), .out7(a7), .out8(a8),
    .out9(a9), .out10(a10), .out11(a11), .out12(a12), .out13(a13), .out14(a14), .out15(a15), .sel(in_7));

  // Other names for the same wires on the sheet: out[11:0] = out_18
endmodule

module MUX32 (
  input  [31:0] in_1,
  input  [31:0] in_2,
  input  [31:0] in_3,
  input  [31:0] in_4,
  input  [31:0] in_5,
  input  [31:0] in_6,
  input  [31:0] in_7,
  input  [31:0] in_8,
  input  [31:0] in_9,
  input  [31:0] in_10,
  input  [31:0] in_11,
  input  [31:0] in_12,
  input  [31:0] in_13,
  input  [31:0] in_14,
  input  [31:0] in_15,
  input  [31:0] in_16,
  input  [31:0] in_17,
  input  [31:0] in_18,
  input  [31:0] in_19,
  input  [31:0] in_20,
  input  [31:0] in_21,
  input  [31:0] in_22,
  input  [31:0] in_23,
  input  [31:0] in_24,
  input  [31:0] in_25,
  input  [31:0] in_26,
  input  [31:0] in_27,
  input  [31:0] in_28,
  input  [31:0] in_29,
  input  [31:0] in_30,
  input  [31:0] in_31,
  input  [31:0] in_32,
  input  [4:0] in_33,
  output [31:0] out_34
);

  wire a0, a1, a2, a3, a4, a5, a6, a7, a8, a9, a10, a11, a12, a13, a14, a15, a16, a17, a18, a19, a20, a21,
       a22, a23, a24, a25, a26, a27, a28, a29, a30, a31;

  Transistor #(.\type ("n"), .gate("br"), .width(32)) transistor_1 (.in(in_1), .out(out_34), .gate(a0));
  Transistor #(.\type ("n"), .gate("br"), .width(32)) transistor_2 (.in(in_2), .out(out_34), .gate(a1));
  Transistor #(.\type ("n"), .gate("br"), .width(32)) transistor_3 (.in(in_3), .out(out_34), .gate(a2));
  Transistor #(.\type ("n"), .gate("br"), .width(32)) transistor_4 (.in(in_4), .out(out_34), .gate(a3));
  Transistor #(.\type ("n"), .gate("br"), .width(32)) transistor_5 (.in(in_5), .out(out_34), .gate(a4));
  Transistor #(.\type ("n"), .gate("br"), .width(32)) transistor_6 (.in(in_6), .out(out_34), .gate(a5));
  Transistor #(.\type ("n"), .gate("br"), .width(32)) transistor_7 (.in(in_7), .out(out_34), .gate(a6));
  Transistor #(.\type ("n"), .gate("br"), .width(32)) transistor_8 (.in(in_8), .out(out_34), .gate(a7));
  Transistor #(.\type ("n"), .gate("br"), .width(32)) transistor_9 (.in(in_9), .out(out_34), .gate(a8));
  Transistor #(.\type ("n"), .gate("br"), .width(32)) transistor_10 (.in(in_10), .out(out_34), .gate(a9));
  Transistor #(.\type ("n"), .gate("br"), .width(32)) transistor_11 (.in(in_11), .out(out_34), .gate(a10));
  Transistor #(.\type ("n"), .gate("br"), .width(32)) transistor_12 (.in(in_12), .out(out_34), .gate(a11));
  Transistor #(.\type ("n"), .gate("br"), .width(32)) transistor_13 (.in(in_13), .out(out_34), .gate(a12));
  Transistor #(.\type ("n"), .gate("br"), .width(32)) transistor_14 (.in(in_14), .out(out_34), .gate(a13));
  Transistor #(.\type ("n"), .gate("br"), .width(32)) transistor_15 (.in(in_15), .out(out_34), .gate(a14));
  Transistor #(.\type ("n"), .gate("br"), .width(32)) transistor_16 (.in(in_16), .out(out_34), .gate(a15));
  Transistor #(.\type ("n"), .gate("br"), .width(32)) transistor_17 (.in(in_17), .out(out_34), .gate(a16));
  Transistor #(.\type ("n"), .gate("br"), .width(32)) transistor_18 (.in(in_18), .out(out_34), .gate(a17));
  Transistor #(.\type ("n"), .gate("br"), .width(32)) transistor_19 (.in(in_19), .out(out_34), .gate(a18));
  Transistor #(.\type ("n"), .gate("br"), .width(32)) transistor_20 (.in(in_20), .out(out_34), .gate(a19));
  Transistor #(.\type ("n"), .gate("br"), .width(32)) transistor_21 (.in(in_21), .out(out_34), .gate(a20));
  Transistor #(.\type ("n"), .gate("br"), .width(32)) transistor_22 (.in(in_22), .out(out_34), .gate(a21));
  Transistor #(.\type ("n"), .gate("br"), .width(32)) transistor_23 (.in(in_23), .out(out_34), .gate(a22));
  Transistor #(.\type ("n"), .gate("br"), .width(32)) transistor_24 (.in(in_24), .out(out_34), .gate(a23));
  Transistor #(.\type ("n"), .gate("br"), .width(32)) transistor_25 (.in(in_25), .out(out_34), .gate(a24));
  Transistor #(.\type ("n"), .gate("br"), .width(32)) transistor_26 (.in(in_26), .out(out_34), .gate(a25));
  Transistor #(.\type ("n"), .gate("br"), .width(32)) transistor_27 (.in(in_27), .out(out_34), .gate(a26));
  Transistor #(.\type ("n"), .gate("br"), .width(32)) transistor_28 (.in(in_28), .out(out_34), .gate(a27));
  Transistor #(.\type ("n"), .gate("br"), .width(32)) transistor_29 (.in(in_29), .out(out_34), .gate(a28));
  Transistor #(.\type ("n"), .gate("br"), .width(32)) transistor_30 (.in(in_30), .out(out_34), .gate(a29));
  Transistor #(.\type ("n"), .gate("br"), .width(32)) transistor_31 (.in(in_31), .out(out_34), .gate(a30));
  Transistor #(.\type ("n"), .gate("br"), .width(32)) transistor_32 (.in(in_32), .out(out_34), .gate(a31));
  Decoder #(.select(5), .enable("false")) decoder_1 (
    .out0(a0), .out1(a1), .out2(a2), .out3(a3), .out4(a4), .out5(a5), .out6(a6), .out7(a7), .out8(a8),
    .out9(a9), .out10(a10), .out11(a11), .out12(a12), .out13(a13), .out14(a14), .out15(a15), .out16(a16),
    .out17(a17), .out18(a18), .out19(a19), .out20(a20), .out21(a21), .out22(a22), .out23(a23), .out24(a24),
    .out25(a25), .out26(a26), .out27(a27), .out28(a28), .out29(a29), .out30(a30), .out31(a31), .sel(in_33));

  // Other names for the same wires on the sheet: out[31:0] = out_34
endmodule

// I.D
module InstructionDecoder (
  input  [31:0] in_1,
  output [15:0] K,
  output [25:0] Jump,
  output U,
  output nop,
  output mul,
  output add,
  output mulu,
  output sub,
  output div,
  output slt,
  output divu,
  output sltu,
  output \and ,
  output mfhi,
  output \or ,
  output mflo,
  output \nor ,
  output jr,
  output \xor ,
  output [4:0] Rs,
  output [4:0] Rd,
  output [4:0] Rt,
  output pop,
  output push,
  output addi,
  output slti,
  output sltiu,
  output andi,
  output ori,
  output xori,
  output lw,
  output sw,
  output halt,
  output beq,
  output tty,
  output bne,
  output rnd,
  output kbd,
  output blez,
  output bgtz,
  output bltz,
  output TJ,
  output EnRd,
  output [2:0] FS,
  output EnRt,
  output TI,
  output IncPC__1ciclo,
  output IncPC
);

  wire and_8_out, and_9_out, and_14_out, or_1_out, or_2_out, or_3_out, or_4_out, or_5_out, S00, TI0, TI001,
       TR0, TR0f5, TR10, TR11;

  or or_1 (or_1_out, \and , andi);
  or or_2 (or_2_out, \or , ori);
  or or_3 (or_3_out, \xor , xori);
  or or_4 (or_4_out, div, divu);
  and and_1 (S00, ~in_1[31], ~in_1[29]);  // AND_Gate
  and and_2 (TI001, ~in_1[31], in_1[29]);  // AND_Gate
  and and_3 (lw, in_1[31], ~in_1[29]);  // AND_Gate
  and and_4 (sw, in_1[31], ~in_1[30], in_1[29]);  // AND_Gate
  or or_5 (or_5_out, add, addi);
  and and_5 (TR11, in_1[30], in_1[28]);
  and and_6 (TR10, in_1[30], ~in_1[28]);  // AND_Gate
  and and_7 (TR0, S00, ~in_1[28], ~in_1[27], ~in_1[26]);  // AND_Gate
  and and_8 (and_8_out, S00, ~in_1[27], in_1[26]);  // AND_Gate
  and and_9 (and_9_out, S00, in_1[28]);
  and and_10 (TJ, S00, ~in_1[28], in_1[27], ~in_1[26]);  // AND_Gate
  and and_11 (FS[2], ~or_5_out, ~sub, ~or_1_out, ~or_2_out);  // AND_Gate
  and and_12 (FS[1], ~or_5_out, ~sub, ~\nor , ~or_3_out);  // AND_Gate
  and and_13 (FS[0], ~or_5_out, ~or_1_out, ~\nor , ~or_4_out);  // AND_Gate
  or or_6 (TI0, and_8_out, and_9_out);
  TR10 tr10_1 (.TR10(TR10), .F0(in_1[0]), .pop(pop), .push(push));
  and and_14 (and_14_out, TR0, ~jr);  // AND_Gate
  TR11 tr11_1 (.TR11(TR11), .f2(in_1[2]), .f1(in_1[1]), .f0(in_1[0]), .halt(halt), .tty(tty), .rnd(rnd), .kbd(kbd));
  or or_7 (IncPC, TI001, 1'b0, sw, TR10, and_14_out);
  TR0 tr0_1 (
    .TR0(TR0), .Func_Code(in_1[5:0]), .mult(mul), .add(add), .mulu(mulu), .sub(sub), .div(div), .slt(slt),
    .divu(divu), .sltu(sltu), .nop(nop), .mfhi(mfhi), .\and (\and ), .jr(jr), .\or (\or ), .mflo(mflo),
    .\nor (\nor ), .\xor (\xor ), .f5v1(TR0f5));
  TI001 ti001_1 (
    .TI001(TI001), .op2(in_1[28]), .op1(in_1[27]), .op0(in_1[26]), .addi(addi), .slti(slti), .sltiu(sltiu),
    .andi(andi), .ori(ori), .xori(xori));
  or or_8 (EnRt, TI001, lw);
  or or_9 (EnRd, TR0f5, mfhi, kbd, mflo, rnd);
  or or_10 (TI, TI001, lw, sw, TI0);
  TI0 ti0_1 (
    .TI0(TI0), .op2(in_1[28]), .op1(in_1[27]), .op0(in_1[26]), .beg(beq), .bne(bne), .blez(blez),
    .bgtz(bgtz), .bltz(bltz));
  or or_11 (IncPC__1ciclo, rnd, TR0, TI0, TJ, TI001, kbd);

  assign Jump = in_1[25:0];
  assign K = in_1[15:0];
  assign Rd = in_1[15:11];
  assign Rs = in_1[25:21];
  assign Rt = in_1[20:16];
  assign U = in_1[0];

  // Other names for the same wires on the sheet: f0 = in_1[0]; Func_Code[5:0] = in_1[5:0]; f1 = in_1[1]; f2 = in_1[2];
  //   f3 = in_1[3]; f4 = in_1[4]; f5 = in_1[5]; mult = mul; op0 = in_1[26]; Op_Code[5:0] = in_1[31:26];
  //   op1 = in_1[27]; op2 = in_1[28]; op3 = in_1[29]; op4 = in_1[30]; S11 = in_1[30]; op5 = in_1[31]
endmodule

// TR 11
module TR11 (
  input  TR11,
  input  f2,
  input  f1,
  input  f0,
  output halt,
  output tty,
  output rnd,
  output kbd
);

  and and_1 (halt, TR11, f2, f1, f0);
  and and_2 (tty, TR11, ~f2, ~f1, f0);  // AND_Gate
  and and_3 (rnd, TR11, ~f2, f1, ~f0);  // AND_Gate
  and and_4 (kbd, TR11, f2, ~f1, ~f0);  // AND_Gate
endmodule

module TR10 (
  input  TR10,
  input  F0,
  output pop,
  output push
);

  and and_1 (push, TR10, F0);
  and and_2 (pop, TR10, ~F0);  // AND_Gate
endmodule

module TI001 (
  input  TI001,
  input  op2,
  input  op1,
  input  op0,
  output addi,
  output slti,
  output sltiu,
  output andi,
  output ori,
  output xori
);

  and and_1 (addi, TI001, ~op2, ~op1, ~op0);  // AND_Gate
  and and_2 (slti, TI001, ~op2, op1, ~op0);  // AND_Gate
  and and_3 (sltiu, TI001, ~op2, op1, op0);  // AND_Gate
  and and_4 (andi, TI001, op2, ~op1, ~op0);  // AND_Gate
  and and_5 (ori, TI001, op2, ~op1, op0);  // AND_Gate
  and and_6 (xori, TI001, op2, op1, ~op0);  // AND_Gate
endmodule

module TI0 (
  input  TI0,
  input  op2,
  input  op1,
  input  op0,
  output beg,
  output bne,
  output blez,
  output bgtz,
  output bltz
);

  and and_1 (bgtz, TI0, op2, op1, op0);
  and and_2 (beg, TI0, op2, ~op1, ~op0);  // AND_Gate
  and and_3 (bne, TI0, op2, ~op1, op0);  // AND_Gate
  and and_4 (blez, TI0, op2, op1, ~op0);  // AND_Gate
  and and_5 (bltz, TI0, ~op2, ~op1, op0);  // AND_Gate
endmodule

module TR0 (
  input  TR0,
  input  [5:0] Func_Code,
  output mult,
  output add,
  output f5v1,
  output mulu,
  output sub,
  output div,
  output slt,
  output divu,
  output sltu,
  output nop,
  output mfhi,
  output \and ,
  output jr,
  output \or ,
  output mflo,
  output \nor ,
  output \xor 
);

  wire f4v0, f4v1, f5v0;

  and and_1 (f5v1, TR0, Func_Code[5]);
  and and_2 (f4v1, f5v0, Func_Code[4]);
  and and_3 (jr, f4v0, Func_Code[3]);
  and and_4 (f5v0, TR0, ~Func_Code[5]);  // AND_Gate
  and and_5 (f4v0, f5v0, ~Func_Code[4]);  // AND_Gate
  and and_6 (nop, f4v0, ~Func_Code[3]);  // AND_Gate
  and and_7 (add, f5v1, ~Func_Code[3], ~Func_Code[2], ~Func_Code[1], ~Func_Code[0]);  // AND_Gate
  and and_8 (sub, f5v1, ~Func_Code[3], ~Func_Code[2], Func_Code[1], ~Func_Code[0]);  // AND_Gate
  and and_9 (slt, f5v1, Func_Code[3], ~Func_Code[2], Func_Code[1], ~Func_Code[0]);  // AND_Gate
  and and_10 (sltu, f5v1, Func_Code[3], ~Func_Code[2], Func_Code[1], Func_Code[0]);  // AND_Gate
  and and_11 (\and , f5v1, ~Func_Code[3], Func_Code[2], ~Func_Code[1], ~Func_Code[0]);  // AND_Gate
  and and_12 (\or , f5v1, ~Func_Code[3], Func_Code[2], ~Func_Code[1], Func_Code[0]);  // AND_Gate
  and and_13 (\nor , f5v1, ~Func_Code[3], Func_Code[2], Func_Code[1], Func_Code[0]);  // AND_Gate
  and and_14 (\xor , f5v1, Func_Code[3], ~Func_Code[2], ~Func_Code[1], ~Func_Code[0]);  // AND_Gate
  and and_15 (mult, f4v1, Func_Code[3], ~Func_Code[2], ~Func_Code[1], ~Func_Code[0]);  // AND_Gate
  and and_16 (mulu, f4v1, Func_Code[3], ~Func_Code[2], ~Func_Code[1], Func_Code[0]);  // AND_Gate
  and and_17 (div, f4v1, Func_Code[3], ~Func_Code[2], Func_Code[1], ~Func_Code[0]);  // AND_Gate
  and and_18 (divu, f4v1, Func_Code[3], ~Func_Code[2], Func_Code[1], Func_Code[0]);  // AND_Gate
  and and_19 (mfhi, f4v1, ~Func_Code[3], ~Func_Code[2], ~Func_Code[1], ~Func_Code[0]);  // AND_Gate
  and and_20 (mflo, f4v1, ~Func_Code[3], ~Func_Code[2], Func_Code[1], ~Func_Code[0]);  // AND_Gate

  // Other names for the same wires on the sheet: f0 = Func_Code[0]; f1 = Func_Code[1]; f2 = Func_Code[2];
  //   f3 = Func_Code[3]; f4 = Func_Code[4]; f5 = Func_Code[5]
endmodule

module Estados (
  input  CLK,
  input  Clear,
  input  [31:0] in_3,
  input  EN,
  input  C,
  input  Z,
  input  O,
  input  S,
  output halt,
  output tty,
  output rnd,
  output kbd,
  output pop,
  output push,
  output minus_R_W,
  output beq,
  output bne,
  output blez,
  output bgtz,
  output bltz,
  output ENHiLo,
  output S_B,
  output IncPC_1ciclo,
  output IncPC,
  output [1:0] SDA,
  output j,
  output sw,
  output lw,
  output jr,
  output [4:0] Rs,
  output [4:0] Rt,
  output [4:0] Rd,
  output U,
  output [31:0] cte,
  output [25:0] Jump,
  output [15:0] K,
  output [2:0] FS,
  output [31:0] C_ID,
  output [2:0] S_ID,
  output S_BA
);

  wire add, add1, addi, addi1, ALU, \and , and1, andi, andi1, beq1, bgtz1, blez1, bltz1, bne1, cmp, cmpu_1_g,
       div, div1, divu, divu1, En_out, EnRd, EnRd1, EnRt, instructiondecoder_1_incpc__1ciclo, j1, jr1, kbd1,
       lw1, mfhi, mfhi1, mflo, mflo1, mult, mult1, mulu, mulu1, nop, nop1, \nor , nor1, \or , or1, ori, ori1,
       pop1, RAM, rnd1, slt, slt1, slti, slti1, sltiu, sltiu1, sltu, sltu1, Sstl, Sstls, Sstlu, sub, sub1,
       sw1, tty1, vs, vu, \xor , xor1, xori, xori1;
  wire [1:1] or_10_out;
  wire [2:0] fs_t;
  wire [31:0] register_1_q;

  D_Flip_Flop d_ff_1 (.clk(CLK), .D(EN), .Q(En_out), .reset(Clear));  // open: Qn, preset, en
  and and_1 (IncPC_1ciclo, En_out, instructiondecoder_1_incpc__1ciclo);
  Register #(.width(32)) register_1 (.D(in_3), .en(EN), .Q(register_1_q), .clk(CLK), .clr(Clear));
  InstructionDecoder instructiondecoder_1 (
    .in_1(register_1_q), .halt(halt), .tty(tty1), .rnd(rnd1), .kbd(kbd1), .pop(pop1), .push(SDA[1]),
    .addi(addi1), .slti(slti1), .sltiu(sltiu1), .andi(andi1), .ori(ori1), .xori(xori1), .beq(beq1),
    .bne(bne1), .blez(blez1), .bgtz(bgtz1), .bltz(bltz1), .nop(nop1), .add(add1), .sub(sub1), .slt(slt1),
    .sltu(sltu1), .\and (and1), .\or (or1), .\nor (nor1), .\xor (xor1), .mul(mult1), .mulu(mulu1),
    .div(div1), .divu(divu1), .mfhi(mfhi1), .mflo(mflo1), .jr(jr1), .lw(lw1), .sw(sw1), .TJ(j1), .Rs(Rs),
    .Rt(Rt), .Rd(Rd), .K({cte[31], cte[14:0]}), .Jump(Jump), .U(U), .FS(fs_t), .EnRd(EnRd1), .EnRt(SDA[0]),
    .IncPC(IncPC), .IncPC__1ciclo(instructiondecoder_1_incpc__1ciclo));  // open: TI
  cmpU cmpu_1 (.VU(vu), .Z(Z), .C(C), .G(cmpu_1_g), .L(Sstlu));  // open: I
  cmpS cmps_1 (.VS(vs), .Z(Z), .S(O), .O(S), .L(Sstls));  // open: G, I
  or or_1 (ALU, andi1, ori1, and1, or1, nor1, xor1, add1, sub1, xori1, addi1);
  or or_2 (RAM, lw1, pop1);
  or or_3 (Sstl, Sstlu, Sstls);
  or or_4 (vs, slti1, slt1);
  or or_5 (vu, sltu1, sltiu1);
  or or_6 (cmp, vs, vu);
  and and_2 (S_ID[2], ~ALU, ~mfhi1, ~mflo1, ~RAM);  // AND_Gate
  and and_3 (S_ID[1], ~ALU, ~mfhi1, ~cmp, ~rnd1);  // AND_Gate
  and and_4 (S_ID[0], ~ALU, ~mflo1, ~cmp, ~kbd1);  // AND_Gate
  MUX4_3bits mux4_3bits_1 (
    .in_1(fs_t), .in_2(3'b001), .in_3(3'b000), .in_4(3'b000), .out_6(FS), .in_5({or_10_out[1], cmp}));
  MUX2 mux2_1 (.in_1({32{1'b0}}), .in_2(32'h1), .out_4(C_ID), .in_3(Sstl));
  or or_7 (minus_R_W, EnRd, EnRt);
  or or_8 (ENHiLo, mult, mulu, div, divu);
  or or_9 (S_B, lw1, sltiu1, addi1, andi1, ori1, xori1, slti1, sw1);
  or or_10 (or_10_out[1], lw1, sw1);
  or or_11 (S_BA, pop1, SDA[1]);
  and and_5 (tty, En_out, tty1);
  and and_6 (rnd, En_out, rnd1);
  and and_7 (kbd, En_out, kbd1);
  and and_8 (push, En_out, SDA[1]);
  and and_9 (slti, En_out, slti1);
  and and_10 (ori, En_out, ori1);
  and and_11 (beq, En_out, beq1);
  and and_12 (bne, En_out, bne1);
  and and_13 (bgtz, En_out, bgtz1);
  and and_14 (nop, En_out, nop1);
  and and_15 (andi, En_out, andi1);
  and and_16 (blez, En_out, blez1);
  and and_17 (bltz, En_out, bltz1);
  and and_18 (addi, En_out, addi1);
  and and_19 (pop, En_out, pop1);
  and and_20 (xori, En_out, xori1);
  and and_21 (sltiu, En_out, sltiu1);
  and and_22 (add, En_out, add1);
  and and_23 (\and , En_out, and1);
  and and_24 (sw, En_out, sw1);
  and and_25 (mflo, En_out, mflo1);
  and and_26 (mfhi, En_out, mfhi1);
  and and_27 (j, En_out, j1);
  and and_28 (lw, En_out, lw1);
  and and_29 (jr, En_out, jr1);
  and and_30 (divu, En_out, divu1);
  and and_31 (div, En_out, div1);
  and and_32 (mult, En_out, mult1);
  and and_33 (mulu, En_out, mulu1);
  and and_34 (\nor , En_out, nor1);
  and and_35 (\or , En_out, or1);
  and and_36 (\xor , En_out, xor1);
  and and_37 (sub, En_out, sub1);
  and and_38 (slt, En_out, slt1);
  and and_39 (sltu, En_out, sltu1);
  and and_40 (EnRt, En_out, SDA[0]);
  and and_41 (EnRd, En_out, EnRd1);

  assign cte[30:15] = {16{cte[31]}};
  assign K = {cte[31], cte[14:0]};

  // Other names for the same wires on the sheet: CLR = Clear; e0 = S_ID[0]; e1 = S_ID[1]; e2 = S_ID[2];
  //   EnRt1 = SDA[0]; push1 = SDA[1]
endmodule

module FS (
  input  add,
  input  sub,
  input  \and ,
  input  \or ,
  input  \nor ,
  input  \xor ,
  input  div,
  output FS2,
  output FS1,
  output FS0
);

  and and_1 (FS2, ~add, ~sub, ~\and , ~\or );  // AND_Gate
  and and_2 (FS1, ~add, ~sub, ~\nor , ~\xor );  // AND_Gate
  and and_3 (FS0, ~add, ~\and , ~\nor , ~div);  // AND_Gate
endmodule

module cmpS (
  input  VS,
  input  Z,
  input  S,
  input  O,
  output G,
  output I,
  output L
);

  wire and_2_out, and_3_out, and_4_out, and_5_out;

  and and_1 (I, VS, Z);
  and and_2 (and_2_out, VS, ~Z, ~S, ~O);  // AND_Gate
  or or_1 (G, and_2_out, and_3_out);
  and and_3 (and_3_out, VS, ~Z, S, O);  // AND_Gate
  and and_4 (and_4_out, VS, ~Z, ~S, O);  // AND_Gate
  or or_2 (L, and_4_out, and_5_out);
  and and_5 (and_5_out, VS, ~Z, S, ~O);  // AND_Gate
endmodule

module cmpU (
  input  VU,
  input  Z,
  input  C,
  output G,
  output I,
  output L
);

  and and_1 (I, VU, Z);
  and and_2 (G, VU, ~Z, ~C);  // AND_Gate
  and and_3 (L, VU, ~Z, C);  // AND_Gate
endmodule

module S_ID (
  input  kbd,
  input  R,
  input  Cte,
  input  RAM,
  input  Lo,
  input  Hi,
  input  ALU,
  output e2,
  output e1,
  output e0
);

  and and_1 (e2, ~Lo, ~Hi, ~ALU);  // AND_Gate
  and and_2 (e1, ~Cte, ~RAM, ~Hi, ~ALU);  // AND_Gate
  and and_3 (e0, ~R, ~RAM, ~Lo, ~ALU);  // AND_Gate
endmodule

module MemoryReader (
  input  Clear,
  input  CLK,
  input  EN,
  input  [3:0] RT,
  input  [31:0] Data0,
  input  [31:0] Data1,
  input  [31:0] Data2,
  input  [31:0] Data3,
  input  [19:0] ADDR,
  output CS,
  output [15:0] ADDR_2,
  output READY
);

  wire CLEAR_t, demultiplexer_1_out0, demultiplexer_1_out1, demultiplexer_2_out0, EQ, or_1_out, or_2_out,
       or_3_out;
  wire [3:0] counter_1_q, xor_1_out;

  or or_1 (or_1_out, demultiplexer_1_out0, READY);
  Counter #(.width(4), .max('hf)) counter_1 (
    .count(CS), .Q(counter_1_q), .clk(CLK), .clr(CLEAR_t));  // open: load, D, carry
  D_Flip_Flop START (.clk(CLK), .D(or_1_out), .Q(CLEAR_t), .preset(Clear));  // open: Qn, en, reset
  assign xor_1_out = counter_1_q ^ RT;  // XOR_Gate xor_1, 4 bits wide
  Demultiplexer #(.enable("false")) demultiplexer_1 (
    .out0(demultiplexer_1_out0), .out1(demultiplexer_1_out1), .in(CLEAR_t), .sel(EN));
  or or_2 (or_2_out, demultiplexer_2_out0, demultiplexer_1_out1);
  D_Flip_Flop COUNT (.clk(CLK), .D(or_2_out), .Q(CS), .reset(Clear));  // open: Qn, preset, en
  not not_1 (EQ, or_3_out);
  or or_3 (or_3_out, xor_1_out[0], xor_1_out[1], xor_1_out[2], xor_1_out[3]);
  Demultiplexer #(.enable("false")) demultiplexer_2 (.out0(demultiplexer_2_out0), .out1(READY), .in(CS), .sel(EQ));

  assign ADDR_2 = ADDR[19:4];

  // Other names for the same wires on the sheet: ADDR_t[15:0] = ADDR[19:4]; CLEARSTR = Clear; INC = CS;
  //   Offset[1:0] = ADDR[3:2]
endmodule

module MemoryWriter (
  input  CLK,
  input  EN,
  input  Clear,
  input  [3:0] WT,
  input  [31:0] Input,
  input  [19:0] ADDR,
  output CS,
  output minus_R_W,
  output [15:0] ADDR_2,
  output READY,
  output [3:0] Mask,
  output [31:0] Data0,
  output [31:0] Data1,
  output [31:0] Data2,
  output [31:0] Data3
);

  wire CLEAR_t, demultiplexer_1_out0, demultiplexer_1_out1, demultiplexer_2_out0, EQ, or_1_out, or_2_out,
       or_3_out;
  wire [3:0] counter_1_q, subtractor_1_out;

  or or_1 (or_1_out, demultiplexer_1_out0, READY);
  Counter #(.width(4), .max('hf)) counter_1 (
    .count(CS), .Q(counter_1_q), .clk(CLK), .clr(CLEAR_t));  // open: load, D, carry
  D_Flip_Flop START (.clk(CLK), .D(or_1_out), .Q(CLEAR_t), .preset(Clear));  // open: Qn, en, reset
  Subtractor #(.width(4)) subtractor_1 (.a(counter_1_q), .b(WT), .out(subtractor_1_out));  // open: bin, bout
  Demultiplexer #(.enable("false")) demultiplexer_1 (
    .out0(demultiplexer_1_out0), .out1(demultiplexer_1_out1), .in(CLEAR_t), .sel(EN));
  or or_2 (or_2_out, demultiplexer_2_out0, demultiplexer_1_out1);
  D_Flip_Flop COUNT (.clk(CLK), .D(or_2_out), .Q(CS));  // open: Qn, preset, en, reset
  not not_1 (EQ, or_3_out);
  or or_3 (or_3_out, subtractor_1_out[0], subtractor_1_out[1], subtractor_1_out[2], subtractor_1_out[3]);
  Demultiplexer #(.enable("false")) demultiplexer_2 (.out0(demultiplexer_2_out0), .out1(READY), .in(CS), .sel(EQ));
  Decoder #(.select(2), .enable("false")) decoder_1 (
    .out0(Mask[0]), .out1(Mask[1]), .out2(Mask[2]), .out3(Mask[3]), .sel(ADDR[3:2]));

  assign ADDR_2 = ADDR[19:4];
  assign Data0 = {Input[7:0], Input[15:8], Input[23:16], Input[31:24]};
  assign Data1 = {Input[7:0], Input[15:8], Input[23:16], Input[31:24]};
  assign Data2 = {Input[7:0], Input[15:8], Input[23:16], Input[31:24]};
  assign Data3 = {Input[7:0], Input[15:8], Input[23:16], Input[31:24]};
  assign minus_R_W = CS;

  // Other names for the same wires on the sheet: ADDR_t[15:0] = ADDR[19:4]; CLEARSTR = Clear; INC = CS;
  //   Offset[1:0] = ADDR[3:2]
endmodule
module Cache (
  input  minus_R_W,
  input  CLK,
  input  CLR,
  input  [31:0] I0,
  input  [31:0] I1,
  input  [31:0] I2,
  input  [31:0] I3,
  input  [19:0] ADDRIN,
  input  [3:0] Mask,
  input  EN,
  input  Clear_Dirty,
  input  Write_RAM,
  input  [31:0] Input_To_RAM,
  output [31:0] O0,
  output [31:0] O1,
  output [31:0] O2,
  output [31:0] O3,
  output [31:0] out_18,
  output Dirty,
  output Ready,
  output [3:0] MASK_2,
  output [15:0] ADDR_out
);

  wire and_9_out, and_10_out, and_11_out, and_12_out, and_13_out, and_14_out, and_15_out, and_16_out,
       and_17_out, and_18_out, and_19_out, and_20_out, and_21_out, and_22_out, and_23_out, and_24_out,
       and_25_out, and_26_out, and_27_out, and_28_out, and_29_out, and_30_out, and_31_out, and_32_out,
       and_33_out, and_34_out, and_35_out, and_36_out, and_37_out, and_38_out, and_39_out, and_40_out,
       and_41_out, and_42_out, and_43_out, and_44_out, and_45_out, and_46_out, and_47_out, and_48_out,
       and_49_out, and_50_out, and_51_out, and_52_out, and_53_out, and_54_out, and_55_out, and_56_out,
       and_57_out, and_58_out, and_59_out, and_60_out, and_61_out, and_62_out, and_63_out, and_64_out,
       and_65_out, and_66_out, and_67_out, and_68_out, and_69_out, and_70_out, and_71_out, and_72_out,
       and_73_out, and_74_out, and_75_out, and_76_out, and_77_out, and_78_out, and_79_out, and_80_out,
       and_81_out, and_82_out, and_83_out, and_84_out, and_85_out, and_86_out, and_87_out, and_88_out,
       and_89_out, and_90_out, and_91_out, and_92_out, and_93_out, and_94_out, and_95_out, and_96_out,
       and_97_out, and_98_out, and_99_out, and_100_out, and_101_out, and_102_out, and_103_out, and_104_out,
       and_105_out, and_106_out, and_107_out, and_108_out, and_109_out, and_110_out, and_111_out,
       and_112_out, and_113_out, and_114_out, and_115_out, and_116_out, and_117_out, and_118_out,
       and_119_out, and_120_out, and_121_out, and_122_out, and_123_out, and_124_out, and_125_out,
       and_126_out, and_127_out, and_128_out, and_129_out, and_130_out, and_131_out, and_132_out,
       and_133_out, and_134_out, and_135_out, and_136_out, and_137_out, and_138_out, and_139_out,
       and_140_out, and_141_out, and_142_out, and_143_out, and_144_out, and_145_out, and_146_out,
       and_147_out, and_148_out, and_149_out, and_150_out, and_151_out, and_152_out, and_153_out,
       and_154_out, and_155_out, and_156_out, and_157_out, and_158_out, and_159_out, and_160_out,
       and_161_out, and_162_out, and_163_out, and_164_out, and_165_out, and_166_out, and_167_out,
       and_168_out, and_169_out, CLR_Dirty_L0, CLR_Dirty_L1, CLR_Dirty_L2, CLR_Dirty_L3, CLR_Dirty_L4,
       CLR_Dirty_L5, CLR_Dirty_L6, CLR_Dirty_L7, CLR_Dirty_L8, CLR_Dirty_L9, CLR_Dirty_L10, CLR_Dirty_L11,
       CLR_Dirty_L12, CLR_Dirty_L13, CLR_Dirty_L14, CLR_Dirty_L15, Current_Dirty, Current_LoadFromRAM,
       Current_Valid, d_ff_113_q, decoder_1_out0, decoder_1_out1, decoder_1_out2, decoder_1_out3, Dirty_L0_0,
       Dirty_L0_1, Dirty_L0_2, Dirty_L0_3, Dirty_L1_0, Dirty_L1_1, Dirty_L1_2, Dirty_L1_3, Dirty_L2_0,
       Dirty_L2_1, Dirty_L2_2, Dirty_L2_3, Dirty_L3_0, Dirty_L3_1, Dirty_L3_2, Dirty_L3_3, Dirty_L4_0,
       Dirty_L4_1, Dirty_L4_2, Dirty_L4_3, Dirty_L5_0, Dirty_L5_1, Dirty_L5_2, Dirty_L5_3, Dirty_L6_0,
       Dirty_L6_1, Dirty_L6_2, Dirty_L6_3, Dirty_L7_0, Dirty_L7_1, Dirty_L7_2, Dirty_L7_3, Dirty_L8_0,
       Dirty_L8_1, Dirty_L8_2, Dirty_L8_3, Dirty_L9_0, Dirty_L9_1, Dirty_L9_2, Dirty_L9_3, Dirty_L10_0,
       Dirty_L10_1, Dirty_L10_2, Dirty_L10_3, Dirty_L11_0, Dirty_L11_1, Dirty_L11_2, Dirty_L11_3,
       Dirty_L12_0, Dirty_L12_1, Dirty_L12_2, Dirty_L12_3, Dirty_L13_0, Dirty_L13_1, Dirty_L13_2,
       Dirty_L13_3, Dirty_L14_0, Dirty_L14_1, Dirty_L14_2, Dirty_L14_3, Dirty_L15_0, Dirty_L15_1,
       Dirty_L15_2, Dirty_L15_3, EN_L0, EN_L1, EN_L2, EN_L3, EN_L4, EN_L5, EN_L6, EN_L7, EN_L8, EN_L9,
       EN_L10, EN_L11, EN_L12, EN_L13, EN_L14, EN_L15, LoadFromRAML0, LoadFromRAML1, LoadFromRAML2,
       LoadFromRAML3, LoadFromRAML4, LoadFromRAML5, LoadFromRAML6, LoadFromRAML7, LoadFromRAML8,
       LoadFromRAML9, LoadFromRAML10, LoadFromRAML11, LoadFromRAML12, LoadFromRAML13, LoadFromRAML14,
       LoadFromRAML15, Mask0, Mask1, Mask2, Mask3, multiplexer_3_out, or_1_out, or_2_out, or_3_out, or_4_out,
       or_5_out, or_6_out, or_7_out, or_8_out, or_9_out, or_10_out, or_11_out, or_12_out, or_13_out,
       or_14_out, or_15_out, or_16_out, or_17_out, or_18_out, or_19_out, or_20_out, or_21_out, or_22_out,
       or_23_out, or_24_out, or_25_out, or_26_out, or_27_out, or_28_out, or_29_out, or_30_out, or_31_out,
       or_32_out, or_33_out, or_34_out, or_35_out, or_36_out, or_37_out, or_38_out, or_39_out, or_40_out,
       or_41_out, or_42_out, or_43_out, or_44_out, or_45_out, or_46_out, or_47_out, or_48_out, or_49_out,
       or_50_out, or_51_out, or_52_out, or_53_out, or_54_out, or_55_out, or_56_out, or_57_out, or_58_out,
       or_59_out, or_60_out, or_61_out, or_62_out, or_63_out, or_64_out, or_65_out, or_66_out, or_67_out,
       or_68_out, or_69_out, or_70_out, or_71_out, or_72_out, or_73_out, or_74_out, or_75_out, or_76_out,
       or_77_out, or_78_out, or_79_out, or_80_out, or_81_out, or_82_out, or_83_out, or_84_out, or_85_out,
       or_86_out, or_87_out, or_88_out, or_89_out, or_90_out, or_91_out, or_92_out, or_93_out, or_94_out,
       or_95_out, or_96_out, or_97_out, or_98_out, or_99_out, or_100_out, or_101_out, or_102_out, or_103_out,
       or_104_out, or_105_out, or_106_out, or_107_out, or_108_out, or_109_out, or_110_out, or_111_out,
       or_112_out, or_113_out, or_114_out, or_115_out, or_116_out, or_117_out, or_118_out, or_119_out,
       or_120_out, or_121_out, or_122_out, or_123_out, or_124_out, or_125_out, or_126_out, or_127_out,
       or_128_out, or_129_out, or_130_out, or_131_out, or_132_out, or_133_out, or_134_out, or_135_out,
       or_136_out, or_137_out, or_138_out, or_139_out, or_140_out, or_141_out, or_142_out, or_143_out,
       or_144_out, or_145_out, or_146_out, or_147_out, or_148_out, or_149_out, or_150_out, or_151_out,
       or_152_out, or_153_out, or_154_out, or_155_out, or_156_out, or_157_out, or_158_out, or_159_out,
       or_160_out, or_161_out, or_162_out, or_163_out, or_164_out, or_165_out, or_166_out, or_167_out,
       or_169_out, or_170_out, Put_Dirty0, Put_Dirty1, Put_Dirty2, Put_Dirty3, TagEq, undriven, Valid_L0,
       Valid_L1, Valid_L2, Valid_L3, Valid_L4, Valid_L5, Valid_L6, Valid_L7, Valid_L8, Valid_L9, Valid_L10,
       Valid_L11, Valid_L12, Valid_L13, Valid_L14, Valid_L15, Valod_L0_Dirty, Valod_L1_Dirty, Valod_L2_Dirty,
       Valod_L3_Dirty, Valod_L4_Dirty, Valod_L5_Dirty, Valod_L6_Dirty, Valod_L7_Dirty, Valod_L8_Dirty,
       Valod_L9_Dirty, Valod_L10_Dirty, Valod_L11_Dirty, Valod_L12_Dirty, Valod_L13_Dirty, Valod_L14_Dirty,
       Valod_L15_Dirty;
  wire [11:0] tagL0, tagL1, tagL2, tagL3, tagL4, tagL5, tagL6, tagL7, tagL8, tagL9, tagL10, tagL11, tagL12,
       tagL13, tagL14, tagL15, xor_1_out;
  wire [31:0] I0_t, I1_t, I2_t, I3_t, InputToRAM, L0_0, L0_1, L0_2, L0_3, L1_0, L1_1, L1_2, L1_3, L2_0, L2_1,
       L2_2, L2_3, L3_0, L3_1, L3_2, L3_3, L4_0, L4_1, L4_2, L4_3, L5_0, L5_1, L5_2, L5_3, L6_0, L6_1, L6_2,
       L6_3, L7_0, L7_1, L7_2, L7_3, L8_0, L8_1, L8_2, L8_3, L9_0, L9_1, L9_2, L9_3, L10_0, L10_1, L10_2,
       L10_3, L11_0, L11_1, L11_2, L11_3, L12_0, L12_1, L12_2, L12_3, L13_0, L13_1, L13_2, L13_3, L14_0,
       L14_1, L14_2, L14_3, L15_0, L15_1, L15_2, L15_3;

  Demultiplexer #(.select(4), .enable("false")) demultiplexer_1 (
    .out0(EN_L0), .out1(EN_L1), .out2(EN_L2), .out3(EN_L3), .out4(EN_L4), .out5(EN_L5), .out6(EN_L6),
    .out7(EN_L7), .out8(EN_L8), .out9(EN_L9), .out10(EN_L10), .out11(EN_L11), .out12(EN_L12), .out13(EN_L13),
    .out14(EN_L14), .out15(EN_L15), .in(minus_R_W), .sel(ADDRIN[7:4]));
  or or_1 (or_1_out, ~Write_RAM, Put_Dirty0);  // OR_Gate
  or or_2 (or_2_out, ~Write_RAM, Put_Dirty3);  // OR_Gate
  Decoder #(.select(2), .enable("false")) decoder_1 (
    .out0(decoder_1_out0), .out1(decoder_1_out1), .out2(decoder_1_out2), .out3(decoder_1_out3),
    .sel(ADDRIN[3:2]));
  and and_1 (Mask0, or_1_out, Mask[0]);
  or or_3 (or_3_out, ~Write_RAM, Put_Dirty1);  // OR_Gate
  or or_4 (or_4_out, ~Write_RAM, Put_Dirty2);  // OR_Gate
  and and_2 (Mask3, or_2_out, Mask[3]);
  ResolverRAMValue resolverramvalue_1 (.in_1(Input_To_RAM), .out_2(InputToRAM));
  and and_3 (Put_Dirty0, Write_RAM, decoder_1_out0);
  and and_4 (Put_Dirty1, Write_RAM, decoder_1_out1);
  and and_5 (Put_Dirty2, decoder_1_out2, Write_RAM);
  and and_6 (Put_Dirty3, decoder_1_out3, Write_RAM);
  and and_7 (Mask1, or_3_out, Mask[1]);
  and and_8 (Mask2, or_4_out, Mask[2]);
  MUX2 mux2_1 (.in_1(I0), .in_2(InputToRAM), .out_4(I0_t), .in_3(Write_RAM));
  and and_9 (and_9_out, EN_L0, Mask0, or_5_out);
  or or_5 (or_5_out, Write_RAM, ~Dirty_L0_0);  // OR_Gate
  or or_6 (or_6_out, Write_RAM, ~Dirty_L7_0);  // OR_Gate
  and and_10 (and_10_out, EN_L8, Mask0, or_7_out);
  or or_7 (or_7_out, Write_RAM, ~Dirty_L8_0);  // OR_Gate
  or or_8 (or_8_out, Write_RAM, ~Dirty_L9_0);  // OR_Gate
  or or_9 (or_9_out, Write_RAM, ~Dirty_L10_0);  // OR_Gate
  or or_10 (or_10_out, Write_RAM, ~Dirty_L11_0);  // OR_Gate
  or or_11 (or_11_out, Write_RAM, ~Dirty_L12_0);  // OR_Gate
  or or_12 (or_12_out, Write_RAM, ~Dirty_L13_0);  // OR_Gate
  or or_13 (or_13_out, Write_RAM, ~Dirty_L14_0);  // OR_Gate
  or or_14 (or_14_out, Write_RAM, ~Dirty_L15_0);  // OR_Gate
  MUX2 mux2_2 (.in_1(I1), .in_2(InputToRAM), .out_4(I1_t), .in_3(Write_RAM));
  Register #(.width(32)) register_1 (.D(I0_t), .en(and_9_out), .Q(L0_0), .clk(CLK), .clr(CLR));
  Register #(.width(32)) register_2 (.D(I0_t), .en(and_11_out), .Q(L1_0), .clk(CLK), .clr(CLR));
  and and_11 (and_11_out, EN_L1, Mask0, or_15_out);
  or or_15 (or_15_out, Write_RAM, ~Dirty_L1_0);  // OR_Gate
  or or_16 (or_16_out, Write_RAM, ~Dirty_L2_0);  // OR_Gate
  or or_17 (or_17_out, Write_RAM, ~Dirty_L3_0);  // OR_Gate
  or or_18 (or_18_out, Write_RAM, ~Dirty_L4_0);  // OR_Gate
  and and_12 (and_12_out, EN_L5, Mask0, or_19_out);
  or or_19 (or_19_out, Write_RAM, ~Dirty_L5_0);  // OR_Gate
  and and_13 (and_13_out, EN_L6, Mask0, or_20_out);
  or or_20 (or_20_out, Write_RAM, ~Dirty_L6_0);  // OR_Gate
  Register #(.width(32)) register_3 (.D(I0_t), .en(and_14_out), .Q(L7_0), .clk(CLK), .clr(CLR));
  and and_14 (and_14_out, EN_L7, Mask0, or_6_out);
  Register #(.width(32)) register_4 (.D(I0_t), .en(and_10_out), .Q(L8_0), .clk(CLK), .clr(CLR));
  Register #(.width(32)) register_5 (.D(I0_t), .en(and_15_out), .Q(L9_0), .clk(CLK), .clr(CLR));
  and and_15 (and_15_out, EN_L9, Mask0, or_8_out);
  Register #(.width(32)) register_6 (.D(I0_t), .en(and_16_out), .Q(L10_0), .clk(CLK), .clr(CLR));
  and and_16 (and_16_out, EN_L10, Mask0, or_9_out);
  Register #(.width(32)) register_7 (.D(I0_t), .en(and_17_out), .Q(L11_0), .clk(CLK), .clr(CLR));
  and and_17 (and_17_out, EN_L11, Mask0, or_10_out);
  Register #(.width(32)) register_8 (.D(I0_t), .en(and_18_out), .Q(L12_0), .clk(CLK), .clr(CLR));
  and and_18 (and_18_out, EN_L12, Mask0, or_11_out);
  Register #(.width(32)) register_9 (.D(I0_t), .en(and_19_out), .Q(L13_0), .clk(CLK), .clr(CLR));
  and and_19 (and_19_out, EN_L13, Mask0, or_12_out);
  Register #(.width(32)) register_10 (.D(I0_t), .en(and_20_out), .Q(L14_0), .clk(CLK), .clr(CLR));
  and and_20 (and_20_out, Mask0, EN_L14, or_13_out);
  Register #(.width(32)) register_11 (.D(I0_t), .en(and_21_out), .Q(L15_0), .clk(CLK), .clr(CLR));
  and and_21 (and_21_out, EN_L15, Mask0, or_14_out);
  MUX2 mux2_3 (.in_1(I2), .in_2(InputToRAM), .out_4(I2_t), .in_3(Write_RAM));
  or or_21 (or_21_out, Write_RAM, ~Dirty_L0_1);  // OR_Gate
  or or_22 (or_22_out, Write_RAM, ~Dirty_L1_1);  // OR_Gate
  Register #(.width(32)) register_12 (.D(I0_t), .en(and_22_out), .Q(L2_0), .clk(CLK), .clr(CLR));
  and and_22 (and_22_out, EN_L2, Mask0, or_16_out);
  Register #(.width(32)) register_13 (.D(I0_t), .en(and_23_out), .Q(L3_0), .clk(CLK), .clr(CLR));
  and and_23 (and_23_out, EN_L3, Mask0, or_17_out);
  Register #(.width(32)) register_14 (.D(I0_t), .en(and_24_out), .Q(L4_0), .clk(CLK), .clr(CLR));
  and and_24 (and_24_out, EN_L4, Mask0, or_18_out);
  Register #(.width(32)) register_15 (.D(I0_t), .en(and_12_out), .Q(L5_0), .clk(CLK), .clr(CLR));
  Register #(.width(32)) register_16 (.D(I0_t), .en(and_13_out), .Q(L6_0), .clk(CLK), .clr(CLR));
  or or_23 (or_23_out, Write_RAM, ~Dirty_L7_1);  // OR_Gate
  or or_24 (or_24_out, Write_RAM, ~Dirty_L8_1);  // OR_Gate
  or or_25 (or_25_out, Write_RAM, ~Dirty_L9_1);  // OR_Gate
  or or_26 (or_26_out, Write_RAM, ~Dirty_L10_1);  // OR_Gate
  or or_27 (or_27_out, Write_RAM, ~Dirty_L12_1);  // OR_Gate
  or or_28 (or_28_out, Write_RAM, ~Dirty_L14_1);  // OR_Gate
  or or_29 (or_29_out, Write_RAM, ~Dirty_L15_1);  // OR_Gate
  Register #(.width(32)) register_17 (.D(I1_t), .en(and_25_out), .Q(L0_1), .clk(CLK), .clr(CLR));
  and and_25 (and_25_out, EN_L0, Mask1, or_21_out);
  and and_26 (and_26_out, EN_L1, Mask1, or_22_out);
  or or_30 (or_30_out, Write_RAM, ~Dirty_L2_1);  // OR_Gate
  or or_31 (or_31_out, Write_RAM, ~Dirty_L3_1);  // OR_Gate
  or or_32 (or_32_out, Write_RAM, ~Dirty_L4_1);  // OR_Gate
  and and_27 (and_27_out, EN_L5, Mask1, or_33_out);
  or or_33 (or_33_out, Write_RAM, ~Dirty_L5_1);  // OR_Gate
  and and_28 (and_28_out, EN_L6, Mask1, or_34_out);
  or or_34 (or_34_out, Write_RAM, ~Dirty_L6_1);  // OR_Gate
  Register #(.width(32)) register_18 (.D(I1_t), .en(and_29_out), .Q(L7_1), .clk(CLK), .clr(CLR));
  and and_29 (and_29_out, EN_L7, Mask1, or_23_out);
  Register #(.width(32)) register_19 (.D(I1_t), .en(and_30_out), .Q(L8_1), .clk(CLK), .clr(CLR));
  and and_30 (and_30_out, EN_L8, Mask1, or_24_out);
  Register #(.width(32)) register_20 (.D(I1_t), .en(and_31_out), .Q(L9_1), .clk(CLK), .clr(CLR));
  and and_31 (and_31_out, EN_L9, Mask1, or_25_out);
  Register #(.width(32)) register_21 (.D(I1_t), .en(and_32_out), .Q(L10_1), .clk(CLK), .clr(CLR));
  and and_32 (and_32_out, EN_L10, Mask1, or_26_out);
  and and_33 (and_33_out, EN_L11, Mask1, or_35_out);
  or or_35 (or_35_out, Write_RAM, ~Dirty_L11_1);  // OR_Gate
  Register #(.width(32)) register_22 (.D(I1_t), .en(and_34_out), .Q(L12_1), .clk(CLK), .clr(CLR));
  and and_34 (and_34_out, EN_L12, Mask1, or_27_out);
  and and_35 (and_35_out, EN_L13, Mask1, or_36_out);
  or or_36 (or_36_out, Write_RAM, ~Dirty_L13_1);  // OR_Gate
  Register #(.width(32)) register_23 (.D(I1_t), .en(and_36_out), .Q(L14_1), .clk(CLK), .clr(CLR));
  and and_36 (and_36_out, EN_L14, Mask1, or_28_out);
  Register #(.width(32)) register_24 (.D(I1_t), .en(and_37_out), .Q(L15_1), .clk(CLK), .clr(CLR));
  and and_37 (and_37_out, EN_L15, Mask1, or_29_out);
  MUX2 mux2_4 (.in_1(I3), .in_2(InputToRAM), .out_4(I3_t), .in_3(Write_RAM));
  or or_37 (or_37_out, Write_RAM, ~Dirty_L0_2);  // OR_Gate
  Register #(.width(32)) register_25 (.D(I1_t), .en(and_26_out), .Q(L1_1), .clk(CLK), .clr(CLR));
  Register #(.width(32)) register_26 (.D(I1_t), .en(and_38_out), .Q(L2_1), .clk(CLK), .clr(CLR));
  and and_38 (and_38_out, EN_L2, Mask1, or_30_out);
  Register #(.width(32)) register_27 (.D(I1_t), .en(and_39_out), .Q(L3_1), .clk(CLK), .clr(CLR));
  and and_39 (and_39_out, EN_L3, Mask1, or_31_out);
  Register #(.width(32)) register_28 (.D(I1_t), .en(and_40_out), .Q(L4_1), .clk(CLK), .clr(CLR));
  and and_40 (and_40_out, EN_L4, Mask1, or_32_out);
  Register #(.width(32)) register_29 (.D(I1_t), .en(and_27_out), .Q(L5_1), .clk(CLK), .clr(CLR));
  Register #(.width(32)) register_30 (.D(I1_t), .en(and_28_out), .Q(L6_1), .clk(CLK), .clr(CLR));
  or or_38 (or_38_out, Write_RAM, ~Dirty_L8_2);  // OR_Gate
  Register #(.width(32)) register_31 (.D(I1_t), .en(and_33_out), .Q(L11_1), .clk(CLK), .clr(CLR));
  Register #(.width(32)) register_32 (.D(I1_t), .en(and_35_out), .Q(L13_1), .clk(CLK), .clr(CLR));
  Register #(.width(32)) register_33 (.D(I2_t), .en(and_41_out), .Q(L0_2), .clk(CLK), .clr(CLR));
  and and_41 (and_41_out, EN_L0, Mask2, or_37_out);
  and and_42 (and_42_out, Mask2, or_39_out);
  or or_39 (or_39_out, Write_RAM, ~Dirty_L1_2);  // OR_Gate
  or or_40 (or_40_out, Write_RAM, ~Dirty_L5_2);  // OR_Gate
  or or_41 (or_41_out, Write_RAM, ~Dirty_L6_2);  // OR_Gate
  and and_43 (and_43_out, EN_L7, Mask2, or_42_out);
  or or_42 (or_42_out, Write_RAM, ~Dirty_L7_2);  // OR_Gate
  Register #(.width(32)) register_34 (.D(I2_t), .en(and_44_out), .Q(L8_2), .clk(CLK), .clr(CLR));
  and and_44 (and_44_out, EN_L8, Mask2, or_38_out);
  and and_45 (and_45_out, EN_L9, Mask2, or_43_out);
  or or_43 (or_43_out, Write_RAM, ~Dirty_L9_2);  // OR_Gate
  and and_46 (and_46_out, EN_L10, Mask2, or_44_out);
  or or_44 (or_44_out, Write_RAM, ~Dirty_L10_2);  // OR_Gate
  and and_47 (and_47_out, EN_L11, Mask2, or_45_out);
  or or_45 (or_45_out, Write_RAM, ~Dirty_L11_2);  // OR_Gate
  and and_48 (and_48_out, EN_L12, Mask2, or_46_out);
  or or_46 (or_46_out, Write_RAM, ~Dirty_L12_2);  // OR_Gate
  and and_49 (and_49_out, EN_L13, Mask2, or_47_out);
  or or_47 (or_47_out, Write_RAM, ~Dirty_L13_2);  // OR_Gate
  and and_50 (and_50_out, EN_L14, Mask2, or_48_out);
  or or_48 (or_48_out, Write_RAM, ~Dirty_L14_2);  // OR_Gate
  and and_51 (and_51_out, EN_L15, Mask2, or_49_out);
  or or_49 (or_49_out, Write_RAM, ~Dirty_L15_2);  // OR_Gate
  Register #(.width(32)) register_35 (.D(I2_t), .en(and_42_out), .Q(L1_2), .clk(CLK), .clr(CLR));
  and and_52 (and_52_out, EN_L2, Mask2, or_50_out);
  or or_50 (or_50_out, Write_RAM, ~Dirty_L2_2);  // OR_Gate
  and and_53 (and_53_out, EN_L3, Mask2, or_51_out);
  or or_51 (or_51_out, Write_RAM, ~Dirty_L3_2);  // OR_Gate
  and and_54 (and_54_out, EN_L4, Mask2, or_52_out);
  or or_52 (or_52_out, Write_RAM, ~Dirty_L4_2);  // OR_Gate
  Register #(.width(32)) register_36 (.D(I2_t), .en(and_55_out), .Q(L5_2), .clk(CLK), .clr(CLR));
  and and_55 (and_55_out, EN_L5, Mask2, or_40_out);
  Register #(.width(32)) register_37 (.D(I2_t), .en(and_56_out), .Q(L6_2), .clk(CLK), .clr(CLR));
  and and_56 (and_56_out, EN_L6, Mask2, or_41_out);
  Register #(.width(32)) register_38 (.D(I2_t), .en(and_43_out), .Q(L7_2), .clk(CLK), .clr(CLR));
  Register #(.width(32)) register_39 (.D(I2_t), .en(and_45_out), .Q(L9_2), .clk(CLK), .clr(CLR));
  Register #(.width(32)) register_40 (.D(I2_t), .en(and_46_out), .Q(L10_2), .clk(CLK), .clr(CLR));
  Register #(.width(32)) register_41 (.D(I2_t), .en(and_47_out), .Q(L11_2), .clk(CLK), .clr(CLR));
  Register #(.width(32)) register_42 (.D(I2_t), .en(and_48_out), .Q(L12_2), .clk(CLK), .clr(CLR));
  Register #(.width(32)) register_43 (.D(I2_t), .en(and_49_out), .Q(L13_2), .clk(CLK), .clr(CLR));
  Register #(.width(32)) register_44 (.D(I2_t), .en(and_50_out), .Q(L14_2), .clk(CLK), .clr(CLR));
  Register #(.width(32)) register_45 (.D(I2_t), .en(and_51_out), .Q(L15_2), .clk(CLK), .clr(CLR));
  and and_57 (and_57_out, EN_L0, Mask3, or_53_out);
  or or_53 (or_53_out, Write_RAM, ~Dirty_L0_3);  // OR_Gate
  or or_54 (or_54_out, Write_RAM, ~Dirty_L1_3);  // OR_Gate
  Register #(.width(32)) register_46 (.D(I2_t), .en(and_52_out), .Q(L2_2), .clk(CLK), .clr(CLR));
  Register #(.width(32)) register_47 (.D(I2_t), .en(and_53_out), .Q(L3_2), .clk(CLK), .clr(CLR));
  Register #(.width(32)) register_48 (.D(I2_t), .en(and_54_out), .Q(L4_2), .clk(CLK), .clr(CLR));
  or or_55 (or_55_out, Write_RAM, ~Dirty_L6_3);  // OR_Gate
  and and_58 (and_58_out, EN_L7, Mask3, or_56_out);
  or or_56 (or_56_out, Write_RAM, ~Dirty_L7_3);  // OR_Gate
  and and_59 (and_59_out, EN_L8, Mask3, or_57_out);
  or or_57 (or_57_out, Write_RAM, ~Dirty_L8_3);  // OR_Gate
  and and_60 (and_60_out, EN_L9, Mask3, or_58_out);
  or or_58 (or_58_out, Write_RAM, ~Dirty_L9_3);  // OR_Gate
  and and_61 (and_61_out, EN_L10, Mask3, or_59_out);
  or or_59 (or_59_out, Write_RAM, ~Dirty_L10_3);  // OR_Gate
  or or_60 (or_60_out, Write_RAM, ~Dirty_L11_3);  // OR_Gate
  and and_62 (and_62_out, EN_L12, Mask3, or_61_out);
  or or_61 (or_61_out, Write_RAM, ~Dirty_L12_3);  // OR_Gate
  or or_62 (or_62_out, Write_RAM, ~Dirty_L13_3);  // OR_Gate
  and and_63 (and_63_out, EN_L14, Mask3, or_63_out);
  or or_63 (or_63_out, Write_RAM, ~Dirty_L14_3);  // OR_Gate
  and and_64 (and_64_out, EN_L15, Mask3, or_64_out);
  or or_64 (or_64_out, Write_RAM, ~Dirty_L15_3);  // OR_Gate
  Register #(.width(32)) register_49 (.D(I3_t), .en(and_57_out), .Q(L0_3), .clk(CLK), .clr(CLR));
  Register #(.width(32)) register_50 (.D(I3_t), .en(and_65_out), .Q(L1_3), .clk(CLK), .clr(CLR));
  and and_65 (and_65_out, EN_L1, Mask3, or_54_out);
  and and_66 (and_66_out, EN_L2, Mask3, or_65_out);
  or or_65 (or_65_out, Write_RAM, ~Dirty_L2_3);  // OR_Gate
  and and_67 (and_67_out, EN_L3, Mask3, or_66_out);
  or or_66 (or_66_out, Write_RAM, ~Dirty_L3_3);  // OR_Gate
  and and_68 (and_68_out, EN_L4, Mask3, or_67_out);
  or or_67 (or_67_out, Write_RAM, ~Dirty_L4_3);  // OR_Gate
  Register #(.width(32)) register_51 (.D(I3_t), .en(and_69_out), .Q(L5_3), .clk(CLK), .clr(CLR));
  and and_69 (and_69_out, EN_L5, Mask3, or_68_out);
  or or_68 (or_68_out, Write_RAM, ~Dirty_L5_3);  // OR_Gate
  Register #(.width(32)) register_52 (.D(I3_t), .en(and_70_out), .Q(L6_3), .clk(CLK), .clr(CLR));
  and and_70 (and_70_out, EN_L6, Mask3, or_55_out);
  Register #(.width(32)) register_53 (.D(I3_t), .en(and_58_out), .Q(L7_3), .clk(CLK), .clr(CLR));
  Register #(.width(32)) register_54 (.D(I3_t), .en(and_59_out), .Q(L8_3), .clk(CLK), .clr(CLR));
  Register #(.width(32)) register_55 (.D(I3_t), .en(and_60_out), .Q(L9_3), .clk(CLK), .clr(CLR));
  Register #(.width(32)) register_56 (.D(I3_t), .en(and_61_out), .Q(L10_3), .clk(CLK), .clr(CLR));
  Register #(.width(32)) register_57 (.D(I3_t), .en(and_71_out), .Q(L11_3), .clk(CLK), .clr(CLR));
  and and_71 (and_71_out, EN_L11, Mask3, or_60_out);
  Register #(.width(32)) register_58 (.D(I3_t), .en(and_62_out), .Q(L12_3), .clk(CLK), .clr(CLR));
  Register #(.width(32)) register_59 (.D(I3_t), .en(and_72_out), .Q(L13_3), .clk(CLK), .clr(CLR));
  and and_72 (and_72_out, EN_L13, Mask3, or_62_out);
  Register #(.width(32)) register_60 (.D(I3_t), .en(and_63_out), .Q(L14_3), .clk(CLK), .clr(CLR));
  Register #(.width(32)) register_61 (.D(I3_t), .en(and_64_out), .Q(L15_3), .clk(CLK), .clr(CLR));
  Register #(.width(32)) register_62 (.D(I3_t), .en(and_66_out), .Q(L2_3), .clk(CLK), .clr(CLR));
  Register #(.width(32)) register_63 (.D(I3_t), .en(and_67_out), .Q(L3_3), .clk(CLK), .clr(CLR));
  Register #(.width(32)) register_64 (.D(I3_t), .en(and_68_out), .Q(L4_3), .clk(CLK), .clr(CLR));
  Register #(.width(12)) register_65 (.D(ADDRIN[19:8]), .en(EN_L0), .Q(tagL0), .clk(CLK), .clr(CLR));
  Register #(.width(12)) register_66 (.D(ADDRIN[19:8]), .en(EN_L1), .Q(tagL1), .clk(CLK), .clr(CLR));
  Register #(.width(12)) register_67 (.D(ADDRIN[19:8]), .en(EN_L7), .Q(tagL7), .clk(CLK), .clr(CLR));
  Register #(.width(12)) register_68 (.D(ADDRIN[19:8]), .en(EN_L8), .Q(tagL8), .clk(CLK), .clr(CLR));
  Register #(.width(12)) register_69 (.D(ADDRIN[19:8]), .en(EN_L9), .Q(tagL9), .clk(CLK), .clr(CLR));
  Register #(.width(12)) register_70 (.D(ADDRIN[19:8]), .en(EN_L10), .Q(tagL10), .clk(CLK), .clr(CLR));
  Register #(.width(12)) register_71 (.D(ADDRIN[19:8]), .en(EN_L11), .Q(tagL11), .clk(CLK), .clr(CLR));
  Register #(.width(12)) register_72 (.D(ADDRIN[19:8]), .en(EN_L12), .Q(tagL12), .clk(CLK), .clr(CLR));
  Register #(.width(12)) register_73 (.D(ADDRIN[19:8]), .en(EN_L13), .Q(tagL13), .clk(CLK), .clr(CLR));
  Register #(.width(12)) register_74 (.D(ADDRIN[19:8]), .en(EN_L14), .Q(tagL14), .clk(CLK), .clr(CLR));
  Register #(.width(12)) register_75 (.D(ADDRIN[19:8]), .en(EN_L15), .Q(tagL15), .clk(CLK), .clr(CLR));
  Register #(.width(12)) register_76 (.D(ADDRIN[19:8]), .en(EN_L2), .Q(tagL2), .clk(CLK), .clr(CLR));
  Register #(.width(12)) register_77 (.D(ADDRIN[19:8]), .en(EN_L3), .Q(tagL3), .clk(CLK), .clr(CLR));
  Register #(.width(12)) register_78 (.D(ADDRIN[19:8]), .en(EN_L4), .Q(tagL4), .clk(CLK), .clr(CLR));
  Register #(.width(12)) register_79 (.D(ADDRIN[19:8]), .en(EN_L5), .Q(tagL5), .clk(CLK), .clr(CLR));
  Register #(.width(12)) register_80 (.D(ADDRIN[19:8]), .en(EN_L6), .Q(tagL6), .clk(CLK), .clr(CLR));
  D_Flip_Flop d_ff_1 (.clk(CLK), .Q(Valid_L0), .preset(EN_L0), .reset(CLR));  // open: D, Qn, en
  D_Flip_Flop d_ff_2 (.clk(CLK), .Q(Valid_L7), .preset(EN_L7), .reset(CLR));  // open: D, Qn, en
  D_Flip_Flop d_ff_3 (.clk(CLK), .Q(Valid_L8), .preset(EN_L8), .reset(CLR));  // open: D, Qn, en
  D_Flip_Flop d_ff_4 (.clk(CLK), .Q(Valid_L9), .preset(EN_L9), .reset(CLR));  // open: D, Qn, en
  D_Flip_Flop d_ff_5 (.clk(CLK), .Q(Valid_L10), .preset(EN_L10), .reset(CLR));  // open: D, Qn, en
  D_Flip_Flop d_ff_6 (.clk(CLK), .Q(Valid_L11), .preset(EN_L11), .reset(CLR));  // open: D, Qn, en
  D_Flip_Flop d_ff_7 (.clk(CLK), .Q(Valid_L12), .preset(EN_L12), .reset(CLR));  // open: D, Qn, en
  D_Flip_Flop d_ff_8 (.clk(CLK), .Q(Valid_L13), .preset(EN_L13), .reset(CLR));  // open: D, Qn, en
  D_Flip_Flop d_ff_9 (.clk(CLK), .Q(Valid_L14), .preset(EN_L14), .reset(CLR));  // open: D, Qn, en
  D_Flip_Flop d_ff_10 (.clk(CLK), .Q(Valid_L15), .preset(EN_L15), .reset(CLR));  // open: D, Qn, en
  D_Flip_Flop d_ff_11 (.clk(CLK), .Q(Valid_L1), .preset(EN_L1), .reset(CLR));  // open: D, Qn, en
  D_Flip_Flop d_ff_12 (.clk(CLK), .Q(Valid_L2), .preset(EN_L2), .reset(CLR));  // open: D, Qn, en
  D_Flip_Flop d_ff_13 (.clk(CLK), .Q(Valid_L3), .preset(EN_L3), .reset(CLR));  // open: D, Qn, en
  D_Flip_Flop d_ff_14 (.clk(CLK), .Q(Valid_L4), .preset(EN_L4), .reset(CLR));  // open: D, Qn, en
  D_Flip_Flop d_ff_15 (.clk(CLK), .Q(Valid_L5), .preset(EN_L5), .reset(CLR));  // open: D, Qn, en
  D_Flip_Flop d_ff_16 (.clk(CLK), .Q(Valid_L6), .preset(EN_L6), .reset(CLR));  // open: D, Qn, en
  D_Flip_Flop d_ff_17 (.clk(CLK), .D(Valid_L0), .Q(Valod_L0_Dirty), .reset(CLR));  // open: Qn, preset, en
  D_Flip_Flop d_ff_18 (.clk(CLK), .D(Valid_L8), .Q(Valod_L8_Dirty), .reset(CLR));  // open: Qn, preset, en
  D_Flip_Flop d_ff_19 (.clk(CLK), .D(Valid_L1), .Q(Valod_L1_Dirty), .reset(CLR));  // open: Qn, preset, en
  D_Flip_Flop d_ff_20 (.clk(CLK), .D(Valid_L3), .Q(Valod_L3_Dirty), .reset(CLR));  // open: Qn, preset, en
  D_Flip_Flop d_ff_21 (.clk(CLK), .D(Valid_L4), .Q(Valod_L4_Dirty), .reset(CLR));  // open: Qn, preset, en
  D_Flip_Flop d_ff_22 (.clk(CLK), .D(Valid_L5), .Q(Valod_L5_Dirty), .reset(CLR));  // open: Qn, preset, en
  D_Flip_Flop d_ff_23 (.clk(CLK), .D(Valid_L6), .Q(Valod_L6_Dirty), .reset(CLR));  // open: Qn, preset, en
  D_Flip_Flop d_ff_24 (.clk(CLK), .D(Valid_L7), .Q(Valod_L7_Dirty), .reset(CLR));  // open: Qn, preset, en
  D_Flip_Flop d_ff_25 (.clk(CLK), .D(Valid_L9), .Q(Valod_L9_Dirty), .reset(CLR));  // open: Qn, preset, en
  D_Flip_Flop d_ff_26 (.clk(CLK), .D(Valid_L10), .Q(Valod_L10_Dirty), .reset(CLR));  // open: Qn, preset, en
  D_Flip_Flop d_ff_27 (.clk(CLK), .D(Valid_L11), .Q(Valod_L11_Dirty), .reset(CLR));  // open: Qn, preset, en
  D_Flip_Flop d_ff_28 (.clk(CLK), .D(Valid_L12), .Q(Valod_L12_Dirty), .reset(CLR));  // open: Qn, preset, en
  D_Flip_Flop d_ff_29 (.clk(CLK), .D(Valid_L13), .Q(Valod_L13_Dirty), .reset(CLR));  // open: Qn, preset, en
  D_Flip_Flop d_ff_30 (.clk(CLK), .D(Valid_L14), .Q(Valod_L14_Dirty), .reset(CLR));  // open: Qn, preset, en
  D_Flip_Flop d_ff_31 (.clk(CLK), .D(Valid_L15), .Q(Valod_L15_Dirty), .reset(CLR));  // open: Qn, preset, en
  D_Flip_Flop d_ff_32 (.clk(CLK), .D(Valid_L2), .Q(Valod_L2_Dirty), .reset(CLR));  // open: Qn, preset, en
  and and_73 (and_73_out, TagEq, EN_L0, Valod_L0_Dirty, Put_Dirty0);
  D_Flip_Flop d_ff_33 (.clk(CLK), .D(and_73_out), .Q(Dirty_L0_0), .reset(or_69_out));  // open: Qn, preset, en
  or or_69 (or_69_out, CLR_Dirty_L0, CLR);
  and and_74 (and_74_out, EN_L1, TagEq, Valod_L1_Dirty, Put_Dirty0);
  and and_75 (and_75_out, EN_L8, Put_Dirty0, Valod_L8_Dirty);
  D_Flip_Flop d_ff_34 (.clk(CLK), .D(and_76_out), .Q(Dirty_L9_0), .reset(or_70_out));  // open: Qn, preset, en
  and and_76 (and_76_out, EN_L9, Put_Dirty0, Valod_L9_Dirty);
  or or_70 (or_70_out, CLR_Dirty_L9, CLR);
  D_Flip_Flop d_ff_35 (.clk(CLK), .D(and_77_out), .Q(Dirty_L10_0), .reset(or_71_out));  // open: Qn, preset, en
  and and_77 (and_77_out, EN_L10, Put_Dirty0, Valod_L10_Dirty);
  or or_71 (or_71_out, CLR_Dirty_L10, CLR);
  D_Flip_Flop d_ff_36 (.clk(CLK), .D(and_78_out), .Q(Dirty_L11_0), .reset(or_72_out));  // open: Qn, preset, en
  and and_78 (and_78_out, EN_L11, Put_Dirty0, Valod_L11_Dirty);
  or or_72 (or_72_out, CLR_Dirty_L11, CLR);
  D_Flip_Flop d_ff_37 (.clk(CLK), .D(and_79_out), .Q(Dirty_L12_0), .reset(or_73_out));  // open: Qn, preset, en
  and and_79 (and_79_out, EN_L12, Put_Dirty0, Valod_L12_Dirty);
  or or_73 (or_73_out, CLR_Dirty_L12, CLR);
  D_Flip_Flop d_ff_38 (.clk(CLK), .D(and_80_out), .Q(Dirty_L13_0), .reset(or_74_out));  // open: Qn, preset, en
  and and_80 (and_80_out, EN_L13, Put_Dirty0, Valod_L13_Dirty);
  or or_74 (or_74_out, CLR_Dirty_L13, CLR);
  D_Flip_Flop d_ff_39 (.clk(CLK), .D(and_81_out), .Q(Dirty_L14_0), .reset(or_75_out));  // open: Qn, preset, en
  and and_81 (and_81_out, EN_L14, Put_Dirty0, Valod_L14_Dirty);
  or or_75 (or_75_out, CLR_Dirty_L14, CLR);
  D_Flip_Flop d_ff_40 (.clk(CLK), .D(and_82_out), .Q(Dirty_L15_0), .reset(or_76_out));  // open: Qn, preset, en
  and and_82 (and_82_out, EN_L15, Put_Dirty0, Valod_L15_Dirty);
  or or_76 (or_76_out, CLR_Dirty_L15, CLR);
  D_Flip_Flop d_ff_41 (.clk(CLK), .Q(Dirty_L1_0), .preset(and_74_out), .reset(or_77_out));  // open: D, Qn, en
  or or_77 (or_77_out, CLR_Dirty_L1, CLR);
  D_Flip_Flop d_ff_42 (.clk(CLK), .D(and_83_out), .Q(Dirty_L2_0), .reset(or_78_out));  // open: Qn, preset, en
  and and_83 (and_83_out, EN_L2, Valod_L2_Dirty, Put_Dirty0);
  or or_78 (or_78_out, CLR_Dirty_L2, CLR);
  and and_84 (and_84_out, EN_L3, Put_Dirty0, Valod_L3_Dirty);
  D_Flip_Flop d_ff_43 (.clk(CLK), .D(and_85_out), .Q(Dirty_L4_0), .reset(or_79_out));  // open: Qn, preset, en
  and and_85 (and_85_out, EN_L4, Put_Dirty0, Valod_L4_Dirty);
  or or_79 (or_79_out, CLR_Dirty_L4, CLR);
  and and_86 (and_86_out, EN_L5, Put_Dirty0, Valod_L5_Dirty);
  and and_87 (and_87_out, EN_L6, Put_Dirty0, Valod_L6_Dirty);
  D_Flip_Flop d_ff_44 (.clk(CLK), .D(and_88_out), .Q(Dirty_L7_0), .reset(or_80_out));  // open: Qn, preset, en
  and and_88 (and_88_out, EN_L7, Put_Dirty0, Valod_L7_Dirty);
  or or_80 (or_80_out, CLR_Dirty_L7, CLR);
  D_Flip_Flop d_ff_45 (.clk(CLK), .D(and_75_out), .Q(Dirty_L8_0), .reset(or_81_out));  // open: Qn, preset, en
  or or_81 (or_81_out, CLR_Dirty_L8, CLR);
  or or_82 (or_82_out, Valod_L1_Dirty, Write_RAM);
  D_Flip_Flop d_ff_46 (.clk(CLK), .D(and_84_out), .Q(Dirty_L3_0), .reset(or_83_out));  // open: Qn, preset, en
  or or_83 (or_83_out, CLR_Dirty_L3, CLR);
  D_Flip_Flop d_ff_47 (.clk(CLK), .D(and_86_out), .Q(Dirty_L5_0), .reset(or_84_out));  // open: Qn, preset, en
  or or_84 (or_84_out, CLR_Dirty_L5, CLR);
  D_Flip_Flop d_ff_48 (.clk(CLK), .D(and_87_out), .Q(Dirty_L6_0), .reset(or_85_out));  // open: Qn, preset, en
  or or_85 (or_85_out, CLR_Dirty_L6, CLR);
  and and_89 (and_89_out, EN_L0, TagEq, Valod_L0_Dirty, Put_Dirty1);
  and and_90 (and_90_out, EN_L9, Put_Dirty1, Valod_L9_Dirty);
  and and_91 (and_91_out, EN_L10, Put_Dirty1, Valod_L10_Dirty);
  and and_92 (and_92_out, EN_L11, Put_Dirty1, Valod_L11_Dirty);
  and and_93 (and_93_out, EN_L12, Put_Dirty1, Valod_L12_Dirty);
  and and_94 (and_94_out, EN_L13, Put_Dirty1, Valod_L13_Dirty);
  and and_95 (and_95_out, EN_L14, Put_Dirty1, Valod_L14_Dirty);
  and and_96 (and_96_out, EN_L15, Put_Dirty1, Valod_L15_Dirty);
  D_Flip_Flop d_ff_49 (.clk(CLK), .D(and_89_out), .Q(Dirty_L0_1), .reset(or_86_out));  // open: Qn, preset, en
  or or_86 (or_86_out, CLR_Dirty_L0, CLR);
  D_Flip_Flop d_ff_50 (.clk(CLK), .Q(Dirty_L1_1), .preset(and_97_out), .reset(or_87_out));  // open: D, Qn, en
  and and_97 (and_97_out, EN_L1, TagEq, or_82_out, Put_Dirty1);
  or or_87 (or_87_out, CLR_Dirty_L1, CLR);
  and and_98 (and_98_out, EN_L2, Valod_L2_Dirty, Put_Dirty1);
  and and_99 (and_99_out, EN_L4, Put_Dirty1, Valod_L4_Dirty);
  and and_100 (and_100_out, EN_L7, Put_Dirty1, Valod_L7_Dirty);
  D_Flip_Flop d_ff_51 (.clk(CLK), .D(and_101_out), .Q(Dirty_L8_1), .reset(or_88_out));  // open: Qn, preset, en
  and and_101 (and_101_out, EN_L8, Put_Dirty1, Valod_L8_Dirty);
  or or_88 (or_88_out, CLR_Dirty_L8, CLR);
  D_Flip_Flop d_ff_52 (.clk(CLK), .D(and_90_out), .Q(Dirty_L9_1), .reset(or_89_out));  // open: Qn, preset, en
  or or_89 (or_89_out, CLR_Dirty_L9, CLR);
  D_Flip_Flop d_ff_53 (.clk(CLK), .D(and_91_out), .Q(Dirty_L10_1), .reset(or_90_out));  // open: Qn, preset, en
  or or_90 (or_90_out, CLR_Dirty_L10, CLR);
  D_Flip_Flop d_ff_54 (.clk(CLK), .D(and_92_out), .Q(Dirty_L11_1), .reset(or_91_out));  // open: Qn, preset, en
  or or_91 (or_91_out, CLR_Dirty_L11, CLR);
  D_Flip_Flop d_ff_55 (.clk(CLK), .D(and_93_out), .Q(Dirty_L12_1), .reset(or_92_out));  // open: Qn, preset, en
  or or_92 (or_92_out, CLR_Dirty_L12, CLR);
  D_Flip_Flop d_ff_56 (.clk(CLK), .D(and_94_out), .Q(Dirty_L13_1), .reset(or_93_out));  // open: Qn, preset, en
  or or_93 (or_93_out, CLR_Dirty_L13, CLR);
  D_Flip_Flop d_ff_57 (.clk(CLK), .D(and_95_out), .Q(Dirty_L14_1), .reset(or_94_out));  // open: Qn, preset, en
  or or_94 (or_94_out, CLR_Dirty_L14, CLR);
  D_Flip_Flop d_ff_58 (.clk(CLK), .D(and_96_out), .Q(Dirty_L15_1), .reset(or_95_out));  // open: Qn, preset, en
  or or_95 (or_95_out, CLR_Dirty_L15, CLR);
  D_Flip_Flop d_ff_59 (.clk(CLK), .D(and_98_out), .Q(Dirty_L2_1), .reset(or_96_out));  // open: Qn, preset, en
  or or_96 (or_96_out, CLR_Dirty_L2, CLR);
  D_Flip_Flop d_ff_60 (.clk(CLK), .D(and_102_out), .Q(Dirty_L3_1), .reset(or_97_out));  // open: Qn, preset, en
  and and_102 (and_102_out, EN_L3, Put_Dirty1, Valod_L3_Dirty);
  or or_97 (or_97_out, CLR_Dirty_L3, CLR);
  D_Flip_Flop d_ff_61 (.clk(CLK), .D(and_99_out), .Q(Dirty_L4_1), .reset(or_98_out));  // open: Qn, preset, en
  or or_98 (or_98_out, CLR_Dirty_L4, CLR);
  D_Flip_Flop d_ff_62 (.clk(CLK), .D(and_103_out), .Q(Dirty_L5_1), .reset(or_99_out));  // open: Qn, preset, en
  and and_103 (and_103_out, EN_L5, Put_Dirty1, Valod_L5_Dirty);
  or or_99 (or_99_out, CLR_Dirty_L5, CLR);
  D_Flip_Flop d_ff_63 (.clk(CLK), .D(and_104_out), .Q(Dirty_L6_1), .reset(or_100_out));  // open: Qn, preset, en
  and and_104 (and_104_out, EN_L6, Put_Dirty1, Valod_L6_Dirty);
  or or_100 (or_100_out, CLR_Dirty_L6, CLR);
  D_Flip_Flop d_ff_64 (.clk(CLK), .D(and_100_out), .Q(Dirty_L7_1), .reset(or_101_out));  // open: Qn, preset, en
  or or_101 (or_101_out, CLR_Dirty_L7, CLR);
  and and_105 (and_105_out, EN_L0, TagEq, Valod_L0_Dirty, Put_Dirty2);
  and and_106 (and_106_out, EN_L9, Put_Dirty2, Valod_L9_Dirty);
  and and_107 (and_107_out, EN_L10, Put_Dirty2, Valod_L10_Dirty);
  and and_108 (and_108_out, EN_L11, Put_Dirty2, Valod_L11_Dirty);
  and and_109 (and_109_out, EN_L12, Put_Dirty2, Valod_L12_Dirty);
  and and_110 (and_110_out, EN_L13, Put_Dirty2, Valod_L13_Dirty);
  and and_111 (and_111_out, EN_L14, Put_Dirty2, Valod_L14_Dirty);
  and and_112 (and_112_out, EN_L15, Put_Dirty2, Valod_L15_Dirty);
  D_Flip_Flop d_ff_65 (.clk(CLK), .D(and_105_out), .Q(Dirty_L0_2), .reset(or_102_out));  // open: Qn, preset, en
  or or_102 (or_102_out, CLR_Dirty_L0, CLR);
  D_Flip_Flop d_ff_66 (.clk(CLK), .D(and_113_out), .Q(Dirty_L1_2), .reset(or_103_out));  // open: Qn, preset, en
  and and_113 (and_113_out, EN_L1, TagEq, Valod_L1_Dirty, Put_Dirty2);
  or or_103 (or_103_out, CLR_Dirty_L1, CLR);
  and and_114 (and_114_out, EN_L2, Valod_L2_Dirty, Put_Dirty2);
  and and_115 (and_115_out, EN_L4, Put_Dirty2, Valod_L4_Dirty);
  and and_116 (and_116_out, EN_L5, Put_Dirty2, Valod_L5_Dirty);
  and and_117 (and_117_out, EN_L7, Put_Dirty2, Valod_L7_Dirty);
  D_Flip_Flop d_ff_67 (.clk(CLK), .D(and_118_out), .Q(Dirty_L8_2), .reset(or_104_out));  // open: Qn, preset, en
  and and_118 (and_118_out, EN_L8, Put_Dirty2, Valod_L8_Dirty);
  or or_104 (or_104_out, CLR_Dirty_L8, CLR);
  D_Flip_Flop d_ff_68 (.clk(CLK), .D(and_106_out), .Q(Dirty_L9_2), .reset(or_105_out));  // open: Qn, preset, en
  or or_105 (or_105_out, CLR_Dirty_L9, CLR);
  D_Flip_Flop d_ff_69 (.clk(CLK), .D(and_107_out), .Q(Dirty_L10_2), .reset(or_106_out));  // open: Qn, preset, en
  or or_106 (or_106_out, CLR_Dirty_L10, CLR);
  D_Flip_Flop d_ff_70 (.clk(CLK), .D(and_108_out), .Q(Dirty_L11_2), .reset(or_107_out));  // open: Qn, preset, en
  or or_107 (or_107_out, CLR_Dirty_L11, CLR);
  D_Flip_Flop d_ff_71 (.clk(CLK), .D(and_109_out), .Q(Dirty_L12_2), .reset(or_108_out));  // open: Qn, preset, en
  or or_108 (or_108_out, CLR_Dirty_L12, CLR);
  D_Flip_Flop d_ff_72 (.clk(CLK), .D(and_110_out), .Q(Dirty_L13_2), .reset(or_109_out));  // open: Qn, preset, en
  or or_109 (or_109_out, CLR_Dirty_L13, CLR);
  D_Flip_Flop d_ff_73 (.clk(CLK), .D(and_111_out), .Q(Dirty_L14_2), .reset(or_110_out));  // open: Qn, preset, en
  or or_110 (or_110_out, CLR_Dirty_L14, CLR);
  D_Flip_Flop d_ff_74 (.clk(CLK), .D(and_112_out), .Q(Dirty_L15_2), .reset(or_111_out));  // open: Qn, preset, en
  or or_111 (or_111_out, CLR_Dirty_L15, CLR);
  D_Flip_Flop d_ff_75 (.clk(CLK), .D(and_114_out), .Q(Dirty_L2_2), .reset(or_112_out));  // open: Qn, preset, en
  or or_112 (or_112_out, CLR_Dirty_L2, CLR);
  D_Flip_Flop d_ff_76 (.clk(CLK), .D(and_119_out), .Q(Dirty_L3_2), .reset(or_113_out));  // open: Qn, preset, en
  and and_119 (and_119_out, EN_L3, Put_Dirty2, Valod_L3_Dirty);
  or or_113 (or_113_out, CLR_Dirty_L3, CLR);
  D_Flip_Flop d_ff_77 (.clk(CLK), .D(and_115_out), .Q(Dirty_L4_2), .reset(or_114_out));  // open: Qn, preset, en
  or or_114 (or_114_out, CLR_Dirty_L4, CLR);
  D_Flip_Flop d_ff_78 (.clk(CLK), .D(and_116_out), .Q(Dirty_L5_2), .reset(or_115_out));  // open: Qn, preset, en
  or or_115 (or_115_out, CLR_Dirty_L5, CLR);
  D_Flip_Flop d_ff_79 (.clk(CLK), .D(and_120_out), .Q(Dirty_L6_2), .reset(or_116_out));  // open: Qn, preset, en
  and and_120 (and_120_out, EN_L6, Put_Dirty2, Valod_L6_Dirty);
  or or_116 (or_116_out, CLR_Dirty_L6, CLR);
  D_Flip_Flop d_ff_80 (.clk(CLK), .D(and_117_out), .Q(Dirty_L7_2), .reset(or_117_out));  // open: Qn, preset, en
  buf or_117 (or_117_out, CLR);  // OR_Gate
  and and_121 (and_121_out, EN_L1, TagEq, Valod_L1_Dirty, Put_Dirty3);
  and and_122 (and_122_out, EN_L8, Put_Dirty3, Valod_L8_Dirty);
  and and_123 (and_123_out, EN_L9, Put_Dirty3, Valod_L9_Dirty);
  D_Flip_Flop d_ff_81 (.clk(CLK), .D(and_124_out), .Q(Dirty_L10_3), .reset(or_118_out));  // open: Qn, preset, en
  and and_124 (and_124_out, EN_L10, Put_Dirty3, Valod_L10_Dirty);
  or or_118 (or_118_out, CLR_Dirty_L10, CLR);
  and and_125 (and_125_out, EN_L11, Put_Dirty3, Valod_L11_Dirty);
  and and_126 (and_126_out, EN_L12, Put_Dirty3, Valod_L12_Dirty);
  and and_127 (and_127_out, EN_L13, Put_Dirty3, Valod_L13_Dirty);
  D_Flip_Flop d_ff_82 (.clk(CLK), .D(and_128_out), .Q(Dirty_L14_3), .reset(or_119_out));  // open: Qn, preset, en
  and and_128 (and_128_out, EN_L14, Put_Dirty3, Valod_L14_Dirty);
  or or_119 (or_119_out, CLR_Dirty_L14, CLR);
  D_Flip_Flop d_ff_83 (.clk(CLK), .D(and_129_out), .Q(Dirty_L15_3), .reset(or_120_out));  // open: Qn, preset, en
  and and_129 (and_129_out, EN_L15, Put_Dirty3, Valod_L15_Dirty);
  or or_120 (or_120_out, CLR_Dirty_L15, CLR);
  D_Flip_Flop d_ff_84 (.clk(CLK), .D(and_130_out), .Q(Dirty_L0_3), .reset(or_121_out));  // open: Qn, preset, en
  and and_130 (and_130_out, EN_L0, TagEq, Valod_L0_Dirty, Put_Dirty3);
  or or_121 (or_121_out, CLR_Dirty_L0, CLR);
  D_Flip_Flop d_ff_85 (.clk(CLK), .D(and_121_out), .Q(Dirty_L1_3), .reset(or_122_out));  // open: Qn, preset, en
  or or_122 (or_122_out, CLR_Dirty_L1, CLR);
  and and_131 (and_131_out, EN_L2, Put_Dirty3, Valod_L2_Dirty);
  and and_132 (and_132_out, EN_L4, Put_Dirty3, Valod_L4_Dirty);
  and and_133 (and_133_out, EN_L5, Put_Dirty3, Valod_L5_Dirty);
  and and_134 (and_134_out, EN_L6, Put_Dirty3, Valod_L6_Dirty);
  and and_135 (and_135_out, EN_L7, Put_Dirty3, Valod_L7_Dirty);
  D_Flip_Flop d_ff_86 (.clk(CLK), .D(and_122_out), .Q(Dirty_L8_3), .reset(or_123_out));  // open: Qn, preset, en
  or or_123 (or_123_out, CLR_Dirty_L8, CLR);
  D_Flip_Flop d_ff_87 (.clk(CLK), .D(and_123_out), .Q(Dirty_L9_3), .reset(or_124_out));  // open: Qn, preset, en
  or or_124 (or_124_out, CLR_Dirty_L9, CLR);
  D_Flip_Flop d_ff_88 (.clk(CLK), .D(and_125_out), .Q(Dirty_L11_3), .reset(or_125_out));  // open: Qn, preset, en
  or or_125 (or_125_out, CLR_Dirty_L11, CLR);
  D_Flip_Flop d_ff_89 (.clk(CLK), .D(and_126_out), .Q(Dirty_L12_3), .reset(or_126_out));  // open: Qn, preset, en
  or or_126 (or_126_out, CLR_Dirty_L12, CLR);
  D_Flip_Flop d_ff_90 (.clk(CLK), .D(and_127_out), .Q(Dirty_L13_3), .reset(or_127_out));  // open: Qn, preset, en
  or or_127 (or_127_out, CLR_Dirty_L13, CLR);
  D_Flip_Flop d_ff_91 (.clk(CLK), .D(and_131_out), .Q(Dirty_L2_3), .reset(or_128_out));  // open: Qn, preset, en
  or or_128 (or_128_out, CLR_Dirty_L2, CLR);
  D_Flip_Flop d_ff_92 (.clk(CLK), .D(and_136_out), .Q(Dirty_L3_3), .reset(or_129_out));  // open: Qn, preset, en
  and and_136 (and_136_out, EN_L3, Put_Dirty3, Valod_L3_Dirty);
  or or_129 (or_129_out, CLR_Dirty_L3, CLR);
  D_Flip_Flop d_ff_93 (.clk(CLK), .D(and_132_out), .Q(Dirty_L4_3), .reset(or_130_out));  // open: Qn, preset, en
  or or_130 (or_130_out, CLR_Dirty_L4, CLR);
  D_Flip_Flop d_ff_94 (.clk(CLK), .D(and_133_out), .Q(Dirty_L5_3), .reset(or_131_out));  // open: Qn, preset, en
  or or_131 (or_131_out, CLR_Dirty_L5, CLR);
  D_Flip_Flop d_ff_95 (.clk(CLK), .D(and_134_out), .Q(Dirty_L6_3), .reset(or_132_out));  // open: Qn, preset, en
  or or_132 (or_132_out, CLR_Dirty_L6, CLR);
  D_Flip_Flop d_ff_96 (.clk(CLK), .D(and_135_out), .Q(Dirty_L7_3), .reset(or_133_out));  // open: Qn, preset, en
  or or_133 (or_133_out, CLR_Dirty_L7, CLR);
  and and_137 (and_137_out, EN_L0, ~Write_RAM);  // AND_Gate
  and and_138 (and_138_out, EN_L1, ~Write_RAM);  // AND_Gate
  and and_139 (and_139_out, EN_L10, ~Write_RAM);  // AND_Gate
  and and_140 (and_140_out, EN_L11, ~Write_RAM);  // AND_Gate
  and and_141 (and_141_out, EN_L12, ~Write_RAM);  // AND_Gate
  and and_142 (and_142_out, EN_L13, ~Write_RAM);  // AND_Gate
  and and_143 (and_143_out, EN_L14, ~Write_RAM);  // AND_Gate
  or or_134 (or_134_out, and_143_out, LoadFromRAML14);
  and and_144 (and_144_out, EN_L15, ~Write_RAM);  // AND_Gate
  or or_135 (or_135_out, CLR, and_159_out);
  or or_136 (or_136_out, and_137_out, LoadFromRAML0);
  D_Flip_Flop d_ff_97 (.clk(CLK), .D(or_137_out), .Q(LoadFromRAML1), .reset(or_138_out));  // open: Qn, preset, en
  or or_137 (or_137_out, and_138_out, LoadFromRAML1);
  or or_138 (or_138_out, CLR, and_145_out);
  and and_145 (and_145_out, EN_L1, ~TagEq, Write_RAM);  // AND_Gate
  and and_146 (and_146_out, EN_L2, ~Write_RAM);  // AND_Gate
  or or_139 (or_139_out, and_146_out, LoadFromRAML2);
  and and_147 (and_147_out, EN_L3, ~Write_RAM);  // AND_Gate
  and and_148 (and_148_out, EN_L4, ~Write_RAM);  // AND_Gate
  and and_149 (and_149_out, EN_L5, ~Write_RAM);  // AND_Gate
  and and_150 (and_150_out, EN_L6, ~Write_RAM);  // AND_Gate
  and and_151 (and_151_out, EN_L7, ~Write_RAM);  // AND_Gate
  or or_140 (or_140_out, and_151_out, LoadFromRAML7);
  and and_152 (and_152_out, EN_L8, ~Write_RAM);  // AND_Gate
  or or_141 (or_141_out, and_152_out, LoadFromRAML8);
  and and_153 (and_153_out, EN_L9, ~Write_RAM);  // AND_Gate
  or or_142 (or_142_out, and_153_out, LoadFromRAML9);
  or or_143 (or_143_out, and_139_out, LoadFromRAML10);
  or or_144 (or_144_out, CLR, and_167_out);
  D_Flip_Flop d_ff_98 (.clk(CLK), .D(or_145_out), .Q(LoadFromRAML11), .reset(or_146_out));  // open: Qn, preset, en
  or or_145 (or_145_out, and_140_out, LoadFromRAML11);
  or or_146 (or_146_out, CLR, and_154_out);
  and and_154 (and_154_out, EN_L11, ~TagEq, Write_RAM);  // AND_Gate
  D_Flip_Flop d_ff_99 (.clk(CLK), .D(or_147_out), .Q(LoadFromRAML12), .reset(or_148_out));  // open: Qn, preset, en
  or or_147 (or_147_out, and_141_out, LoadFromRAML12);
  or or_148 (or_148_out, CLR, and_155_out);
  and and_155 (and_155_out, EN_L12, ~TagEq, Write_RAM);  // AND_Gate
  D_Flip_Flop d_ff_100 (.clk(CLK), .D(or_149_out), .Q(LoadFromRAML13), .reset(or_150_out));  // open: Qn, preset, en
  or or_149 (or_149_out, and_142_out, LoadFromRAML13);
  or or_150 (or_150_out, CLR, and_156_out);
  and and_156 (and_156_out, EN_L13, ~TagEq, Write_RAM);  // AND_Gate
  D_Flip_Flop d_ff_101 (.clk(CLK), .D(or_134_out), .Q(LoadFromRAML14), .reset(or_151_out));  // open: Qn, preset, en
  or or_151 (or_151_out, CLR, and_157_out);
  and and_157 (and_157_out, EN_L14, ~TagEq, Write_RAM);  // AND_Gate
  D_Flip_Flop d_ff_102 (.clk(CLK), .D(or_152_out), .Q(LoadFromRAML15), .reset(or_153_out));  // open: Qn, preset, en
  or or_152 (or_152_out, and_144_out, LoadFromRAML15);
  or or_153 (or_153_out, CLR, and_158_out);
  and and_158 (and_158_out, EN_L15, ~TagEq, Write_RAM);  // AND_Gate
  D_Flip_Flop d_ff_103 (
    .clk(CLK), .D(or_136_out), .Q(LoadFromRAML0), .preset(undriven), .en(undriven), .reset(or_135_out));  // open: Qn
  and and_159 (and_159_out, EN_L0, ~TagEq, Write_RAM);  // AND_Gate
  D_Flip_Flop d_ff_104 (.clk(CLK), .D(or_139_out), .Q(LoadFromRAML2), .reset(or_154_out));  // open: Qn, preset, en
  or or_154 (or_154_out, CLR, and_160_out);
  and and_160 (and_160_out, EN_L2, ~TagEq, Write_RAM);  // AND_Gate
  D_Flip_Flop d_ff_105 (.clk(CLK), .D(or_155_out), .Q(LoadFromRAML3), .reset(or_156_out));  // open: Qn, preset, en
  or or_155 (or_155_out, and_147_out, LoadFromRAML3);
  or or_156 (or_156_out, CLR, and_161_out);
  and and_161 (and_161_out, EN_L3, ~TagEq, Write_RAM);  // AND_Gate
  D_Flip_Flop d_ff_106 (.clk(CLK), .D(or_157_out), .Q(LoadFromRAML4), .reset(or_158_out));  // open: Qn, preset, en
  or or_157 (or_157_out, and_148_out, LoadFromRAML4);
  or or_158 (or_158_out, CLR, and_162_out);
  and and_162 (and_162_out, EN_L4, ~TagEq, Write_RAM);  // AND_Gate
  D_Flip_Flop d_ff_107 (.clk(CLK), .D(or_159_out), .Q(LoadFromRAML5), .reset(or_160_out));  // open: Qn, preset, en
  or or_159 (or_159_out, and_149_out, LoadFromRAML5);
  or or_160 (or_160_out, CLR, and_163_out);
  and and_163 (and_163_out, EN_L5, ~TagEq, Write_RAM);  // AND_Gate
  or or_161 (or_161_out, and_150_out, LoadFromRAML6);
  or or_162 (or_162_out, CLR, and_168_out);
  D_Flip_Flop d_ff_108 (.clk(CLK), .D(or_140_out), .Q(LoadFromRAML7), .reset(or_163_out));  // open: Qn, preset, en
  or or_163 (or_163_out, CLR, and_164_out);
  and and_164 (and_164_out, EN_L7, ~TagEq, Write_RAM);  // AND_Gate
  D_Flip_Flop d_ff_109 (.clk(CLK), .D(or_141_out), .Q(LoadFromRAML8), .reset(or_164_out));  // open: Qn, preset, en
  or or_164 (or_164_out, CLR, and_165_out);
  and and_165 (and_165_out, EN_L8, ~TagEq, Write_RAM);  // AND_Gate
  D_Flip_Flop d_ff_110 (.clk(CLK), .D(or_142_out), .Q(LoadFromRAML9), .reset(or_165_out));  // open: Qn, preset, en
  or or_165 (or_165_out, CLR, and_166_out);
  and and_166 (and_166_out, EN_L9, ~TagEq, Write_RAM);  // AND_Gate
  D_Flip_Flop d_ff_111 (.clk(CLK), .D(or_143_out), .Q(LoadFromRAML10), .reset(or_144_out));  // open: Qn, preset, en
  and and_167 (and_167_out, EN_L10, ~TagEq, Write_RAM);  // AND_Gate
  D_Flip_Flop d_ff_112 (.clk(CLK), .D(or_161_out), .Q(LoadFromRAML6), .reset(or_162_out));  // open: Qn, preset, en
  and and_168 (and_168_out, EN_L6, ~TagEq, Write_RAM);  // AND_Gate
  Demultiplexer #(.select(4), .enable("false")) demultiplexer_2 (
    .out0(CLR_Dirty_L0), .out1(CLR_Dirty_L1), .out2(CLR_Dirty_L2), .out3(CLR_Dirty_L3), .out4(CLR_Dirty_L4),
    .out5(CLR_Dirty_L5), .out6(CLR_Dirty_L6), .out7(CLR_Dirty_L7), .out8(CLR_Dirty_L8), .out9(CLR_Dirty_L9),
    .out10(CLR_Dirty_L10), .out11(CLR_Dirty_L11), .out12(CLR_Dirty_L12), .out13(CLR_Dirty_L13),
    .out14(CLR_Dirty_L14), .out15(CLR_Dirty_L15), .in(Clear_Dirty), .sel(ADDRIN[7:4]));
  MUX16 mux16_1 (
    .in_1(L0_0), .in_2(L1_0), .in_3(L2_0), .in_4(L3_0), .in_5(L4_0), .in_6(L5_0), .in_8(L6_0), .in_9(L7_0),
    .in_10(L8_0), .in_11(L9_0), .in_12(L10_0), .in_13(L11_0), .in_14(L12_0), .in_15(L13_0), .in_16(L14_0),
    .in_17(L15_0), .out_18(O0), .in_7(ADDRIN[7:4]));
  MUX16 mux16_2 (
    .in_1(L0_1), .in_2(L1_1), .in_3(L2_1), .in_4(L3_1), .in_5(L4_1), .in_6(L5_1), .in_8(L6_1), .in_9(L7_1),
    .in_10(L8_1), .in_11(L9_1), .in_12(L10_1), .in_13(L11_1), .in_14(L12_1), .in_15(L13_1), .in_16(L14_1),
    .in_17(L15_1), .out_18(O1), .in_7(ADDRIN[7:4]));
  MUX16_12bits mux16_12bits_1 (
    .in_1(tagL0), .in_2(tagL1), .in_3(tagL2), .in_4(tagL3), .in_5(tagL4), .in_6(tagL5), .in_8(tagL6),
    .in_9(tagL7), .in_10(tagL8), .in_11(tagL9), .in_12(tagL10), .in_13(tagL11), .in_14(tagL12),
    .in_15(tagL13), .in_16(tagL14), .in_17(tagL15), .out_18(ADDR_out[15:4]), .in_7(ADDRIN[7:4]));
  Multiplexer #(.select(4), .enable("false")) multiplexer_1 (
    .in0(Valid_L0), .in1(Valid_L1), .in2(Valid_L2), .in3(Valid_L3), .in4(Valid_L4), .in5(Valid_L5),
    .in6(Valid_L6), .in7(Valid_L7), .in8(Valid_L8), .in9(Valid_L9), .in10(Valid_L10), .in11(Valid_L11),
    .in12(Valid_L12), .in13(Valid_L13), .in14(Valid_L14), .in15(Valid_L15), .out(Current_Valid),
    .sel(ADDRIN[7:4]));
  Multiplexer #(.select(4), .enable("false")) multiplexer_2 (
    .in0(LoadFromRAML0), .in1(LoadFromRAML1), .in2(LoadFromRAML2), .in3(LoadFromRAML3), .in4(LoadFromRAML4),
    .in5(LoadFromRAML5), .in6(LoadFromRAML6), .in7(LoadFromRAML7), .in8(LoadFromRAML8), .in9(LoadFromRAML9),
    .in10(LoadFromRAML10), .in11(LoadFromRAML11), .in12(LoadFromRAML12), .in13(LoadFromRAML13),
    .in14(LoadFromRAML14), .in15(LoadFromRAML15), .out(Current_LoadFromRAM), .sel(ADDRIN[7:4]));
  MUX16 mux16_3 (
    .in_1(L0_2), .in_2(L1_2), .in_3(L2_2), .in_4(L3_2), .in_5(L4_2), .in_6(L5_2), .in_8(L6_2), .in_9(L7_2),
    .in_10(L8_2), .in_11(L9_2), .in_12(L10_2), .in_13(L11_2), .in_14(L12_2), .in_15(L13_2), .in_16(L14_2),
    .in_17(L15_2), .out_18(O2), .in_7(ADDRIN[7:4]));
  MUX16 mux16_4 (
    .in_1(L0_3), .in_2(L1_3), .in_3(L2_3), .in_4(L3_3), .in_5(L4_3), .in_6(L5_3), .in_8(L6_3), .in_9(L7_3),
    .in_10(L8_3), .in_11(L9_3), .in_12(L10_3), .in_13(L11_3), .in_14(L12_3), .in_15(L13_3), .in_16(L14_3),
    .in_17(L15_3), .out_18(O3), .in_7(ADDRIN[7:4]));
  assign xor_1_out = ADDR_out[15:4] ^ ADDRIN[19:8];  // XOR_Gate xor_1, 12 bits wide
  Multiplexer #(.select(2), .enable("false")) multiplexer_3 (
    .in0(MASK_2[0]), .in1(MASK_2[1]), .in2(MASK_2[2]), .in3(MASK_2[3]), .out(multiplexer_3_out),
    .sel(ADDRIN[3:2]));
  and and_169 (and_169_out, multiplexer_3_out, Current_Dirty);
  MUX4 mux4_1 (.in_1(O0), .in_2(O1), .in_3(O2), .in_4(O3), .out_6(out_18), .in_5(ADDRIN[3:2]));
  or or_166 (or_166_out, xor_1_out[11], xor_1_out[10], xor_1_out[9], xor_1_out[8], xor_1_out[7], xor_1_out[6], xor_1_out[5], xor_1_out[4], xor_1_out[3], xor_1_out[2], xor_1_out[1], xor_1_out[0]);
  not not_1 (TagEq, or_166_out);
  or or_167 (or_167_out, Current_LoadFromRAM, and_169_out);
  or or_168 (Current_Dirty, MASK_2[0], MASK_2[1], MASK_2[2], MASK_2[3]);
  Multiplexer #(.select(4), .enable("false")) multiplexer_4 (
    .in0(Dirty_L0_2), .in1(Dirty_L1_2), .in2(Dirty_L2_2), .in3(Dirty_L3_2), .in4(Dirty_L4_2),
    .in5(Dirty_L5_2), .in6(Dirty_L6_2), .in7(Dirty_L7_2), .in8(Dirty_L8_2), .in9(Dirty_L9_2),
    .in10(Dirty_L10_2), .in11(Dirty_L11_2), .in12(Dirty_L12_2), .in13(Dirty_L13_2), .in14(Dirty_L14_2),
    .in15(Dirty_L15_2), .out(MASK_2[2]), .sel(ADDRIN[7:4]));
  or or_169 (or_169_out, EN, Clear_Dirty);
  or or_170 (or_170_out, or_167_out, ~Current_Dirty);  // OR_Gate
  and and_170 (Ready, or_170_out, TagEq, or_169_out, Current_Valid, ~d_ff_113_q);  // AND_Gate
  Multiplexer #(.select(4), .enable("false")) multiplexer_5 (
    .in0(Dirty_L0_0), .in1(Dirty_L1_0), .in2(Dirty_L2_0), .in3(Dirty_L3_0), .in4(Dirty_L4_0),
    .in5(Dirty_L5_0), .in6(Dirty_L6_0), .in7(Dirty_L7_0), .in8(Dirty_L8_0), .in9(Dirty_L9_0),
    .in10(Dirty_L10_0), .in11(Dirty_L11_0), .in12(Dirty_L12_0), .in13(Dirty_L13_0), .in14(Dirty_L14_0),
    .in15(Dirty_L15_0), .out(MASK_2[0]), .sel(ADDRIN[7:4]));
  and and_171 (Dirty, Current_Dirty, minus_R_W, ~TagEq);  // AND_Gate
  D_Flip_Flop d_ff_113 (.Q(d_ff_113_q), .preset(Dirty), .reset(Clear_Dirty));  // open: clk, D, Qn, en
  Multiplexer #(.select(4), .enable("false")) multiplexer_6 (
    .in0(Dirty_L0_1), .in1(Dirty_L1_1), .in2(Dirty_L2_1), .in3(Dirty_L3_1), .in4(Dirty_L4_1),
    .in5(Dirty_L5_1), .in6(Dirty_L6_1), .in7(Dirty_L7_1), .in8(Dirty_L8_1), .in9(Dirty_L9_1),
    .in10(Dirty_L10_1), .in11(Dirty_L11_1), .in12(Dirty_L12_1), .in13(Dirty_L13_1), .in14(Dirty_L14_1),
    .in15(Dirty_L15_1), .out(MASK_2[1]), .sel(ADDRIN[7:4]));
  Multiplexer #(.select(4), .enable("false")) multiplexer_7 (
    .in0(Dirty_L0_3), .in1(Dirty_L1_3), .in2(Dirty_L2_3), .in3(Dirty_L3_3), .in4(Dirty_L4_3),
    .in5(Dirty_L5_3), .in6(Dirty_L6_3), .in7(Dirty_L7_3), .in8(Dirty_L8_3), .in9(Dirty_L9_3),
    .in10(Dirty_L10_3), .in11(Dirty_L11_3), .in12(Dirty_L12_3), .in13(Dirty_L13_3), .in14(Dirty_L14_3),
    .in15(Dirty_L15_3), .out(MASK_2[3]), .sel(ADDRIN[7:4]));

  assign ADDR_out[3:0] = ADDRIN[7:4];

  // Other names for the same wires on the sheet: S_Lineas[3:0] = ADDRIN[7:4]; CLR_Dirty = Clear_Dirty;
  //   Current_Tag[11:0] = ADDR_out[15:4]; Mask_0 = MASK_2[0]; Mask_1 = MASK_2[1]; Mask_2_t = MASK_2[2];
  //   Mask_3 = MASK_2[3]; offset[1:0] = ADDRIN[3:2]; tag[11:0] = ADDRIN[19:8]; WriteRAM = Write_RAM
endmodule

module Cache_Intruc (
  input  minus_R_W,
  input  CLK,
  input  CLR,
  input  [31:0] I0,
  input  [31:0] I1,
  input  [31:0] I2,
  input  [31:0] I3,
  input  [19:0] ADDRIN,
  input  EN,
  output [31:0] out_10,
  output Ready
);

  wire Current_Valid, EN_L0, EN_L1, EN_L2, EN_L3, EN_L4, EN_L5, EN_L6, EN_L7, or_1_out, TagEq, Valid_L0,
       Valid_L1, Valid_L2, Valid_L3, Valid_L4, Valid_L5, Valid_L6, Valid_L7;
  wire [12:0] Current_Tag, tagL0, tagL1, tagL2, tagL3, tagL4, tagL5, tagL6, tagL7, xor_1_out;
  wire [31:0] L0_0, L0_1, L0_2, L0_3, L1_0, L1_1, L1_2, L1_3, L2_0, L2_1, L2_2, L2_3, L3_0, L3_1, L3_2, L3_3,
       L4_0, L4_1, L4_2, L4_3, L5_0, L5_1, L5_2, L5_3, L6_0, L6_1, L6_2, L6_3, L7_0, L7_1, L7_2, L7_3, O0,
       O1, O2, O3;

  Demultiplexer #(.select(3), .enable("false")) demultiplexer_1 (
    .out0(EN_L0), .out1(EN_L1), .out2(EN_L2), .out3(EN_L3), .out4(EN_L4), .out5(EN_L5), .out6(EN_L6),
    .out7(EN_L7), .in(minus_R_W), .sel(ADDRIN[6:4]));
  Register #(.width(32)) register_1 (.D(I0), .en(EN_L0), .Q(L0_0), .clk(CLK), .clr(CLR));
  Register #(.width(32)) register_2 (.D(I0), .en(EN_L1), .Q(L1_0), .clk(CLK), .clr(CLR));
  Register #(.width(32)) register_3 (.D(I0), .en(EN_L2), .Q(L2_0), .clk(CLK), .clr(CLR));
  Register #(.width(32)) register_4 (.D(I0), .en(EN_L3), .Q(L3_0), .clk(CLK), .clr(CLR));
  Register #(.width(32)) register_5 (.D(I0), .en(EN_L4), .Q(L4_0), .clk(CLK), .clr(CLR));
  Register #(.width(32)) register_6 (.D(I0), .en(EN_L5), .Q(L5_0), .clk(CLK), .clr(CLR));
  Register #(.width(32)) register_7 (.D(I0), .en(EN_L6), .Q(L6_0), .clk(CLK), .clr(CLR));
  Register #(.width(32)) register_8 (.D(I0), .en(EN_L7), .Q(L7_0), .clk(CLK), .clr(CLR));
  Register #(.width(32)) register_9 (.D(I1), .en(EN_L0), .Q(L0_1), .clk(CLK), .clr(CLR));
  Register #(.width(32)) register_10 (.D(I1), .en(EN_L1), .Q(L1_1), .clk(CLK), .clr(CLR));
  Register #(.width(32)) register_11 (.D(I1), .en(EN_L2), .Q(L2_1), .clk(CLK), .clr(CLR));
  Register #(.width(32)) register_12 (.D(I1), .en(EN_L3), .Q(L3_1), .clk(CLK), .clr(CLR));
  Register #(.width(32)) register_13 (.D(I1), .en(EN_L4), .Q(L4_1), .clk(CLK), .clr(CLR));
  Register #(.width(32)) register_14 (.D(I1), .en(EN_L5), .Q(L5_1), .clk(CLK), .clr(CLR));
  Register #(.width(32)) register_15 (.D(I1), .en(EN_L6), .Q(L6_1), .clk(CLK), .clr(CLR));
  Register #(.width(32)) register_16 (.D(I1), .en(EN_L7), .Q(L7_1), .clk(CLK), .clr(CLR));
  Register #(.width(32)) register_17 (.D(I2), .en(EN_L0), .Q(L0_2), .clk(CLK), .clr(CLR));
  Register #(.width(32)) register_18 (.D(I2), .en(EN_L1), .Q(L1_2), .clk(CLK), .clr(CLR));
  Register #(.width(32)) register_19 (.D(I2), .en(EN_L2), .Q(L2_2), .clk(CLK), .clr(CLR));
  Register #(.width(32)) register_20 (.D(I2), .en(EN_L3), .Q(L3_2), .clk(CLK), .clr(CLR));
  Register #(.width(32)) register_21 (.D(I2), .en(EN_L4), .Q(L4_2), .clk(CLK), .clr(CLR));
  Register #(.width(32)) register_22 (.D(I2), .en(EN_L5), .Q(L5_2), .clk(CLK), .clr(CLR));
  Register #(.width(32)) register_23 (.D(I2), .en(EN_L6), .Q(L6_2), .clk(CLK), .clr(CLR));
  Register #(.width(32)) register_24 (.D(I2), .en(EN_L7), .Q(L7_2), .clk(CLK), .clr(CLR));
  Register #(.width(32)) register_25 (.D(I3), .en(EN_L0), .Q(L0_3), .clk(CLK), .clr(CLR));
  Register #(.width(32)) register_26 (.D(I3), .en(EN_L1), .Q(L1_3), .clk(CLK), .clr(CLR));
  Register #(.width(32)) register_27 (.D(I3), .en(EN_L2), .Q(L2_3), .clk(CLK), .clr(CLR));
  Register #(.width(32)) register_28 (.D(I3), .en(EN_L3), .Q(L3_3), .clk(CLK), .clr(CLR));
  Register #(.width(32)) register_29 (.D(I3), .en(EN_L4), .Q(L4_3), .clk(CLK), .clr(CLR));
  Register #(.width(32)) register_30 (.D(I3), .en(EN_L5), .Q(L5_3), .clk(CLK), .clr(CLR));
  Register #(.width(32)) register_31 (.D(I3), .en(EN_L6), .Q(L6_3), .clk(CLK), .clr(CLR));
  Register #(.width(32)) register_32 (.D(I3), .en(EN_L7), .Q(L7_3), .clk(CLK), .clr(CLR));
  Register #(.width(13)) register_33 (.D(ADDRIN[19:7]), .en(EN_L0), .Q(tagL0), .clk(CLK), .clr(CLR));
  Register #(.width(13)) register_34 (.D(ADDRIN[19:7]), .en(EN_L1), .Q(tagL1), .clk(CLK), .clr(CLR));
  Register #(.width(13)) register_35 (.D(ADDRIN[19:7]), .en(EN_L2), .Q(tagL2), .clk(CLK), .clr(CLR));
  Register #(.width(13)) register_36 (.D(ADDRIN[19:7]), .en(EN_L3), .Q(tagL3), .clk(CLK), .clr(CLR));
  Register #(.width(13)) register_37 (.D(ADDRIN[19:7]), .en(EN_L4), .Q(tagL4), .clk(CLK), .clr(CLR));
  Register #(.width(13)) register_38 (.D(ADDRIN[19:7]), .en(EN_L5), .Q(tagL5), .clk(CLK), .clr(CLR));
  Register #(.width(13)) register_39 (.D(ADDRIN[19:7]), .en(EN_L6), .Q(tagL6), .clk(CLK), .clr(CLR));
  Register #(.width(13)) register_40 (.D(ADDRIN[19:7]), .en(EN_L7), .Q(tagL7), .clk(CLK), .clr(CLR));
  D_Flip_Flop d_ff_1 (.clk(CLK), .Q(Valid_L0), .preset(EN_L0), .reset(CLR));  // open: D, Qn, en
  D_Flip_Flop d_ff_2 (.clk(CLK), .Q(Valid_L1), .preset(EN_L1), .reset(CLR));  // open: D, Qn, en
  D_Flip_Flop d_ff_3 (.clk(CLK), .Q(Valid_L2), .preset(EN_L2), .reset(CLR));  // open: D, Qn, en
  D_Flip_Flop d_ff_4 (.clk(CLK), .Q(Valid_L3), .preset(EN_L3), .reset(CLR));  // open: D, Qn, en
  D_Flip_Flop d_ff_5 (.clk(CLK), .Q(Valid_L4), .preset(EN_L4), .reset(CLR));  // open: D, Qn, en
  D_Flip_Flop d_ff_6 (.clk(CLK), .Q(Valid_L5), .preset(EN_L5), .reset(CLR));  // open: D, Qn, en
  D_Flip_Flop d_ff_7 (.clk(CLK), .Q(Valid_L6), .preset(EN_L6), .reset(CLR));  // open: D, Qn, en
  D_Flip_Flop d_ff_8 (.clk(CLK), .Q(Valid_L7), .preset(EN_L7), .reset(CLR));  // open: D, Qn, en
  Multiplexer #(.select(3), .enable("false")) multiplexer_1 (
    .in0(Valid_L0), .in1(Valid_L1), .in2(Valid_L2), .in3(Valid_L3), .in4(Valid_L4), .in5(Valid_L5),
    .in6(Valid_L6), .in7(Valid_L7), .out(Current_Valid), .sel(ADDRIN[6:4]));
  MUX8 mux8_1 (
    .in_1(L0_0), .in_2(L1_0), .in_3(L2_0), .in_4(L3_0), .in_5(L4_0), .in_7(L5_0), .in_8(L6_0), .in_9(L7_0),
    .out_10(O0), .in_6(ADDRIN[6:4]));
  MUX8 mux8_2 (
    .in_1(L0_1), .in_2(L1_1), .in_3(L2_1), .in_4(L3_1), .in_5(L4_1), .in_7(L5_1), .in_8(L6_1), .in_9(L7_1),
    .out_10(O1), .in_6(ADDRIN[6:4]));
  MUX8_13bits mux8_13bits_1 (
    .in_1(tagL0), .in_2(tagL1), .in_3(tagL2), .in_4(tagL3), .in_5(tagL4), .in_7(tagL5), .in_8(tagL6),
    .in_9(tagL7), .out_10(Current_Tag), .in_6(ADDRIN[6:4]));
  MUX8 mux8_3 (
    .in_1(L0_2), .in_2(L1_2), .in_3(L2_2), .in_4(L3_2), .in_5(L4_2), .in_7(L5_2), .in_8(L6_2), .in_9(L7_2),
    .out_10(O2), .in_6(ADDRIN[6:4]));
  MUX8 mux8_4 (
    .in_1(L0_3), .in_2(L1_3), .in_3(L2_3), .in_4(L3_3), .in_5(L4_3), .in_7(L5_3), .in_8(L6_3), .in_9(L7_3),
    .out_10(O3), .in_6(ADDRIN[6:4]));
  assign xor_1_out = Current_Tag ^ ADDRIN[19:7];  // XOR_Gate xor_1, 13 bits wide
  or or_1 (or_1_out, xor_1_out[12], xor_1_out[11], xor_1_out[10], xor_1_out[9], xor_1_out[8], xor_1_out[7], xor_1_out[6], xor_1_out[5], xor_1_out[4], xor_1_out[3], xor_1_out[2], xor_1_out[1], xor_1_out[0]);
  not not_1 (TagEq, or_1_out);
  MUX4 mux4_1 (.in_1(O0), .in_2(O1), .in_3(O2), .in_4(O3), .out_6(out_10), .in_5(ADDRIN[3:2]));
  and and_1 (Ready, TagEq, EN, Current_Valid);

  // Other names for the same wires on the sheet: offset[1:0] = ADDRIN[3:2]; S_Lineas[2:0] = ADDRIN[6:4];
  //   tag[12:0] = ADDRIN[19:7]
endmodule

module MUX8_13bits (
  input  [12:0] in_1,
  input  [12:0] in_2,
  input  [12:0] in_3,
  input  [12:0] in_4,
  input  [12:0] in_5,
  input  [2:0] in_6,
  input  [12:0] in_7,
  input  [12:0] in_8,
  input  [12:0] in_9,
  output [12:0] out_10
);

  wire a0, a1, a2, a3, a4, a5, a6, a7;

  Transistor #(.\type ("n"), .gate("br"), .width(13)) transistor_1 (.in(in_1), .out(out_10), .gate(a0));
  Transistor #(.\type ("n"), .gate("br"), .width(13)) transistor_2 (.in(in_2), .out(out_10), .gate(a1));
  Transistor #(.\type ("n"), .gate("br"), .width(13)) transistor_3 (.in(in_3), .out(out_10), .gate(a2));
  Transistor #(.\type ("n"), .gate("br"), .width(13)) transistor_4 (.in(in_4), .out(out_10), .gate(a3));
  Transistor #(.\type ("n"), .gate("br"), .width(13)) transistor_5 (.in(in_5), .out(out_10), .gate(a4));
  Transistor #(.\type ("n"), .gate("br"), .width(13)) transistor_6 (.in(in_7), .out(out_10), .gate(a5));
  Transistor #(.\type ("n"), .gate("br"), .width(13)) transistor_7 (.in(in_8), .out(out_10), .gate(a6));
  Transistor #(.\type ("n"), .gate("br"), .width(13)) transistor_8 (.in(in_9), .out(out_10), .gate(a7));
  Decoder #(.select(3), .enable("false")) decoder_1 (
    .out0(a0), .out1(a1), .out2(a2), .out3(a3), .out4(a4), .out5(a5), .out6(a6), .out7(a7), .sel(in_6));

  // Other names for the same wires on the sheet: out[12:0] = out_10
endmodule

module Config_Only_Cache (
);

  wire CLK, CLR, ENMR, or_1_out, ReadyMR;
  wire [3:0] Mask_Cache;
  wire [19:0] ADDR_READ;
  wire [31:0] RAM, RAM_OUTPUT_0, RAM_OUTPUT_1, RAM_OUTPUT_2, RAM_OUTPUT_3;

  or or_1 (or_1_out, ENMR, ReadyMR);
  Cache cache_1 (
    .minus_R_W(ReadyMR), .CLK(CLK), .CLR(CLR), .I0(RAM_OUTPUT_0), .I1(RAM_OUTPUT_1), .I2(RAM_OUTPUT_2),
    .I3(RAM_OUTPUT_3), .ADDRIN(ADDR_READ), .Mask(Mask_Cache), .out_18(RAM), .EN(or_1_out));  // open: O0, O1, O2, O3, Ready, Dirty, Clear_Dirty, ADDR_out, MASK_2, Write_RAM, Input_To_RAM
endmodule

module Cache_Data (
  input  minus_R_W,
  input  CLK,
  input  CLR,
  input  [31:0] I0,
  input  [31:0] I1,
  input  [31:0] I2,
  input  [31:0] I3,
  input  [19:0] ADDRIN,
  input  [3:0] Mask,
  input  EN,
  input  Clear_Dirty,
  output [31:0] O0,
  output [31:0] O1,
  output [31:0] O2,
  output [31:0] O3,
  output [31:0] out_16,
  output [19:0] ADDR_out,
  output Dirty,
  output Ready
);

  wire and_1_out, and_2_out, and_3_out, and_4_out, and_5_out, and_6_out, and_7_out, and_8_out, and_9_out,
       and_10_out, and_11_out, and_12_out, and_13_out, and_14_out, and_15_out, and_16_out, and_17_out,
       and_18_out, and_19_out, and_20_out, and_21_out, and_22_out, and_23_out, and_24_out, and_25_out,
       and_26_out, and_27_out, and_28_out, and_29_out, and_30_out, and_31_out, and_32_out, and_33_out,
       and_34_out, and_35_out, and_36_out, and_37_out, and_38_out, and_39_out, and_40_out, CLR_Dirty_L0,
       CLR_Dirty_L1, CLR_Dirty_L2, CLR_Dirty_L3, CLR_Dirty_L4, CLR_Dirty_L5, CLR_Dirty_L6, CLR_Dirty_L7,
       Current_Dirty, Current_Valid, d_ff_9_q, d_ff_10_q, d_ff_11_q, d_ff_12_q, d_ff_13_q, d_ff_14_q,
       d_ff_15_q, d_ff_16_q, Dirty_L0, Dirty_L1, Dirty_L2, Dirty_L3, Dirty_L4, Dirty_L5, Dirty_L6, Dirty_L7,
       EN_L0, EN_L1, EN_L2, EN_L3, EN_L4, EN_L5, EN_L6, EN_L7, or_1_out, or_2_out, or_3_out, or_4_out,
       or_5_out, or_6_out, or_7_out, or_8_out, or_9_out, TagEq, Valid_L0, Valid_L1, Valid_L2, Valid_L3,
       Valid_L4, Valid_L5, Valid_L6, Valid_L7;
  wire [12:0] Current_Tag, tagL0, tagL1, tagL2, tagL3, tagL4, tagL5, tagL6, tagL7, xor_1_out;
  wire [31:0] L0_0, L0_1, L0_2, L0_3, L1_0, L1_1, L1_2, L1_3, L2_0, L2_1, L2_2, L2_3, L3_0, L3_1, L3_2, L3_3,
       L4_0, L4_1, L4_2, L4_3, L5_0, L5_1, L5_2, L5_3, L6_0, L6_1, L6_2, L6_3, L7_0, L7_1, L7_2, L7_3;

  Demultiplexer #(.select(3), .enable("false")) demultiplexer_1 (
    .out0(EN_L0), .out1(EN_L1), .out2(EN_L2), .out3(EN_L3), .out4(EN_L4), .out5(EN_L5), .out6(EN_L6),
    .out7(EN_L7), .in(minus_R_W), .sel(ADDRIN[6:4]));
  and and_1 (and_1_out, EN_L0, Mask[0]);
  and and_2 (and_2_out, EN_L1, Mask[0]);
  and and_3 (and_3_out, EN_L2, Mask[0]);
  and and_4 (and_4_out, EN_L3, Mask[0]);
  and and_5 (and_5_out, EN_L4, Mask[0]);
  and and_6 (and_6_out, EN_L5, Mask[0]);
  and and_7 (and_7_out, EN_L6, Mask[0]);
  and and_8 (and_8_out, EN_L7, Mask[0]);
  Register #(.width(32)) register_1 (.D(I0), .en(and_1_out), .Q(L0_0), .clk(CLK), .clr(CLR));
  Register #(.width(32)) register_2 (.D(I0), .en(and_2_out), .Q(L1_0), .clk(CLK), .clr(CLR));
  Register #(.width(32)) register_3 (.D(I0), .en(and_3_out), .Q(L2_0), .clk(CLK), .clr(CLR));
  Register #(.width(32)) register_4 (.D(I0), .en(and_4_out), .Q(L3_0), .clk(CLK), .clr(CLR));
  Register #(.width(32)) register_5 (.D(I0), .en(and_5_out), .Q(L4_0), .clk(CLK), .clr(CLR));
  Register #(.width(32)) register_6 (.D(I0), .en(and_6_out), .Q(L5_0), .clk(CLK), .clr(CLR));
  Register #(.width(32)) register_7 (.D(I0), .en(and_7_out), .Q(L6_0), .clk(CLK), .clr(CLR));
  Register #(.width(32)) register_8 (.D(I0), .en(and_8_out), .Q(L7_0), .clk(CLK), .clr(CLR));
  and and_9 (and_9_out, EN_L0, Mask[1]);
  and and_10 (and_10_out, EN_L1, Mask[1]);
  and and_11 (and_11_out, EN_L2, Mask[1]);
  and and_12 (and_12_out, EN_L3, Mask[1]);
  and and_13 (and_13_out, EN_L4, Mask[1]);
  and and_14 (and_14_out, EN_L5, Mask[1]);
  and and_15 (and_15_out, EN_L6, Mask[1]);
  and and_16 (and_16_out, EN_L7, Mask[1]);
  Register #(.width(32)) register_9 (.D(I1), .en(and_9_out), .Q(L0_1), .clk(CLK), .clr(CLR));
  Register #(.width(32)) register_10 (.D(I1), .en(and_10_out), .Q(L1_1), .clk(CLK), .clr(CLR));
  Register #(.width(32)) register_11 (.D(I1), .en(and_11_out), .Q(L2_1), .clk(CLK), .clr(CLR));
  Register #(.width(32)) register_12 (.D(I1), .en(and_12_out), .Q(L3_1), .clk(CLK), .clr(CLR));
  Register #(.width(32)) register_13 (.D(I1), .en(and_13_out), .Q(L4_1), .clk(CLK), .clr(CLR));
  Register #(.width(32)) register_14 (.D(I1), .en(and_14_out), .Q(L5_1), .clk(CLK), .clr(CLR));
  Register #(.width(32)) register_15 (.D(I1), .en(and_15_out), .Q(L6_1), .clk(CLK), .clr(CLR));
  Register #(.width(32)) register_16 (.D(I1), .en(and_16_out), .Q(L7_1), .clk(CLK), .clr(CLR));
  and and_17 (and_17_out, EN_L0, Mask[2]);
  and and_18 (and_18_out, EN_L1, Mask[2]);
  and and_19 (and_19_out, EN_L2, Mask[2]);
  and and_20 (and_20_out, EN_L3, Mask[2]);
  and and_21 (and_21_out, EN_L4, Mask[2]);
  and and_22 (and_22_out, EN_L5, Mask[2]);
  and and_23 (and_23_out, EN_L6, Mask[2]);
  and and_24 (and_24_out, EN_L7, Mask[2]);
  Register #(.width(32)) register_17 (.D(I2), .en(and_17_out), .Q(L0_2), .clk(CLK), .clr(CLR));
  Register #(.width(32)) register_18 (.D(I2), .en(and_18_out), .Q(L1_2), .clk(CLK), .clr(CLR));
  Register #(.width(32)) register_19 (.D(I2), .en(and_19_out), .Q(L2_2), .clk(CLK), .clr(CLR));
  Register #(.width(32)) register_20 (.D(I2), .en(and_20_out), .Q(L3_2), .clk(CLK), .clr(CLR));
  Register #(.width(32)) register_21 (.D(I2), .en(and_21_out), .Q(L4_2), .clk(CLK), .clr(CLR));
  Register #(.width(32)) register_22 (.D(I2), .en(and_22_out), .Q(L5_2), .clk(CLK), .clr(CLR));
  Register #(.width(32)) register_23 (.D(I2), .en(and_23_out), .Q(L6_2), .clk(CLK), .clr(CLR));
  Register #(.width(32)) register_24 (.D(I2), .en(and_24_out), .Q(L7_2), .clk(CLK), .clr(CLR));
  Register #(.width(32)) register_25 (.D(I3), .en(and_25_out), .Q(L0_3), .clk(CLK), .clr(CLR));
  and and_25 (and_25_out, EN_L0, Mask[3]);
  Register #(.width(32)) register_26 (.D(I3), .en(and_26_out), .Q(L1_3), .clk(CLK), .clr(CLR));
  and and_26 (and_26_out, EN_L1, Mask[3]);
  Register #(.width(32)) register_27 (.D(I3), .en(and_27_out), .Q(L2_3), .clk(CLK), .clr(CLR));
  and and_27 (and_27_out, EN_L2, Mask[3]);
  Register #(.width(32)) register_28 (.D(I3), .en(and_28_out), .Q(L3_3), .clk(CLK), .clr(CLR));
  and and_28 (and_28_out, EN_L3, Mask[3]);
  Register #(.width(32)) register_29 (.D(I3), .en(and_29_out), .Q(L4_3), .clk(CLK), .clr(CLR));
  and and_29 (and_29_out, EN_L4, Mask[3]);
  Register #(.width(32)) register_30 (.D(I3), .en(and_30_out), .Q(L5_3), .clk(CLK), .clr(CLR));
  and and_30 (and_30_out, EN_L5, Mask[3]);
  Register #(.width(32)) register_31 (.D(I3), .en(and_31_out), .Q(L6_3), .clk(CLK), .clr(CLR));
  and and_31 (and_31_out, EN_L6, Mask[3]);
  Register #(.width(32)) register_32 (.D(I3), .en(and_32_out), .Q(L7_3), .clk(CLK), .clr(CLR));
  and and_32 (and_32_out, EN_L7, Mask[3]);
  Register #(.width(13)) register_33 (.D(ADDRIN[19:7]), .en(EN_L0), .Q(tagL0), .clk(CLK), .clr(CLR));
  Register #(.width(13)) register_34 (.D(ADDRIN[19:7]), .en(EN_L1), .Q(tagL1), .clk(CLK), .clr(CLR));
  Register #(.width(13)) register_35 (.D(ADDRIN[19:7]), .en(EN_L2), .Q(tagL2), .clk(CLK), .clr(CLR));
  Register #(.width(13)) register_36 (.D(ADDRIN[19:7]), .en(EN_L3), .Q(tagL3), .clk(CLK), .clr(CLR));
  Register #(.width(13)) register_37 (.D(ADDRIN[19:7]), .en(EN_L4), .Q(tagL4), .clk(CLK), .clr(CLR));
  Register #(.width(13)) register_38 (.D(ADDRIN[19:7]), .en(EN_L5), .Q(tagL5), .clk(CLK), .clr(CLR));
  Register #(.width(13)) register_39 (.D(ADDRIN[19:7]), .en(EN_L6), .Q(tagL6), .clk(CLK), .clr(CLR));
  Register #(.width(13)) register_40 (.D(ADDRIN[19:7]), .en(EN_L7), .Q(tagL7), .clk(CLK), .clr(CLR));
  D_Flip_Flop d_ff_1 (.clk(CLK), .Q(Valid_L0), .preset(EN_L0), .reset(CLR));  // open: D, Qn, en
  D_Flip_Flop d_ff_2 (.clk(CLK), .Q(Valid_L1), .preset(EN_L1), .reset(CLR));  // open: D, Qn, en
  D_Flip_Flop d_ff_3 (.clk(CLK), .Q(Valid_L2), .preset(EN_L2), .reset(CLR));  // open: D, Qn, en
  D_Flip_Flop d_ff_4 (.clk(CLK), .Q(Valid_L3), .preset(EN_L3), .reset(CLR));  // open: D, Qn, en
  D_Flip_Flop d_ff_5 (.clk(CLK), .Q(Valid_L4), .preset(EN_L4), .reset(CLR));  // open: D, Qn, en
  D_Flip_Flop d_ff_6 (.clk(CLK), .Q(Valid_L5), .preset(EN_L5), .reset(CLR));  // open: D, Qn, en
  D_Flip_Flop d_ff_7 (.clk(CLK), .Q(Valid_L6), .preset(EN_L6), .reset(CLR));  // open: D, Qn, en
  D_Flip_Flop d_ff_8 (.clk(CLK), .Q(Valid_L7), .preset(EN_L7), .reset(CLR));  // open: D, Qn, en
  D_Flip_Flop d_ff_9 (.clk(CLK), .D(Valid_L0), .Q(d_ff_9_q), .reset(CLR));  // open: Qn, preset, en
  D_Flip_Flop d_ff_10 (.clk(CLK), .D(Valid_L1), .Q(d_ff_10_q), .reset(CLR));  // open: Qn, preset, en
  D_Flip_Flop d_ff_11 (.clk(CLK), .D(Valid_L2), .Q(d_ff_11_q), .reset(CLR));  // open: Qn, preset, en
  D_Flip_Flop d_ff_12 (.clk(CLK), .D(Valid_L3), .Q(d_ff_12_q), .reset(CLR));  // open: Qn, preset, en
  D_Flip_Flop d_ff_13 (.clk(CLK), .D(Valid_L4), .Q(d_ff_13_q), .reset(CLR));  // open: Qn, preset, en
  D_Flip_Flop d_ff_14 (.clk(CLK), .D(Valid_L5), .Q(d_ff_14_q), .reset(CLR));  // open: Qn, preset, en
  D_Flip_Flop d_ff_15 (.clk(CLK), .D(Valid_L6), .Q(d_ff_15_q), .reset(CLR));  // open: Qn, preset, en
  D_Flip_Flop d_ff_16 (.clk(CLK), .D(Valid_L7), .Q(d_ff_16_q), .reset(CLR));  // open: Qn, preset, en
  and and_33 (and_33_out, EN_L0, TagEq, d_ff_9_q);
  and and_34 (and_34_out, EN_L1, TagEq, d_ff_10_q);
  and and_35 (and_35_out, EN_L2, TagEq, d_ff_11_q);
  and and_36 (and_36_out, EN_L3, TagEq, d_ff_12_q);
  and and_37 (and_37_out, EN_L4, TagEq, d_ff_13_q);
  and and_38 (and_38_out, EN_L5, TagEq, d_ff_14_q);
  and and_39 (and_39_out, EN_L6, TagEq, d_ff_15_q);
  and and_40 (and_40_out, EN_L7, TagEq, d_ff_16_q);
  D_Flip_Flop d_ff_17 (.clk(CLK), .D(and_33_out), .Q(Dirty_L0), .reset(or_1_out));  // open: Qn, preset, en
  or or_1 (or_1_out, CLR_Dirty_L0, CLR);
  D_Flip_Flop d_ff_18 (.clk(CLK), .D(and_34_out), .Q(Dirty_L1), .reset(or_2_out));  // open: Qn, preset, en
  or or_2 (or_2_out, CLR_Dirty_L1, CLR);
  D_Flip_Flop d_ff_19 (.clk(CLK), .D(and_35_out), .Q(Dirty_L2), .reset(or_3_out));  // open: Qn, preset, en
  or or_3 (or_3_out, CLR_Dirty_L2, CLR);
  D_Flip_Flop d_ff_20 (.clk(CLK), .D(and_36_out), .Q(Dirty_L3), .reset(or_4_out));  // open: Qn, preset, en
  or or_4 (or_4_out, CLR_Dirty_L3, CLR);
  D_Flip_Flop d_ff_21 (.clk(CLK), .D(and_37_out), .Q(Dirty_L4), .reset(or_5_out));  // open: Qn, preset, en
  or or_5 (or_5_out, CLR_Dirty_L4, CLR);
  D_Flip_Flop d_ff_22 (.clk(CLK), .D(and_38_out), .Q(Dirty_L5), .reset(or_6_out));  // open: Qn, preset, en
  or or_6 (or_6_out, CLR_Dirty_L5, CLR);
  D_Flip_Flop d_ff_23 (.clk(CLK), .D(and_39_out), .Q(Dirty_L6), .reset(or_7_out));  // open: Qn, preset, en
  or or_7 (or_7_out, CLR_Dirty_L6, CLR);
  D_Flip_Flop d_ff_24 (.clk(CLK), .D(and_40_out), .Q(Dirty_L7), .reset(or_8_out));  // open: Qn, preset, en
  or or_8 (or_8_out, CLR_Dirty_L7, CLR);
  Demultiplexer #(.select(3), .enable("false")) demultiplexer_2 (
    .out0(CLR_Dirty_L0), .out1(CLR_Dirty_L1), .out2(CLR_Dirty_L2), .out3(CLR_Dirty_L3), .out4(CLR_Dirty_L4),
    .out5(CLR_Dirty_L5), .out6(CLR_Dirty_L6), .out7(CLR_Dirty_L7), .in(Clear_Dirty), .sel(ADDRIN[6:4]));
  MUX8 mux8_1 (
    .in_1(L0_0), .in_2(L1_0), .in_3(L2_0), .in_4(L3_0), .in_5(L4_0), .in_7(L5_0), .in_8(L6_0), .in_9(L7_0),
    .out_10(O0), .in_6(ADDRIN[6:4]));
  MUX8 mux8_2 (
    .in_1(L0_1), .in_2(L1_1), .in_3(L2_1), .in_4(L3_1), .in_5(L4_1), .in_7(L5_1), .in_8(L6_1), .in_9(L7_1),
    .out_10(O1), .in_6(ADDRIN[6:4]));
  Multiplexer #(.select(3), .enable("false")) multiplexer_1 (
    .in0(Valid_L0), .in1(Valid_L1), .in2(Valid_L2), .in3(Valid_L3), .in4(Valid_L4), .in5(Valid_L5),
    .in6(Valid_L6), .in7(Valid_L7), .out(Current_Valid), .sel(ADDRIN[6:4]));
  Multiplexer #(.select(3), .enable("false")) multiplexer_2 (
    .in0(Dirty_L0), .in1(Dirty_L1), .in2(Dirty_L2), .in3(Dirty_L3), .in4(Dirty_L4), .in5(Dirty_L5),
    .in6(Dirty_L6), .in7(Dirty_L7), .out(Dirty), .sel(ADDRIN[6:4]));
  MUX8 mux8_3 (
    .in_1(L0_2), .in_2(L1_2), .in_3(L2_2), .in_4(L3_2), .in_5(L4_2), .in_7(L5_2), .in_8(L6_2), .in_9(L7_2),
    .out_10(O2), .in_6(ADDRIN[6:4]));
  MUX8 mux8_4 (
    .in_1(L0_3), .in_2(L1_3), .in_3(L2_3), .in_4(L3_3), .in_5(L4_3), .in_7(L5_3), .in_8(L6_3), .in_9(L7_3),
    .out_10(O3), .in_6(ADDRIN[6:4]));
  MUX8_13bits mux8_13bits_1 (
    .in_1(tagL0), .in_2(tagL1), .in_3(tagL2), .in_4(tagL3), .in_5(tagL4), .in_7(tagL5), .in_8(tagL6),
    .in_9(tagL7), .out_10(Current_Tag), .in_6(ADDRIN[6:4]));
  and and_41 (Ready, ~Current_Dirty, TagEq, EN, Current_Valid);  // AND_Gate
  assign xor_1_out = Current_Tag ^ ADDRIN[19:7];  // XOR_Gate xor_1, 13 bits wide
  or or_9 (or_9_out, xor_1_out[12], xor_1_out[11], xor_1_out[10], xor_1_out[9], xor_1_out[8], xor_1_out[7], xor_1_out[6], xor_1_out[5], xor_1_out[4], xor_1_out[3], xor_1_out[2], xor_1_out[1], xor_1_out[0]);
  not not_1 (TagEq, or_9_out);
  MUX4 mux4_1 (.in_1(O0), .in_2(O1), .in_3(O2), .in_4(O3), .out_6(out_16), .in_5(ADDRIN[3:2]));

  assign ADDR_out = ADDRIN;

  // Other names for the same wires on the sheet: CLR_Dirty = Clear_Dirty; offset[1:0] = ADDRIN[3:2];
  //   S_Lineas[2:0] = ADDRIN[6:4]; tag[12:0] = ADDRIN[19:7]
endmodule

module Config_Cache_Data (
);

  wire and_1_out, CLK, CLR, ENMR, InCache, or_1_out, ReadyMR;
  wire [1:0] S_AddrMR;
  wire [19:0] ADDR_READ;
  wire [31:0] RAM, RAM_OUTPUT_0, RAM_OUTPUT_1, RAM_OUTPUT_2, RAM_OUTPUT_3;

  and and_1 (and_1_out, ENMR, ~S_AddrMR[0], ~S_AddrMR[1]);  // AND_Gate
  or or_1 (or_1_out, and_1_out, ReadyMR);
  Cache_Intruc cache_intruc_1 (
    .EN(or_1_out), .out_10(RAM), .minus_R_W(ReadyMR), .CLK(CLK), .CLR(CLR), .I0(RAM_OUTPUT_0),
    .I1(RAM_OUTPUT_1), .I2(RAM_OUTPUT_2), .I3(RAM_OUTPUT_3), .ADDRIN(ADDR_READ), .Ready(InCache));
endmodule

module Memory_Writer_Cache (
  input  CLK,
  input  EN,
  input  Clear,
  input  [3:0] WT,
  input  [31:0] I0,
  input  [31:0] I1,
  input  [31:0] I2,
  input  [31:0] I3,
  input  [15:0] ADDR,
  input  [3:0] Mask,
  output CS,
  output minus_R_W,
  output [15:0] ADDR_2,
  output READY,
  output [3:0] Mask_2,
  output [31:0] Data0,
  output [31:0] Data1,
  output [31:0] Data2,
  output [31:0] Data3
);

  wire CLEAR_t, demultiplexer_1_out0, demultiplexer_1_out1, demultiplexer_2_out0, EQ, or_1_out, or_2_out,
       or_3_out;
  wire [3:0] counter_1_q, xor_1_out;

  or or_1 (or_1_out, demultiplexer_1_out0, READY);
  Counter #(.width(4), .max('hf)) counter_1 (
    .count(CS), .Q(counter_1_q), .clk(CLK), .clr(CLEAR_t));  // open: load, D, carry
  D_Flip_Flop START (.clk(CLK), .D(or_1_out), .Q(CLEAR_t), .preset(Clear));  // open: Qn, en, reset
  assign xor_1_out = counter_1_q ^ WT;  // XOR_Gate xor_1, 4 bits wide
  Demultiplexer #(.enable("false")) demultiplexer_1 (
    .out0(demultiplexer_1_out0), .out1(demultiplexer_1_out1), .in(CLEAR_t), .sel(EN));
  or or_2 (or_2_out, demultiplexer_2_out0, demultiplexer_1_out1);
  D_Flip_Flop COUNT (.clk(CLK), .D(or_2_out), .Q(CS), .reset(Clear));  // open: Qn, preset, en
  not not_1 (EQ, or_3_out);
  or or_3 (or_3_out, xor_1_out[0], xor_1_out[1], xor_1_out[2], xor_1_out[3]);
  Demultiplexer #(.enable("false")) demultiplexer_2 (.out0(demultiplexer_2_out0), .out1(READY), .in(CS), .sel(EQ));

  assign ADDR_2 = ADDR;
  assign Data0 = I0;
  assign Data1 = I1;
  assign Data2 = I2;
  assign Data3 = I3;
  assign Mask_2 = Mask;
  assign minus_R_W = CS;

  // Other names for the same wires on the sheet: CLEARSTR = Clear; INC = CS
endmodule

module Config_MW_sin_Cache (
);

  wire CLK, CLR, CS2, ENMW, ReadyMW, RW, S_AddrMW, S_InputMW;
  wire [3:0] RAM_MASK, Write_Time;
  wire [15:0] RAM_A_MW;
  wire [19:0] lw_sw_Value, mux2_20bits_1_out_4, SP_ADDR;
  wire [31:0] A, B, mux2_1_out_4, RAM_INPUT_0, RAM_INPUT_1, RAM_INPUT_2, RAM_INPUT_3;

  MUX2_20bits mux2_20bits_1 (.in_1(SP_ADDR), .in_2(lw_sw_Value), .out_4(mux2_20bits_1_out_4), .in_3(S_AddrMW));
  MUX2 mux2_1 (.in_1(A), .in_2(B), .out_4(mux2_1_out_4), .in_3(S_InputMW));
  MemoryWriter memorywriter_1 (
    .ADDR_2(RAM_A_MW), .READY(ReadyMW), .Mask(RAM_MASK), .Input(mux2_1_out_4), .ADDR(mux2_20bits_1_out_4),
    .WT(Write_Time), .CS(CS2), .minus_R_W(RW), .CLK(CLK), .EN(ENMW), .Data0(RAM_INPUT_0),
    .Data1(RAM_INPUT_1), .Data2(RAM_INPUT_2), .Data3(RAM_INPUT_3), .Clear(CLR));
endmodule

module Config_MW_Cache (
);

  wire CLK, CLR, CS2, ENMW, memory_writer_cache_1_p3, memory_writer_cache_1_p6, memory_writer_cache_1_p7,
       memory_writer_cache_1_p9, memory_writer_cache_1_p11, ReadyMW, RW, S_AddrMW, S_InputMW;
  wire [3:0] RAM_MASK, Write_Time;
  wire [15:0] RAM_A_MW;
  wire [19:0] lw_sw_Value, mux2_20bits_1_out_4, SP_ADDR;
  wire [31:0] A, B, RAM_INPUT_0, RAM_INPUT_1, RAM_INPUT_2, RAM_INPUT_3;

  MUX2_20bits mux2_20bits_1 (.in_1(SP_ADDR), .in_2(lw_sw_Value), .out_4(mux2_20bits_1_out_4), .in_3(S_AddrMW));
  // Memory_Writer_Cache memory_writer_cache_1: pin names not known; wires that end beside it: CLR, Write_Time, memory_writer_cache_1_p3, ENMW, CLK, memory_writer_cache_1_p6, memory_writer_cache_1_p7, RAM_INPUT_0, memory_writer_cache_1_p9, RAM_INPUT_1, memory_writer_cache_1_p11, RAM_INPUT_2, RAM_INPUT_3, CS2, RAM_A_MW, RAM_MASK, RW, ReadyMW
  MUX2 mux2_1 (.in_1(A), .in_2(B), .in_3(S_InputMW));  // open: out_4

  // Notes on the sheet:
  //   CAMBIAR
endmodule

module ResolverRAMValue (
  input  [31:0] in_1,
  output [31:0] out_2
);


  assign out_2 = {in_1[7:0], in_1[15:8], in_1[23:16], in_1[31:24]};
endmodule
