// Logisim project s-mips(En tallapiedra).circ as structural Verilog: 27 circuits, main circuit S-MIPS Board
module S_MIPS_Board (
  output halt
);

  wire button_1_out, CLK, CS, d_ff_1_q, R_W, Reset_out, RST, TTY_EN;
  wire [2:0] KDB;
  wire [3:0] Mask, ram_1_read_time, ram_1_write_time;
  wire [6:0] KDB_DATA, TTY_DATA;
  wire [15:0] Addr;
  wire [31:0] ram_1_data_out_0, ram_1_data_out_1, ram_1_data_out_2, ram_1_data_out_3, s_mips_1_ram_in_0,
       s_mips_1_ram_in_1, s_mips_1_ram_in_2, s_mips_1_ram_in_3;

  TTY #(.rows(25), .cols(80)) tty_1 (.data(TTY_DATA), .clk(CLK), .we(TTY_EN), .clr(RST));
  RAM ram_1 (
    .Address(Addr), .Data_Out_0(ram_1_data_out_0), .Data_Out_1(ram_1_data_out_1),
    .Data_Out_2(ram_1_data_out_2), .Data_Out_3(ram_1_data_out_3), .Data_In_0(s_mips_1_ram_in_0),
    .Data_In_1(s_mips_1_ram_in_1), .Data_In_2(s_mips_1_ram_in_2), .Data_In_3(s_mips_1_ram_in_3), .Mask(Mask),
    .nRead_Write(R_W), .Chip_Select(CS), .Read_Time(ram_1_read_time), .Reset(button_1_out),
    .Write_Time(ram_1_write_time), .in_2(CLK));
  Button button_1 (.out(button_1_out));
  Keyboard #(.buflen(64)) keyboard_1 (.clk(CLK), .re(KDB[0]), .avail(KDB[2]), .data(KDB_DATA));  // open: clr
  S_MIPS s_mips_1 (
    .Kbd_Enable(KDB[0]), .Address(Addr), .Kbd_Clear(KDB[1]), .Kbd_Available(KDB[2]),
    .RAM_In_0(s_mips_1_ram_in_0), .Kbd_ASCII_Data(KDB_DATA), .RAM_In_1(s_mips_1_ram_in_1),
    .TTY_Enable(TTY_EN), .RAM_In_2(s_mips_1_ram_in_2), .RAM_In_3(s_mips_1_ram_in_3),
    .TTY_ASCII_Data(TTY_DATA), .Reset(RST), .RAM_Out_0(ram_1_data_out_0), .Clock(CLK),
    .RAM_Out_1(ram_1_data_out_1), .Stop(halt), .RAM_Out_2(ram_1_data_out_2), .RAM_Out_3(ram_1_data_out_3),
    .Mask(Mask), .Read_Time(ram_1_read_time), .Write_Time(ram_1_write_time), .nRead_Write(R_W),
    .Chip_Select(CS));
  D_Flip_Flop d_ff_1 (.clk(CLK), .D(1'b1), .Q(d_ff_1_q), .reset(Reset_out));  // open: Qn, preset, en
  Button Reset (.out(Reset_out));
  D_Flip_Flop d_ff_2 (.clk(CLK), .D(d_ff_1_q), .Qn(RST), .reset(Reset_out));  // open: Q, preset, en
  Clock clock_1 (.out(CLK));

  // Notes on the sheet:
  //   NO MODIFICAR
  //   Keyboard
endmodule

module RAM (
  input  [15:0] Address,
  input  in_2,
  input  [31:0] Data_In_0,
  input  [31:0] Data_In_1,
  input  [31:0] Data_In_2,
  input  [31:0] Data_In_3,
  input  [3:0] Mask,
  input  nRead_Write,
  input  Chip_Select,
  input  Reset,
  output [31:0] Data_Out_0,
  output [31:0] Data_Out_1,
  output [31:0] Data_Out_2,
  output [31:0] Data_Out_3,
  output [3:0] Read_Time,
  output [3:0] Write_Time
);

  wire and_2_out, and_3_out, and_4_out, and_5_out, and_6_out, and_7_out, and_8_out, and_9_out, Changed,
       comparator_2_eq, comparator_3_eq, comparator_4_eq, comparator_5_eq, comparator_6_eq, Count,
       demultiplexer_3_out0, Idle, Idle_q, Load, Load0, Load1, nand_1_out, or_1_out, or_2_out, or_3_out,
       or_4_out, or_5_out, or_6_out, or_7_out, or_8_out, or_9_out, or_10_out, Proc_q, Update_Mem, Zero_Time;
  wire [3:0] counter_1_q, multiplexer_1_out, subtractor_1_out;
  wire [31:0] register_1_q, register_2_q, register_3_q, register_4_q, register_5_q;

  // Probe on 4'b0011
  // Probe on 4'b0101
  Multiplexer #(.width(4), .enable("false")) multiplexer_1 (
    .in0(4'b0011), .in1(4'b0101), .out(multiplexer_1_out), .sel(nRead_Write));
  or or_1 (or_1_out, Idle, Update_Mem);
  or or_2 (or_2_out, ~Chip_Select, Reset);  // OR_Gate
  Subtractor #(.width(4)) subtractor_1 (.a(multiplexer_1_out), .b(4'b0010), .out(subtractor_1_out));  // open: bin, bout
  D_Flip_Flop u_Idle (.clk(in_2), .D(or_1_out), .Q(Idle_q), .preset(or_2_out));  // open: Qn, en, reset
  Demultiplexer #(.enable("false")) demultiplexer_1 (.out0(Idle), .out1(Load0), .in(Idle_q), .sel(Changed));
  // Probe on counter_1_q
  Counter #(.width(4), .max('hf)) counter_1 (
    .load(Load), .D(subtractor_1_out), .count(Count), .Q(counter_1_q), .clk(in_2), .clr(or_3_out));  // open: carry
  or or_3 (or_3_out, ~Chip_Select, Reset);  // OR_Gate
  Comparator #(.width(4), .mode("unsigned")) comparator_1 (
    .a(4'b0000), .b(counter_1_q), .eq(Zero_Time));  // open: gt, lt
  or or_4 (or_4_out, Count, Load0, Load1);
  Register #(.width(32)) register_1 (.D(Data_In_0), .en(Chip_Select), .Q(register_1_q), .clk(in_2), .clr(or_5_out));
  or or_5 (or_5_out, ~Chip_Select, Reset);  // OR_Gate
  Register #(.width(32)) register_2 (.D(Data_In_1), .en(Chip_Select), .Q(register_2_q), .clk(in_2), .clr(or_6_out));
  or or_6 (or_6_out, ~Chip_Select, Reset);  // OR_Gate
  Register #(.width(32)) register_3 (.D(Data_In_2), .en(Chip_Select), .Q(register_3_q), .clk(in_2), .clr(or_7_out));
  or or_7 (or_7_out, ~Chip_Select, Reset);  // OR_Gate
  Register #(.width(32)) register_4 (.D(Data_In_3), .en(Chip_Select), .Q(register_4_q), .clk(in_2), .clr(or_8_out));
  or or_8 (or_8_out, ~Chip_Select, Reset);  // OR_Gate
  Register #(.width(32)) register_5 (
    .D({{11{1'b1}}, nRead_Write, Mask, Address}), .en(Chip_Select), .Q(register_5_q), .clk(in_2),
    .clr(or_9_out));
  or or_9 (or_9_out, ~Chip_Select, Reset);  // OR_Gate
  D_Flip_Flop Proc (.clk(in_2), .D(or_4_out), .Q(Proc_q), .reset(or_10_out));  // open: Qn, preset, en
  or or_10 (or_10_out, ~Chip_Select, Reset);  // OR_Gate
  Demultiplexer #(.enable("false")) demultiplexer_2 (
    .out0(Count), .out1(Update_Mem), .in(demultiplexer_3_out0), .sel(Zero_Time));
  Demultiplexer #(.enable("false")) demultiplexer_3 (
    .out0(demultiplexer_3_out0), .out1(Load1), .in(Proc_q), .sel(Changed));
  Comparator #(.width(32)) comparator_2 (.a(register_1_q), .b(Data_In_0), .eq(comparator_2_eq));  // open: gt, lt
  Comparator #(.width(32)) comparator_3 (.a(register_2_q), .b(Data_In_1), .eq(comparator_3_eq));  // open: gt, lt
  Comparator #(.width(32)) comparator_4 (.a(register_3_q), .b(Data_In_2), .eq(comparator_4_eq));  // open: gt, lt
  Comparator #(.width(32)) comparator_5 (.a(register_4_q), .b(Data_In_3), .eq(comparator_5_eq));  // open: gt, lt
  Comparator #(.width(32)) comparator_6 (
    .a(register_5_q), .b({{11{1'b1}}, nRead_Write, Mask, Address}), .eq(comparator_6_eq));  // open: gt, lt
  nand nand_1 (nand_1_out, comparator_6_eq, comparator_2_eq, comparator_3_eq, comparator_4_eq, comparator_5_eq);
  and and_1 (Changed, nand_1_out, Chip_Select);
  or or_11 (Load, Count, Load1, Load0);
  and and_2 (and_2_out, Mask[0], Update_Mem, nRead_Write);
  and and_3 (and_3_out, Mask[1], Update_Mem, nRead_Write);
  and and_4 (and_4_out, Mask[2], Update_Mem, nRead_Write);
  and and_5 (and_5_out, Mask[3], Update_Mem, nRead_Write);
  RAM_part #(.addrWidth(16), .dataWidth(32), .bus("separate")) ram_1 (
    .addr(Address), .din(Data_In_0), .data(Data_Out_0), .str(and_2_out), .sel(Chip_Select), .clk(in_2),
    .ld(and_6_out), .clr(Reset));
  and and_6 (and_6_out, ~nRead_Write, Idle);  // AND_Gate
  RAM_part #(.addrWidth(16), .dataWidth(32), .bus("separate")) ram_2 (
    .addr(Address), .din(Data_In_1), .data(Data_Out_1), .str(and_3_out), .sel(Chip_Select), .clk(in_2),
    .ld(and_7_out), .clr(Reset));
  and and_7 (and_7_out, ~nRead_Write, Idle);  // AND_Gate
  RAM_part #(.addrWidth(16), .dataWidth(32), .bus("separate")) ram_3 (
    .addr(Address), .din(Data_In_2), .data(Data_Out_2), .str(and_4_out), .sel(Chip_Select), .clk(in_2),
    .ld(and_8_out), .clr(Reset));
  and and_8 (and_8_out, ~nRead_Write, Idle);  // AND_Gate
  RAM_part #(.addrWidth(16), .dataWidth(32), .bus("separate")) ram_4 (
    .addr(Address), .din(Data_In_3), .data(Data_Out_3), .str(and_5_out), .sel(Chip_Select), .clk(in_2),
    .ld(and_9_out), .clr(Reset));
  and and_9 (and_9_out, ~nRead_Write, Idle);  // AND_Gate

  assign Read_Time = 4'b0011;
  assign Write_Time = 4'b0101;

  // Other names for the same wires on the sheet: M0 = Mask[0]; M1 = Mask[1]; M2 = Mask[2]; M3 = Mask[3];
  //   RW = nRead_Write; CLK = in_2; CLR = Reset; CS = Chip_Select; Load2 = Count

  // Notes on the sheet:
  //   NO MODIFICAR
  //   excepto quizás los valores RT y WT
  //   BANK0
  //   BANK1
  //   BANK2
  //   BANK3
endmodule

module S_MIPS (
  input  Kbd_Available,
  input  [6:0] Kbd_ASCII_Data,
  input  [31:0] RAM_Out_0,
  input  [31:0] RAM_Out_1,
  input  Reset,
  input  [31:0] RAM_Out_2,
  input  Clock,
  input  [31:0] RAM_Out_3,
  input  [3:0] Read_Time,
  input  [3:0] Write_Time,
  output Kbd_Enable,
  output [15:0] Address,
  output Kbd_Clear,
  output TTY_Enable,
  output [6:0] TTY_ASCII_Data,
  output Stop,
  output [31:0] RAM_In_0,
  output [31:0] RAM_In_1,
  output [31:0] RAM_In_2,
  output [31:0] RAM_In_3,
  output [3:0] Mask,
  output nRead_Write,
  output Chip_Select
);

  wire _2OP, Execute, ID_Ld, L_R31, or_1_out, R_W, Read_En_1, Read_En_2, Read_Flag, ReadSel, Ready, tunnel,
       tunnel_t, tunnel_t_t, Write_En, Write_Flag;
  wire [1:0] PP;
  wire [2:0] FS, IS, J_Type, Mult_Div;
  wire [4:0] R_Add_A, R_Add_B, W_Add;
  wire [15:0] K;
  wire [25:0] J_Dest;
  wire [31:0] ALU, B, Hi, Inst, Lo, mux1bit_1_out_4, mux1bit_2_out_4, mux1bit_3_out_4, R31, RAM, Read_Add,
       register_1_q, Write_Add, Write_Data;
  wire [31:7] A;

  MUX1bit mux1bit_1 (.out_4(mux1bit_1_out_4), .in_2(Read_Add), .in_3(Inst), .in_1(ReadSel));
  MUX1bit mux1bit_2 (.out_4(mux1bit_2_out_4), .in_2(mux1bit_1_out_4), .in_3(Write_Add), .in_1(Write_En));
  MUX1bit mux1bit_3 (.out_4(mux1bit_3_out_4), .in_2(RAM), .in_3({32{1'b0}}), .in_1(Execute));
  Register #(.width(32)) register_1 (.D(mux1bit_3_out_4), .en(ID_Ld), .Q(register_1_q), .clk(Clock));  // open: clr
  or or_1 (or_1_out, Read_En_1, Read_En_2);
  CACHE cache_1 (
    .Clock(Clock), .in_5(mux1bit_2_out_4), .RAM_0(RAM_Out_0), .RAM_1(RAM_Out_1), .RAM_2(RAM_Out_2),
    .RAM_3(RAM_Out_3), .Read_Time(Read_Time), .Reader_Enable(or_1_out), .Write_Time(Write_Time),
    .Writer_Enable(Write_En), .ReadOutput(RAM), .ReadReady(Read_Flag), .RAM_0_2(RAM_In_0),
    .RAM_1_2(RAM_In_1), .RAM_2_2(RAM_In_2), .RAM_3_2(RAM_In_3), .R_W(nRead_Write), .WriteReady(Write_Flag),
    .Mask(Mask), .C_S(Chip_Select), .RAM_A(Address), .Write_Data(Write_Data), .Clear(Reset));
  ID id_1 (
    .Instruction(register_1_q), .R_W_Selector(R_W), .Write_Address(W_Add), .Read_Address_A(R_Add_A),
    .Read_Address_B(R_Add_B), .JUMP_TYPE(J_Type), .FS(FS), .Constant_Input(K), .Jump_Destination(J_Dest),
    ._2OP(_2OP), .MULTDIV_SELECT(Mult_Div), .IS(IS), .Halt(Stop), .Tty(TTY_Enable), .in_4(Clock),
    .Pop_Push(PP), .out_10(Read_Add), .out_11(Write_Add), .out_16(Write_Data), .RF_31(R31), .ALU(ALU),
    .RF_A({A, TTY_ASCII_Data}), .RF_B(B), .in_6(Read_Flag), .in_7(Write_Flag), .Read_Enable(Read_En_1),
    .Write_Enable(Write_En), .PC_Enable(Ready), .in_5(Reset), .KBD_Enable(Kbd_Enable), .L_R31(L_R31));
  ControlUnit controlunit_1 (
    .Reader_Flag(Read_Flag), .Instruction_Flag(Ready), .Clock(Clock), .Reader_Enable(Read_En_2),
    .ID_Load(ID_Ld), .Execute(Execute), .Read_Selector(ReadSel), .Clear(Reset), .Halt(Stop));
  PC pc_1 (
    .Next_Instruction_Address(Inst), .Jump_Destination_Input(J_Dest), .Register_Input({A, TTY_ASCII_Data}),
    .Constant_Input(K), .Enable(Execute), .Instruction_Selector(J_Type), ._32bits(tunnel),
    ._32bits_2(tunnel_t), ._32bits_3(tunnel_t_t), .Clock(Clock), .Clear(Reset));
  ALU alu_1 (
    .out_9(ALU), .RF_Out_A({A, TTY_ASCII_Data}), .RF_Out_B(B), .Constant(K), .Function_Selector(FS),
    ._2nd_Operand_Selector(_2OP), .out_10(Hi), .out_11(Lo), .Clock(Clock), .out_12(tunnel),
    .out_13(tunnel_t), .out_14(tunnel_t_t), .Mult_Div_Selector(Mult_Div), .Clear(Reset));
  RF rf_1 (
    .out_16({A, TTY_ASCII_Data}), .out_18(B), .Input_Selector(IS), .R_W_Selector(R_W), .Memory_Input(RAM),
    .Write_Address(W_Add), .ALU_Input(ALU), .Read_Address_A(R_Add_A), .Hi_Register_Input(Hi),
    .Read_Address_B(R_Add_B), .Lo_Register_Input(Lo), .Clock(Clock), .SP_Selector(PP), .out_17(R31),
    .Clear(Reset), .Kbd_Data(Kbd_ASCII_Data), .Keyboard_Avail(Kbd_Available), .Load_R31(L_R31));

  // Other names for the same wires on the sheet: A[6:0] = TTY_ASCII_Data; TTY_DATA[6:0] = TTY_ASCII_Data; CLK = Clock;
  //   CLR = Reset; CS = Chip_Select; KBD_AVAIL = Kbd_Available; KBD_CLR = Kbd_Clear; KBD_DATA[6:0] = Kbd_ASCII_Data;
  //   RAM_A[15:0] = Address; RAM_INPUT_0[31:0] = RAM_In_0; RAM_INPUT_1[31:0] = RAM_In_1; RAM_INPUT_2[31:0] = RAM_In_2;
  //   RAM_INPUT_3[31:0] = RAM_In_3; RAM_MASK[3:0] = Mask; RAM_OUTPUT_0[31:0] = RAM_Out_0;
  //   RAM_OUTPUT_1[31:0] = RAM_Out_1; RAM_OUTPUT_2[31:0] = RAM_Out_2; RAM_OUTPUT_3[31:0] = RAM_Out_3;
  //   RW = nRead_Write

  // Notes on the sheet:
  //   RAM ADDRESS
  //   DATA FROM RAM
  //   DATA TO RAM
  //   DATA WRITE MASK
  //   RAM TIMING
  //   RAM CONTROL
  //   KEYBOARD
  //   TTY
  //   SEQUENCING
endmodule

module ALU (
  input  [2:0] Function_Selector,
  input  _2nd_Operand_Selector,
  input  [2:0] Mult_Div_Selector,
  input  [31:0] RF_Out_A,
  input  [31:0] RF_Out_B,
  input  [15:0] Constant,
  input  Clock,
  input  Clear,
  output [31:0] out_9,
  output [31:0] out_10,
  output [31:0] out_11,
  output out_12,
  output out_13,
  output out_14
);

  wire [0:0] _32_U;
  wire [31:0] _2ndOp, ADD, AND, DIV_Div, DIV_Rem, MUL_High, MUL_Low, mux2bits_1_out_6, mux2bits_2_out_6, NOR,
       OR, SUB, U_DIV_Div, U_DIV_Rem, U_MUL_High, U_MUL_Low, XOR;

  unsignedMult unsignedmult_1 (.out_3(U_MUL_Low), .out_4(U_MUL_High), .in_1(RF_Out_A), .in_2(_2ndOp));
  MUX2bits mux2bits_1 (
    .out_6(mux2bits_1_out_6), .in_2(MUL_High), .in_3(U_MUL_High), .in_4(DIV_Rem), .in_5(U_DIV_Rem),
    .in_1(Mult_Div_Selector[1:0]));
  Adder #(.width(32)) adder_1 (.a(RF_Out_A), .b(_2ndOp), .out(ADD), .cin(1'b0));  // open: cout
  Divider #(.width(32)) divider_1 (.a(RF_Out_A), .b(_2ndOp), .out(U_DIV_Div), .upper({32{1'b0}}), .rem(U_DIV_Rem));
  Comparator #(.width(32)) comparator_1 (.a(RF_Out_A), .b(_2ndOp), .gt(out_14), .eq(out_13), .lt(out_12));
  Register #(.width(32)) Hi (.D(mux2bits_1_out_6), .en(Mult_Div_Selector[2]), .Q(out_10), .clk(Clock), .clr(Clear));
  Subtractor #(.width(32)) subtractor_1 (.a(RF_Out_A), .b(_2ndOp), .out(SUB), .bin(1'b0));  // open: bout
  Multiplier #(.width(32)) multiplier_1 (.a(RF_Out_A), .b(_2ndOp), .out(MUL_Low), .cin({32{1'b0}}), .cout(MUL_High));
  signedDivider signeddivider_1 (.out_3(DIV_Div), .out_4(DIV_Rem), .in_1(RF_Out_A), .in_2(_2ndOp));
  Comparator #(.width(32), .mode("unsigned")) comparator_2 (.a(RF_Out_A), .b(_2ndOp), .lt(_32_U[0]));  // open: gt, eq
  MUX2bits mux2bits_2 (
    .out_6(mux2bits_2_out_6), .in_2(MUL_Low), .in_3(U_MUL_Low), .in_4(DIV_Div), .in_5(U_DIV_Div),
    .in_1(Mult_Div_Selector[1:0]));
  Register #(.width(32)) Lo (.D(mux2bits_2_out_6), .en(Mult_Div_Selector[2]), .Q(out_11), .clk(Clock), .clr(Clear));
  assign AND = RF_Out_A & _2ndOp;  // AND_Gate and_1, 32 bits wide
  assign OR = RF_Out_A | _2ndOp;  // OR_Gate or_1, 32 bits wide
  assign NOR = ~(RF_Out_A | _2ndOp);  // NOR_Gate nor_1, 32 bits wide
  assign XOR = RF_Out_A ^ _2ndOp;  // XOR_Gate xor_1, 32 bits wide
  MUX3bits_Transistors mux3bits_transistors_1 (
    .out_10(out_9), .in_1(ADD), .in_9(Function_Selector), .in_2(SUB), .in_3({{31{1'b0}}, out_12}),
    .in_4({{31{1'b0}}, _32_U[0]}), .in_5(AND), .in_6(OR), .in_7(NOR), .in_8(XOR));
  MUX1bit mux1bit_1 (
    .out_4(_2ndOp), .in_2(RF_Out_B), .in_3({{17{Constant[15]}}, Constant[14:0]}), .in_1(_2nd_Operand_Selector));

  // Other names for the same wires on the sheet: _2ndOpSel = _2nd_Operand_Selector; _32[0] = out_12; Flag = out_12;
  //   Flag_U = _32_U[0]; CLR = Clear; Flag_t = out_13; Flag_t_t = out_14; Hi[31:0] = out_10;
  //   K[31:0] = {{17{Constant[15]}}, Constant[14:0]}; Lo[31:0] = out_11; En = Mult_Div_Selector[2];
  //   Mult_Div[2:0] = Mult_Div_Selector; Mult_Div_Sel[1:0] = Mult_Div_Selector[1:0]; OpSel[2:0] = Function_Selector;
  //   Output[31:0] = out_9; RF_A[31:0] = RF_Out_A; RF_B[31:0] = RF_Out_B

  // Notes on the sheet:
  //   ADD
  //   U-MUL
  //   U-DIV
  //   COMP SIGNED
  //   ARITHMETIC OPS
  //   DETERMINES WETHER IS MUL/DIV OR NOT
  //   SUB
  //   MUL
  //   DIV
  //   SPECIAL MUL/DIV REGISTERS
  //   INPUTS
  //   COMP UNSIGNED
  //   0
  //   1
  //   bit1
  //   bit0
  //   signed
  //   mult
  //   -------------------------------------------
  //   div
  //   unsigned
  //   LOGIC OPS
  //   AND
  //   OR
  //   bit2
  //   disabled
  //   enable
  //   NOR
  //   XOR
  //   SELECTING THE OUTPUT
  //   OUTPUTS
  //   SECOND OPERAND SELECTOR
endmodule

module unsignedMult (
  input  [31:0] in_1,
  input  [31:0] in_2,
  output [31:0] out_3,
  output [31:0] out_4
);

  wire C;
  wire [31:0] _4XResHigh, Add, mux2bits_1_out_6;
  wire [31:2] _4XResLow;
  wire [31:30] ResHigh;

  MUX2bits mux2bits_1 (
    .out_6(mux2bits_1_out_6), .in_2({32{1'b0}}), .in_3(in_2), .in_4(in_1), .in_5(Add),
    .in_1({in_2[0], in_1[0]}));
  Adder #(.width(32)) adder_1 (.a({in_1[31:1], 1'b0}), .b({in_2[31:1], 1'b0}), .out(Add), .cin(1'b1));  // open: cout
  Multiplier #(.width(32)) multiplier_1 (
    .a({1'b0, in_1[31:1]}), .b({1'b0, in_2[31:1]}), .out({_4XResHigh[1:0], _4XResLow}),
    .cout({ResHigh, _4XResHigh[31:2]}));  // open: cin
  Adder #(.width(32)) adder_2 (.a(mux2bits_1_out_6), .b({_4XResLow, 2'b00}), .out(out_3), .cout(C));  // open: cin
  Adder #(.width(32)) adder_3 (.a({32{1'b0}}), .b(_4XResHigh), .out(out_4), .cin(C));  // open: cout

  // Other names for the same wires on the sheet: ResLow[31:0] = {_4XResHigh[1:0], _4XResLow};
  //   ResHigh[29:0] = _4XResHigh[31:2]; A[31:0] = in_1; Add_A[31:1] = in_1[31:1]; Op_A[30:0] = in_1[31:1];
  //   Up_A[30:0] = in_1[31:1]; Add_B[31:1] = in_2[31:1]; B[31:0] = in_2; Op_B[30:0] = in_2[31:1];
  //   Up_B[30:0] = in_2[31:1]; CarrySel[1:0] = {in_2[0], in_1[0]}; Last_A = in_1[0]; Last_B = in_2[0];
  //   RetHigh[31:0] = out_4; RetLow[31:0] = out_3

  // Notes on the sheet:
  //   INPUTS
  //   REDUCING TO 31 BITS
  //   BUILDING RESULT
  //   OUTPUTS
  //   BUILDING AMOUNT TO ADD
  //   BUILDING CARRY SELECTOR
  //   MULTIPLYING
endmodule

module signedDivider (
  input  [31:0] in_1,
  input  [31:0] in_2,
  output [31:0] out_3,
  output [31:0] out_4
);

  wire [31:0] minus_A, minus_B, minus_U_Rem, minus_U_Rem_B, minus_U_Res, minus_U_Res_1, mux1bit_1_out_4,
       mux1bit_2_out_4, U_Rem, U_Rem_B, U_Res, U_Res_1;

  Negator #(.width(32)) negator_1 (.in(in_1), .out(minus_A));
  Negator #(.width(32)) negator_2 (.in(in_2), .out(minus_B));
  Negator #(.width(32)) negator_3 (.in(U_Res), .out(minus_U_Res));
  MUX2bits mux2bits_1 (
    .out_6(out_3), .in_2(U_Res), .in_3(minus_U_Res), .in_4(minus_U_Res_1), .in_5(U_Res_1),
    .in_1({in_2[31], in_1[31]}));
  Adder #(.width(32)) adder_1 (.a(32'h1), .b(U_Res), .out(U_Res_1));  // open: cin, cout
  Adder #(.width(32)) adder_2 (.a({32{1'b1}}), .b(minus_U_Res), .out(minus_U_Res_1));  // open: cin, cout
  MUX1bit mux1bit_1 (.out_4(mux1bit_1_out_4), .in_2(in_1), .in_3(minus_A), .in_1(in_1[31]));
  MUX1bit mux1bit_2 (.out_4(mux1bit_2_out_4), .in_2(in_2), .in_3(minus_B), .in_1(in_2[31]));
  Adder #(.width(32)) adder_3 (.a(minus_B), .b(minus_U_Rem), .out(minus_U_Rem_B));  // open: cin, cout
  Adder #(.width(32)) adder_4 (.a(in_2), .b(U_Rem), .out(U_Rem_B));  // open: cin, cout
  Divider #(.width(32)) divider_1 (.a(mux1bit_1_out_4), .b(mux1bit_2_out_4), .out(U_Res), .rem(U_Rem));  // open: upper
  Negator #(.width(32)) negator_4 (.in(U_Rem), .out(minus_U_Rem));
  MUX2bits mux2bits_2 (
    .out_6(out_4), .in_2(U_Rem), .in_3(U_Rem), .in_4(U_Rem_B), .in_5(minus_U_Rem_B),
    .in_1({in_2[31], in_1[31]}));

  // Other names for the same wires on the sheet: A[31:0] = in_1; Last_A = in_1[31]; B[31:0] = in_2; Last_B = in_2[31];
  //   Rem[31:0] = out_4; Res[31:0] = out_3

  // Notes on the sheet:
  //   INPUTS
  //   SAVING SIGN BIT
  //   GETTING THE 2's COMPLEMENT OF THE INPUTS
  //   BULDING THE RESULT
  //   OUTPUTS
  //   DIVIDING THE MODULES
  //   BUILDING THE REMAINDER
endmodule

module RF (
  input  [6:0] Kbd_Data,
  input  [31:0] Memory_Input,
  input  [31:0] ALU_Input,
  input  [31:0] Hi_Register_Input,
  input  [31:0] Lo_Register_Input,
  input  [2:0] Input_Selector,
  input  R_W_Selector,
  input  [4:0] Write_Address,
  input  [4:0] Read_Address_A,
  input  [4:0] Read_Address_B,
  input  Clock,
  input  [1:0] SP_Selector,
  input  Load_R31,
  input  Clear,
  input  Keyboard_Avail,
  output [31:0] out_16,
  output [31:0] out_17,
  output [31:0] out_18
);

  wire and_1_out, L0, L1, L2, L3, L4, L5, L6, L7, L8, L9, L10, L11, L12, L13, L14, L15, L16, L17, L18, L19,
       L20, L21, L22, L23, L24, L25, L26, L27, L28, L29, L30, L31, or_1_out;
  wire [31:0] In, minus_4, mux1bit_2_out_4, mux2bits_1_out_6, mux3bits_transistors_1_out_10, plus_4, R0, R1,
       R2, R3, R4, R5, R6, R7, R8, R9, R10, R11, R12, R13, R14, R15, R16, R17, R18, R19, R20, R21, R22, R23,
       R24, R25, R26, R27, R28, R29, R30, Rnd;

  Random #(.width(32)) random_1 (.clk(Clock), .out(Rnd));  // open: next, clr
  Register #(.width(32), .trigger("falling")) u_R0 (.D(In), .en(L0), .Q(R0), .clk(Clock), .clr(1'b1));
  Register #(.width(32)) u_R8 (.D(In), .en(L8), .Q(R8), .clk(Clock), .clr(Clear));
  Register #(.width(32)) u_R16 (.D(In), .en(L16), .Q(R16), .clk(Clock), .clr(Clear));
  Register #(.width(32)) u_R24 (.D(In), .en(L24), .Q(R24), .clk(Clock), .clr(Clear));
  MUX3bits_Transistors mux3bits_transistors_1 (
    .out_10(mux3bits_transistors_1_out_10), .in_1(ALU_Input), .in_9(Input_Selector),
    .in_2(Hi_Register_Input), .in_3(Lo_Register_Input), .in_4(Memory_Input), .in_5(Rnd),
    .in_6({{25{1'b0}}, Kbd_Data}));  // open: in_7, in_8
  Register #(.width(32)) u_R1 (.D(In), .en(L1), .Q(R1), .clk(Clock), .clr(Clear));
  Register #(.width(32)) u_R9 (.D(In), .en(L9), .Q(R9), .clk(Clock), .clr(Clear));
  Register #(.width(32)) u_R17 (.D(In), .en(L17), .Q(R17), .clk(Clock), .clr(Clear));
  Register #(.width(32)) u_R25 (.D(In), .en(L25), .Q(R25), .clk(Clock), .clr(Clear));
  and and_1 (and_1_out, Input_Selector[2], ~Input_Selector[1], Input_Selector[0], ~Keyboard_Avail);  // AND_Gate
  MUX1bit mux1bit_1 (.out_4(In), .in_2(mux3bits_transistors_1_out_10), .in_3({32{1'b1}}), .in_1(and_1_out));
  Register #(.width(32)) u_R2 (.D(In), .en(L2), .Q(R2), .clk(Clock), .clr(Clear));
  Register #(.width(32)) u_R10 (.D(In), .en(L10), .Q(R10), .clk(Clock), .clr(Clear));
  Register #(.width(32)) u_R18 (.D(In), .en(L18), .Q(R18), .clk(Clock), .clr(Clear));
  Register #(.width(32)) u_R26 (.D(In), .en(L26), .Q(R26), .clk(Clock), .clr(Clear));
  Demultiplexer #(.select(5), .enable("false")) demultiplexer_1 (
    .out0(L0), .out1(L1), .out2(L2), .out3(L3), .out4(L4), .out5(L5), .out6(L6), .out7(L7), .out8(L8),
    .out9(L9), .out10(L10), .out11(L11), .out12(L12), .out13(L13), .out14(L14), .out15(L15), .out16(L16),
    .out17(L17), .out18(L18), .out19(L19), .out20(L20), .out21(L21), .out22(L22), .out23(L23), .out24(L24),
    .out25(L25), .out26(L26), .out27(L27), .out28(L28), .out29(L29), .out30(L30), .out31(L31),
    .in(R_W_Selector), .sel(Write_Address));
  Register #(.width(32)) u_R3 (.D(In), .en(L3), .Q(R3), .clk(Clock), .clr(Clear));
  Register #(.width(32)) u_R11 (.D(In), .en(L11), .Q(R11), .clk(Clock), .clr(Clear));
  Register #(.width(32)) u_R19 (.D(In), .en(L19), .Q(R19), .clk(Clock), .clr(Clear));
  Register #(.width(32)) u_R27 (.D(In), .en(L27), .Q(R27), .clk(Clock), .clr(Clear));
  Register #(.width(32)) u_R4 (.D(In), .en(L4), .Q(R4), .clk(Clock), .clr(Clear));
  Register #(.width(32)) u_R12 (.D(In), .en(L12), .Q(R12), .clk(Clock), .clr(Clear));
  Register #(.width(32)) u_R20 (.D(In), .en(L20), .Q(R20), .clk(Clock), .clr(Clear));
  Register #(.width(32)) u_R28 (.D(In), .en(L28), .Q(R28), .clk(Clock), .clr(Clear));
  Register #(.width(32)) u_R5 (.D(In), .en(L5), .Q(R5), .clk(Clock), .clr(Clear));
  Register #(.width(32)) u_R13 (.D(In), .en(L13), .Q(R13), .clk(Clock), .clr(Clear));
  Register #(.width(32)) u_R21 (.D(In), .en(L21), .Q(R21), .clk(Clock), .clr(Clear));
  Register #(.width(32)) u_R29 (.D(In), .en(L29), .Q(R29), .clk(Clock), .clr(Clear));
  Register #(.width(32)) u_R6 (.D(In), .en(L6), .Q(R6), .clk(Clock), .clr(Clear));
  Register #(.width(32)) u_R14 (.D(In), .en(L14), .Q(R14), .clk(Clock), .clr(Clear));
  Register #(.width(32)) u_R22 (.D(In), .en(L22), .Q(R22), .clk(Clock), .clr(Clear));
  Register #(.width(32)) u_R30 (.D(In), .en(L30), .Q(R30), .clk(Clock), .clr(Clear));
  Adder #(.width(32)) adder_1 (.a(out_17), .b(32'h4), .out(plus_4));  // open: cin, cout
  Subtractor #(.width(32)) subtractor_1 (.a(out_17), .b(32'h4), .out(minus_4));  // open: bin, bout
  MUX5bits mux5bits_1 (
    .in_1(R0), .in_9(R8), .in_17(R16), .in_25(R24), .in_33(Read_Address_A), .in_2(R1), .in_10(R9),
    .in_18(R17), .in_26(R25), .in_3(R2), .in_11(R10), .in_19(R18), .in_27(R26), .in_4(R3), .in_12(R11),
    .in_20(R19), .in_28(R27), .in_5(R4), .in_13(R12), .in_21(R20), .in_29(R28), .in_6(R5), .in_14(R13),
    .in_22(R21), .in_30(R29), .in_7(R6), .in_15(R14), .in_23(R22), .in_31(R30), .in_8(R7), .in_16(R15),
    .in_24(R23), .in_32(out_17), .out_34(out_16));
  Register #(.width(32)) u_R7 (.D(In), .en(L7), .Q(R7), .clk(Clock), .clr(Clear));
  Register #(.width(32)) u_R15 (.D(In), .en(L15), .Q(R15), .clk(Clock), .clr(Clear));
  Register #(.width(32)) u_R23 (.D(In), .en(L23), .Q(R23), .clk(Clock), .clr(Clear));
  MUX2bits mux2bits_1 (
    .out_6(mux2bits_1_out_6), .in_2(In), .in_3(In), .in_4(plus_4), .in_5(minus_4), .in_1(SP_Selector));
  MUX1bit mux1bit_2 (.out_4(mux1bit_2_out_4), .in_2(mux2bits_1_out_6), .in_3({32{1'b1}}), .in_1(Clear));
  or or_1 (or_1_out, L31, Load_R31, Clear);
  Register #(.width(32)) R31 (.D(mux1bit_2_out_4), .en(or_1_out), .Q(out_17), .clk(Clock));  // open: clr
  MUX5bits mux5bits_2 (
    .in_1(R0), .in_9(R8), .in_17(R16), .in_25(R24), .in_33(Read_Address_B), .in_2(R1), .in_10(R9),
    .in_18(R17), .in_26(R25), .in_3(R2), .in_11(R10), .in_19(R18), .in_27(R26), .in_4(R3), .in_12(R11),
    .in_20(R19), .in_28(R27), .in_5(R4), .in_13(R12), .in_21(R20), .in_29(R28), .in_6(R5), .in_14(R13),
    .in_22(R21), .in_30(R29), .in_7(R6), .in_15(R14), .in_23(R22), .in_31(R30), .in_8(R7), .in_16(R15),
    .in_24(R23), .in_32(out_17), .out_34(out_18));

  // Other names for the same wires on the sheet: A[31:0] = out_16; ALU[31:0] = ALU_Input; B[31:0] = out_18;
  //   CLR = Clear; Hi[31:0] = Hi_Register_Input; IS[2:0] = Input_Selector; Kbd_32[6:0] = Kbd_Data;
  //   Kbd_Av = Keyboard_Avail; L31_PP = Load_R31; Lo[31:0] = Lo_Register_Input; R31[31:0] = out_17;
  //   R31_Sel[1:0] = SP_Selector; R_W = R_W_Selector; RA[4:0] = Read_Address_A; RAM[31:0] = Memory_Input;
  //   RB[4:0] = Read_Address_B; WA[4:0] = Write_Address

  // Notes on the sheet:
  //   INPUTS
  //   GENERAL PURPOSE REGISTERS
  //   FROG Write Selector
  //   0 reads, 1 writes
  //   "THE FROGS"
  //   RULE THE
  //   REGISTER FILE!!!
  //   OUTPUTS
  //   FROG Output A
  //   FROG Output B
endmodule

module ID (
  input  [31:0] Instruction,
  input  [31:0] RF_31,
  input  [31:0] ALU,
  input  in_4,
  input  in_5,
  input  in_6,
  input  in_7,
  input  [31:0] RF_A,
  input  [31:0] RF_B,
  output [31:0] out_10,
  output [31:0] out_11,
  output R_W_Selector,
  output PC_Enable,
  output [2:0] FS,
  output [2:0] MULTDIV_SELECT,
  output [31:0] out_16,
  output [15:0] Constant_Input,
  output Halt,
  output [25:0] Jump_Destination,
  output [1:0] Pop_Push,
  output _2OP,
  output KBD_Enable,
  output [4:0] Read_Address_A,
  output [4:0] Read_Address_B,
  output [4:0] Write_Address,
  output L_R31,
  output Tty,
  output [2:0] IS,
  output [2:0] JUMP_TYPE,
  output Read_Enable,
  output Write_Enable
);

  wire _2OP1, _2OP2, _2OP3, _2OP4, _2OP5, _2OP6, _2OP7, _2OP8, ADD, ALU_EN1, ALU_EN2, ALU_EN3, ALU_EN4, AND,
       BEQ, BGTZ, BLEZ, BLTZ, BNE, FS0_1, FS0_2, FS0_3, FS0_4, FS1_1, FS1_3, I, IS0_1, IS0_2, IS0_3, IS1_1,
       IS2_1, J, JR, L_R31_1, NOP, or_10_out, or_11_out, PC_EN30, PC_EN32, POP, PP1_2, PUSH, R_general,
       R_special, R_stack, Read_En1, Read_En2, Write_En1, Write_En2;

  and u_NOP (NOP, R_general, ~Instruction[0], ~Instruction[1], ~Instruction[2], ~Instruction[3], ~Instruction[4], ~Instruction[5]);  // AND_Gate
  and u_ADD (ADD, R_general, ~Instruction[0], ~Instruction[1], ~Instruction[2], ~Instruction[3], ~Instruction[4], Instruction[5]);  // AND_Gate
  and SUB (FS0_1, R_general, ~Instruction[0], Instruction[1], ~Instruction[2], ~Instruction[3], ~Instruction[4], Instruction[5]);  // AND_Gate
  and MULT (ALU_EN1, R_general, ~Instruction[0], ~Instruction[1], ~Instruction[2], Instruction[3], Instruction[4], ~Instruction[5]);  // AND_Gate
  and MULU (ALU_EN2, R_general, Instruction[0], ~Instruction[1], ~Instruction[2], Instruction[3], Instruction[4], ~Instruction[5]);  // AND_Gate
  and ADDI (_2OP1, I, ~Instruction[26], ~Instruction[27], ~Instruction[28], Instruction[29], ~Instruction[30], ~Instruction[31]);  // AND_Gate
  and SLTI (_2OP5, I, ~Instruction[26], Instruction[27], ~Instruction[28], ~Instruction[29], ~Instruction[30], Instruction[31]);  // AND_Gate
  and SLTIU (_2OP6, I, Instruction[26], Instruction[27], ~Instruction[28], Instruction[29], ~Instruction[30], ~Instruction[31]);  // AND_Gate
  and ANDI (_2OP2, I, ~Instruction[26], ~Instruction[27], Instruction[28], Instruction[29], ~Instruction[30], ~Instruction[31]);  // AND_Gate
  and ORI (_2OP3, I, Instruction[26], ~Instruction[27], Instruction[28], Instruction[29], ~Instruction[30], ~Instruction[31]);  // AND_Gate
  or or_1 (_2OP, _2OP8, _2OP1, _2OP2, _2OP3, _2OP4, _2OP5, _2OP6, _2OP7);
  LoadWord loadword_1 (.in_1(_2OP7), .in_2(in_6), .in_3(in_4), .out_5(IS0_2), .out_6(Read_En1), .in_4(in_5));
  StoreWord storeword_1 (.in_1(_2OP8), .in_2(in_7), .in_3(in_4), .out_5(PC_EN30), .out_6(Write_En1), .in_4(in_5));
  or or_2 (FS[0], FS0_1, FS0_2, FS0_3, FS0_4, _2OP3, _2OP4, _2OP6);
  or or_3 (FS[1], FS1_1, FS0_2, FS1_3, FS0_4, _2OP4, _2OP5, _2OP6);
  or or_4 (FS[2], AND, FS0_3, FS1_3, FS0_4, _2OP2, _2OP3, _2OP4);
  and XORI (_2OP4, I, ~Instruction[26], Instruction[27], Instruction[28], Instruction[29], ~Instruction[30], ~Instruction[31]);  // AND_Gate
  and LW (_2OP7, I, Instruction[26], Instruction[27], ~Instruction[28], ~Instruction[29], ~Instruction[30], Instruction[31]);  // AND_Gate
  and SW (_2OP8, I, Instruction[26], Instruction[27], ~Instruction[28], Instruction[29], ~Instruction[30], Instruction[31]);  // AND_Gate
  and u_BEQ (BEQ, I, ~Instruction[26], ~Instruction[27], Instruction[28], ~Instruction[29], ~Instruction[30], ~Instruction[31]);  // AND_Gate
  and u_BNE (BNE, I, Instruction[26], ~Instruction[27], Instruction[28], ~Instruction[29], ~Instruction[30], ~Instruction[31]);  // AND_Gate
  and DIV (ALU_EN3, R_general, ~Instruction[0], Instruction[1], ~Instruction[2], Instruction[3], Instruction[4], ~Instruction[5]);  // AND_Gate
  and DIVU (ALU_EN4, R_general, Instruction[0], Instruction[1], ~Instruction[2], Instruction[3], Instruction[4], ~Instruction[5]);  // AND_Gate
  and SLT (FS1_1, R_general, ~Instruction[0], Instruction[1], ~Instruction[2], Instruction[3], ~Instruction[4], Instruction[5]);  // AND_Gate
  and SLTU (FS0_2, R_general, Instruction[0], Instruction[1], ~Instruction[2], Instruction[3], ~Instruction[4], Instruction[5]);  // AND_Gate
  and u_AND (AND, R_general, ~Instruction[0], ~Instruction[1], Instruction[2], ~Instruction[3], ~Instruction[4], Instruction[5]);  // AND_Gate
  or or_5 (MULTDIV_SELECT[0], ALU_EN2, ALU_EN4);
  or or_6 (MULTDIV_SELECT[1], ALU_EN3, ALU_EN4);
  or or_7 (MULTDIV_SELECT[2], ALU_EN1, ALU_EN2, ALU_EN3, ALU_EN4);
  and u_BLEZ (BLEZ, I, ~Instruction[26], Instruction[27], Instruction[28], ~Instruction[29], ~Instruction[30], ~Instruction[31]);  // AND_Gate
  and u_BGTZ (BGTZ, I, Instruction[26], Instruction[27], Instruction[28], ~Instruction[29], ~Instruction[30], ~Instruction[31]);  // AND_Gate
  and u_BLTZ (BLTZ, I, Instruction[26], ~Instruction[27], ~Instruction[28], ~Instruction[29], ~Instruction[30], ~Instruction[31]);  // AND_Gate
  LoadWord loadword_2 (.in_1(POP), .in_2(in_6), .in_3(in_4), .out_5(IS0_3), .out_6(Read_En2), .in_4(in_5));
  StoreWord_Push storeword_push_1 (
    .in_1(PUSH), .in_2(in_7), .in_3(in_4), .in_4(in_5), .out_5(PC_EN32), .out_6(Write_En2), .out_7(PP1_2),
    .out_8(Pop_Push[0]), .out_9(L_R31_1));
  and OR_8 (FS0_3, R_general, Instruction[0], ~Instruction[1], Instruction[2], ~Instruction[3], ~Instruction[4], Instruction[5]);  // AND_Gate
  and NOR (FS1_3, R_general, Instruction[0], Instruction[1], Instruction[2], ~Instruction[3], ~Instruction[4], Instruction[5]);  // AND_Gate
  and XOR (FS0_4, R_general, ~Instruction[0], ~Instruction[1], ~Instruction[2], Instruction[3], ~Instruction[4], Instruction[5]);  // AND_Gate
  and u_JR (JR, R_general, ~Instruction[0], ~Instruction[1], ~Instruction[2], Instruction[3], ~Instruction[4], ~Instruction[5]);  // AND_Gate
  and MFHI (IS0_1, R_general, ~Instruction[0], ~Instruction[1], ~Instruction[2], ~Instruction[3], Instruction[4], ~Instruction[5]);  // AND_Gate
  and and_2 (R_stack, ~Instruction[26], ~Instruction[27], ~Instruction[28], Instruction[29], Instruction[30], Instruction[31]);  // AND_Gate
  and and_3 (R_special, Instruction[26], Instruction[27], Instruction[28], Instruction[29], Instruction[30], Instruction[31]);
  nor nor_2 (R_general, Instruction[26], Instruction[27], Instruction[28], Instruction[29], Instruction[30], Instruction[31]);
  and and_4 (J, ~Instruction[26], Instruction[27], ~Instruction[28], ~Instruction[29], ~Instruction[30], ~Instruction[31]);  // AND_Gate
  and MFLO (IS1_1, R_general, ~Instruction[0], Instruction[1], ~Instruction[2], ~Instruction[3], Instruction[4], ~Instruction[5]);  // AND_Gate
  and u_POP (POP, R_stack, ~Instruction[0], ~Instruction[1], ~Instruction[2], ~Instruction[3], ~Instruction[4], ~Instruction[5]);  // AND_Gate
  and u_PUSH (PUSH, R_stack, Instruction[0], ~Instruction[1], ~Instruction[2], ~Instruction[3], ~Instruction[4], ~Instruction[5]);  // AND_Gate
  or or_9 (PC_Enable, or_11_out, KBD_Enable, IS2_1, Tty);
  or or_10 (or_10_out, R_stack, R_special, R_general);
  MUX1bit mux1bit_1 (.out_4(out_10), .in_2(RF_31), .in_3(ALU), .in_1(_2OP7));
  MUX1bit mux1bit_2 (.out_4(out_11), .in_2(RF_31), .in_3(ALU), .in_1(_2OP8));
  MUX1bit mux1bit_3 (.out_4(out_16), .in_2(RF_A), .in_3(RF_B), .in_1(_2OP8));
  nor nor_3 (I, or_10_out, J);
  or or_11 (or_11_out, ADD, FS0_1, FS1_1, FS0_2, AND, FS0_3, FS1_3, FS0_4, _2OP1, _2OP2, _2OP3, _2OP4, _2OP5, _2OP6, ALU_EN1, ALU_EN2, ALU_EN3, ALU_EN4, J, JR, BEQ, BNE, BLEZ, BGTZ, BLTZ, IS1_1, IS0_1, NOP, IS0_2, PC_EN30, IS0_3, PC_EN32);
  and u_HALT (Halt, R_special, Instruction[0], Instruction[1], Instruction[2], Instruction[3], Instruction[4], Instruction[5]);
  and u_TTY (Tty, R_special, Instruction[0], ~Instruction[1], ~Instruction[2], ~Instruction[3], ~Instruction[4], ~Instruction[5]);  // AND_Gate
  and RND (IS2_1, R_special, ~Instruction[0], Instruction[1], ~Instruction[2], ~Instruction[3], ~Instruction[4], ~Instruction[5]);  // AND_Gate
  and KBD (KBD_Enable, R_special, ~Instruction[0], ~Instruction[1], Instruction[2], ~Instruction[3], ~Instruction[4], ~Instruction[5]);  // AND_Gate
  or or_12 (JUMP_TYPE[0], J, BEQ, BLEZ, BLTZ);
  or or_13 (JUMP_TYPE[1], JR, BEQ, BGTZ, BLTZ);
  or or_14 (JUMP_TYPE[2], BNE, BLEZ, BGTZ, BLTZ);
  or or_15 (R_W_Selector, ADD, FS0_1, FS1_1, FS0_2, AND, FS0_3, FS1_3, FS0_4, _2OP1, _2OP2, _2OP3, _2OP4, _2OP5, _2OP6, ALU_EN1, ALU_EN2, ALU_EN3, ALU_EN4, IS1_1, IS0_1, IS0_2, IS0_3, IS2_1, KBD_Enable);
  Multiplexer #(.width(5), .enable("false")) multiplexer_1 (
    .in0(Instruction[15:11]), .in1(Instruction[20:16]), .out(Write_Address), .sel(I));
  or or_16 (IS[0], IS0_1, IS0_2, IS0_3, KBD_Enable);
  or or_17 (IS[1], IS1_1, IS0_2, IS0_3);
  or or_18 (IS[2], IS2_1, KBD_Enable);
  or or_19 (Pop_Push[1], IS0_3, PP1_2);
  or or_20 (L_R31, IS0_3, L_R31_1);
  or or_21 (Read_Enable, Read_En1, Read_En2);
  or or_22 (Write_Enable, Write_En1, Write_En2);

  assign Constant_Input = Instruction[15:0];
  assign Jump_Destination = Instruction[25:0];
  assign Read_Address_A = Instruction[25:21];
  assign Read_Address_B = Instruction[20:16];

  // Other names for the same wires on the sheet: Clock = in_4; CLR = in_5; Constant[15:0] = Instruction[15:0];
  //   Jmp_Dest[25:0] = Instruction[25:0]; Func_code[5:0] = Instruction[5:0]; Op_code[5:0] = Instruction[31:26];
  //   JT0_1 = J; PC_EN19 = J; JT1_1 = JR; PC_EN20 = JR; JT0_2 = BEQ; JT1_2 = BEQ; PC_EN21 = BEQ; JT2_1 = BNE;
  //   PC_EN22 = BNE; JT0_3 = BLEZ; JT2_2 = BLEZ; PC_EN23 = BLEZ; JT1_3 = BGTZ; JT2_3 = BGTZ; PC_EN24 = BGTZ;
  //   JT0_4 = BLTZ; JT1_4 = BLTZ; JT2_4 = BLTZ; PC_EN25 = BLTZ; PC_EN28 = NOP; PC_EN35 = Tty; PP2 = Pop_Push[0];
  //   PC_EN1 = ADD; R_W1 = ADD; FS2_1 = AND; PC_EN5 = AND; R_W5 = AND; FS2_2 = FS0_3; OR = FS0_3; PC_EN6 = FS0_3;
  //   R_W6 = FS0_3; FS2_3 = FS1_3; NOR = FS1_3; PC_EN7 = FS1_3; R_W7 = FS1_3; ADDI = _2OP1; PC_EN9 = _2OP1;
  //   R_W9 = _2OP1; ANDI = _2OP2; FS2_5 = _2OP2; PC_EN10 = _2OP2; R_W10 = _2OP2; FS0_5 = _2OP3; FS2_6 = _2OP3;
  //   ORI = _2OP3; PC_EN11 = _2OP3; R_W11 = _2OP3; MULT = ALU_EN1; PC_EN15 = ALU_EN1; R_W15 = ALU_EN1; DIV = ALU_EN3;
  //   MULT_DIV1 = ALU_EN3; PC_EN17 = ALU_EN3; R_W17 = ALU_EN3; MFLO = IS1_1; PC_EN26 = IS1_1; R_W19 = IS1_1;
  //   MFHI = IS0_1; PC_EN27 = IS0_1; R_W20 = IS0_1; IS1_2 = IS0_2; PC_EN29 = IS0_2; R_W21 = IS0_2; IS1_3 = IS0_3;
  //   L_R31_0 = IS0_3; PC_EN31 = IS0_3; PP1_1 = IS0_3; R_W22 = IS0_3; IS0_4 = KBD_Enable; IS2_2 = KBD_Enable;
  //   KBD = KBD_Enable; KBD_EN = KBD_Enable; PC_EN33 = KBD_Enable; R_W24 = KBD_Enable; LW = _2OP7; RA_Sel = _2OP7;
  //   Rd[4:0] = Instruction[15:11]; ReadAdd[31:0] = out_10; ReadFlag = in_6; PC_EN34 = IS2_1; R_W23 = IS2_1;
  //   RND = IS2_1; Rs[4:0] = Instruction[25:21]; Rt[4:0] = Instruction[20:16]; PC_EN3 = FS1_1; R_W3 = FS1_1;
  //   SLT = FS1_1; FS1_6 = _2OP5; PC_EN13 = _2OP5; R_W13 = _2OP5; SLTI = _2OP5; FS0_7 = _2OP6; FS1_7 = _2OP6;
  //   PC_EN14 = _2OP6; R_W14 = _2OP6; RF_EN5 = _2OP6; SLTIU = _2OP6; FS1_2 = FS0_2; PC_EN4 = FS0_2; R_W4 = FS0_2;
  //   SLTU = FS0_2; PC_EN2 = FS0_1; R_W2 = FS0_1; SUB = FS0_1; MULU = ALU_EN2; PC_EN16 = ALU_EN2; R_W16 = ALU_EN2;
  //   UNS1 = ALU_EN2; DIVU = ALU_EN4; MULT_DIV2 = ALU_EN4; PC_EN18 = ALU_EN4; R_W18 = ALU_EN4; UNS2 = ALU_EN4;
  //   SW = _2OP8; WA_Sel = _2OP8; WD_Sel = _2OP8; WriteAdd[31:0] = out_11; WriteData[31:0] = out_16; WriteFlag = in_7;
  //   FS1_4 = FS0_4; FS2_4 = FS0_4; PC_EN8 = FS0_4; R_W8 = FS0_4; XOR = FS0_4; FS0_6 = _2OP4; FS1_5 = _2OP4;
  //   FS2_7 = _2OP4; PC_EN12 = _2OP4; R_W12 = _2OP4; XORI = _2OP4

  // Notes on the sheet:
  //   ALU
  //   INPUTS
  //   R-type DECODER
  //   R-general
  //   I-type DECODER
  //   Activate Control Signals
  //   R-general
  //   SPLITTING THE INSTRUCTION
  //   R-general
  //   DECODING THE INSTRUCTION
  //   OUTPUTS 
  //   PC
  //   R-general
  //   R-stack
  //   R-type
  //   I-type
  //   J-tpye
  //   R-special
  //   RF
  //   Directs Outs
endmodule

module PC (
  input  [2:0] Instruction_Selector,
  input  Enable,
  input  Clock,
  input  Clear,
  input  [15:0] Constant_Input,
  input  [25:0] Jump_Destination_Input,
  input  [31:0] Register_Input,
  input  _32bits,
  input  _32bits_2,
  input  _32bits_3,
  output [31:0] Next_Instruction_Address
);

  wire and_1_out;
  wire [1:0] Input_Sel;
  wire [29:0] multiplexer_1_out;
  wire [31:0] IP_In;
  wire [31:2] Adder_In;

  and and_1 (and_1_out, Input_Sel[0], Input_Sel[1]);
  Multiplexer #(.width(30), .enable("false")) multiplexer_1 (
    .in0({30{1'b0}}), .in1({{15{Constant_Input[15]}}, Constant_Input[14:0]}), .out(multiplexer_1_out),
    .sel(and_1_out));
  Adder #(.width(30)) adder_1 (
    .a(multiplexer_1_out), .b(Next_Instruction_Address[31:2]), .out(Adder_In), .cin(1'b1));  // open: cout
  PC_AuxCirc1 pc_auxcirc1_1 (
    .b2(Instruction_Selector[2]), .b1(Instruction_Selector[1]), .b0(Instruction_Selector[0]), .men(_32bits),
    .eq(_32bits_2), .may(_32bits_3), .a(Input_Sel[1]), .b(Input_Sel[0]));
  MUX2bits mux2bits_1 (
    .out_6(IP_In), .in_2({Adder_In, 2'b00}),
    .in_3({Next_Instruction_Address[31:28], Jump_Destination_Input, 2'b00}), .in_4(Register_Input),
    .in_5({Adder_In, 2'b00}), .in_1(Input_Sel));
  Register #(.width(32)) IP (.D(IP_In), .en(Enable), .Q(Next_Instruction_Address), .clk(Clock), .clr(Clear));

  // Other names for the same wires on the sheet: Adder_Out[29:0] = Adder_In; CLR = Clear;
  //   Constant[15:0] = Constant_Input; Increment[29:0] = {{15{Constant_Input[15]}}, Constant_Input[14:0]};
  //   Inst_Sel[2:0] = Instruction_Selector; IP_Add[29:0] = Next_Instruction_Address[31:2];
  //   IP_Out[31:0] = Next_Instruction_Address; Ip_Load = Enable;
  //   Jmp_Add[31:2] = {Next_Instruction_Address[31:28], Jump_Destination_Input};
  //   Jmp_Dest[25:0] = Jump_Destination_Input; Reg[31:0] = Register_Input; tunnel = _32bits; tunnel_t = _32bits_2;
  //   tunnel_t_t = _32bits_3

  // Notes on the sheet:
  //   INPUTS
  //   BUILDING THE OFFSET
  //   BUILDING THE IP BITS TO ADD
  //   BUILDING THE ADDER IN
  //   BUILDING THE INPUT SELECTOR
  //   BUILDING THE JUMP ADDRESS
  //   //Using the fact that IP will be always divisible by 4
  //   SELECTING THE IP INPUT DATA
  //   OUTPUTS
  //   //Takes the Adder input if it is a 
  //   //Constant Jump or a Normal Increment
  //   000-None
  //   001-J
  //   010-JR
  //   011-BEQ
  //   100-BNE
  //   101-BLEZ
  //   110-BGTZ
  //   111-BLTZ
endmodule

module PC_AuxCirc1 (
  input  b2,
  input  b1,
  input  b0,
  input  men,
  input  eq,
  input  may,
  output a,
  output b
);

  wire and_1_out, and_2_out, and_3_out, and_4_out, and_5_out, and_6_out, and_7_out, and_8_out, and_9_out,
       and_10_out, and_11_out, and_12_out, not_1_out, not_2_out, not_3_out, not_4_out, not_5_out, not_6_out,
       not_7_out, not_8_out, not_9_out, not_10_out, not_11_out, not_12_out, not_13_out, not_14_out;

  not not_1 (not_1_out, b2);
  not not_2 (not_2_out, b0);
  not not_3 (not_3_out, b2);
  not not_4 (not_4_out, b0);
  not not_5 (not_5_out, b1);
  not not_6 (not_6_out, b1);
  not not_7 (not_7_out, may);
  not not_8 (not_8_out, b2);
  not not_9 (not_9_out, b1);
  not not_10 (not_10_out, b1);
  not not_11 (not_11_out, may);
  not not_12 (not_12_out, b2);
  not not_13 (not_13_out, b0);
  not not_14 (not_14_out, b1);
  and and_1 (and_1_out, not_1_out, b1, not_2_out);
  and and_2 (and_2_out, not_3_out, b1, eq);
  and and_3 (and_3_out, b2, not_4_out, may);
  and and_4 (and_4_out, b2, not_5_out, men);
  and and_5 (and_5_out, b2, not_6_out, b0, not_7_out);
  and and_6 (and_6_out, b2, b0, men);
  and and_7 (and_7_out, not_8_out, not_9_out, b0);
  and and_8 (and_8_out, not_10_out, b0, not_11_out);
  and and_9 (and_9_out, not_12_out, b0, eq);
  and and_10 (and_10_out, b2, not_13_out, may);
  and and_11 (and_11_out, b2, not_14_out, men);
  and and_12 (and_12_out, b2, b0, men);
  or or_1 (a, and_1_out, and_2_out, and_3_out, and_4_out, and_5_out, and_6_out);
  or or_2 (b, and_7_out, and_8_out, and_9_out, and_10_out, and_11_out, and_12_out);
endmodule

module CACHE (
  input  [3:0] Read_Time,
  input  Reader_Enable,
  input  [3:0] Write_Time,
  input  Writer_Enable,
  input  [31:0] in_5,
  input  [31:0] Write_Data,
  input  [31:0] RAM_0,
  input  [31:0] RAM_1,
  input  [31:0] RAM_2,
  input  [31:0] RAM_3,
  input  Clock,
  input  Clear,
  output ReadReady,
  output R_W,
  output WriteReady,
  output [3:0] Mask,
  output C_S,
  output [15:0] RAM_A,
  output [31:0] ReadOutput,
  output [31:0] RAM_0_2,
  output [31:0] RAM_1_2,
  output [31:0] RAM_2_2,
  output [31:0] RAM_3_2
);

  wire a, and_1_out, and_2_out, and_3_out, and_4_out, and_5_out, and_6_out, and_7_out, and_8_out, and_9_out,
       and_10_out, and_11_out, and_12_out, and_13_out, and_14_out, and_15_out, and_16_out, and_17_out,
       and_18_out, and_19_out, and_20_out, and_21_out, and_22_out, and_23_out, and_24_out, and_25_out,
       and_26_out, and_27_out, and_28_out, and_29_out, and_30_out, and_31_out, and_32_out, and_33_out,
       and_34_out, and_35_out, and_36_out, c, CacheWrite, CacheWrite0, CacheWrite1, comparator_1_eq,
       comparator_2_eq, comparator_3_eq, comparator_4_eq, CS_1, CS_2, d, demultiplexer_2_out2,
       demultiplexer_3_out1, demultiplexer_4_out0, demultiplexer_6_out0, demultiplexer_6_out1,
       demultiplexer_7_out1, DirtyFlag, Hit, L1A, L1A_O, L1A_W, L1B, L1B_O, L1B_W, L2A, L2A_O, L2A_W, L2B,
       L2B_O, L2B_W, L3A, L3A_O, L3A_W, L3B, L3B_O, L3B_W, L4A, L4A_O, L4A_W, L4B, L4B_O, L4B_W, M0, M1, M2,
       M3, or_18_out, or_20_out, or_22_out, Read_Flag, Reader, Rnd_En, Rnd_En0, Rnd_En1, START_q, Tag_Match,
       Val0, Val1, Val2, Val3, w, WRITE_D_2_q, WRITE_D_q, Write_Flag, WriteHit, Writer, Writer0, Writer1, x,
       y, z;
  wire [1:0] LineSel, priority_encoder_1_out, Rnd;
  wire [3:0] Dirt0A, Dirt0B, Dirt1A, Dirt1B, Dirt2A, Dirt2B, Dirt3A, Dirt3B, DirtIn, mux1bit_4data_1_out_4,
       mux1bit_4data_2_out_4, mux1bit_4data_3_out_4, mux1bit_4data_4_out_4, mux1bit_4data_5_out_4,
       mux1bit_4data_6_out_4, mux1bit_4data_7_out_4, mux1bit_4data_8_out_4, mux1bit_4data_9_out_4,
       mux1bit_4data_10_out_4, mux1bit_4data_11_out_4, mux1bit_4data_12_out_4, mux1bit_4data_15_out_4,
       mux1bit_4data_16_out_4, mux1bit_4data_17_out_4, mux1bit_4data_18_out_4, mux1bit_4data_19_out_4,
       mux1bit_4data_20_out_4, mux1bit_4data_21_out_4, mux1bit_4data_22_out_4, or_1_out, or_2_out, or_3_out,
       or_4_out, or_5_out, or_6_out, or_7_out, or_8_out, or_9_out, or_10_out, or_11_out, or_12_out,
       or_13_out, or_14_out, or_15_out, or_16_out, RAM_MASK_W, Val0A, Val0B, Val1A, Val1B, Val2A, Val2B,
       Val3A, Val3B, ValIn;
  wire [14:0] mux1bit_15data_1_out_4, mux1bit_15data_2_out_4, mux1bit_15data_3_out_4, mux1bit_15data_4_out_4,
       RT0A, RT0B, RT1A, RT1B, RT2A, RT2B, RT3A, RT3B, Write_Tag;
  wire [15:0] Add16_Read, Add16_Write;
  wire [31:0] COL_0, COL_1, COL_2, COL_3, Data_if_Hit, Data_if_NO_Hit, In0, In1, In2, In3, R0, R1, R2, R3,
       R4, R5, R6, R7, R8, R9, R10, R11, R12, R13, R14, R15, R16, R17, R18, R19, R20, R21, R22, R23, R24,
       R25, R26, R27, R28, R29, R30, R31, RAM_INPUT_0, RAM_INPUT_1, RAM_INPUT_2, RAM_INPUT_3, RAM_OUTPUT_0,
       RAM_OUTPUT_1, RAM_OUTPUT_2, RAM_OUTPUT_3, undriven;

  MUX1bit_15Data mux1bit_15data_1 (.out_4(mux1bit_15data_1_out_4), .in_2(RT0A), .in_3(RT0B), .in_1(in_5[4]));
  MUX1bit_15Data mux1bit_15data_2 (.out_4(mux1bit_15data_2_out_4), .in_2(RT1A), .in_3(RT1B), .in_1(in_5[4]));
  MUX1bit_15Data mux1bit_15data_3 (.out_4(mux1bit_15data_3_out_4), .in_2(RT2A), .in_3(RT2B), .in_1(in_5[4]));
  MUX1bit_15Data mux1bit_15data_4 (.out_4(mux1bit_15data_4_out_4), .in_2(RT3A), .in_3(RT3B), .in_1(in_5[4]));
  MUX1bit_4Data mux1bit_4data_1 (.out_4(mux1bit_4data_1_out_4), .in_2(Val0A), .in_3(Val0B), .in_1(in_5[4]));
  MUX1bit_4Data mux1bit_4data_2 (.out_4(mux1bit_4data_2_out_4), .in_2(Val1A), .in_3(Val1B), .in_1(in_5[4]));
  MUX1bit_4Data mux1bit_4data_3 (.out_4(mux1bit_4data_3_out_4), .in_2(Val2A), .in_3(Val2B), .in_1(in_5[4]));
  MUX1bit_4Data mux1bit_4data_4 (.out_4(mux1bit_4data_4_out_4), .in_2(Val3A), .in_3(Val3B), .in_1(in_5[4]));
  MUX1bit_4Data mux1bit_4data_5 (.out_4(mux1bit_4data_5_out_4), .in_2(4'b0000), .in_3(Dirt0A), .in_1(WriteHit));
  MUX1bit_4Data mux1bit_4data_6 (.out_4(mux1bit_4data_6_out_4), .in_2(4'b0000), .in_3(Dirt1A), .in_1(WriteHit));
  MUX1bit_4Data mux1bit_4data_7 (.out_4(mux1bit_4data_7_out_4), .in_2(4'b0000), .in_3(Dirt2A), .in_1(WriteHit));
  MUX1bit_4Data mux1bit_4data_8 (.out_4(mux1bit_4data_8_out_4), .in_2(4'b0000), .in_3(Dirt3A), .in_1(WriteHit));
  MUX1bit_4Data mux1bit_4data_9 (.out_4(mux1bit_4data_9_out_4), .in_2(4'b0000), .in_3(Dirt0B), .in_1(WriteHit));
  MUX1bit_4Data mux1bit_4data_10 (.out_4(mux1bit_4data_10_out_4), .in_2(4'b0000), .in_3(Dirt1B), .in_1(WriteHit));
  MUX1bit_4Data mux1bit_4data_11 (.out_4(mux1bit_4data_11_out_4), .in_2(4'b0000), .in_3(Dirt2B), .in_1(WriteHit));
  MUX1bit_4Data mux1bit_4data_12 (.out_4(mux1bit_4data_12_out_4), .in_2(4'b0000), .in_3(Dirt3B), .in_1(WriteHit));
  Comparator #(.width(15)) comparator_1 (
    .a(mux1bit_15data_1_out_4), .b(in_5[19:5]), .eq(comparator_1_eq));  // open: gt, lt
  Comparator #(.width(15)) comparator_2 (
    .a(mux1bit_15data_2_out_4), .b(in_5[19:5]), .eq(comparator_2_eq));  // open: gt, lt
  Comparator #(.width(15)) comparator_3 (
    .a(mux1bit_15data_3_out_4), .b(in_5[19:5]), .eq(comparator_3_eq));  // open: gt, lt
  Comparator #(.width(15)) comparator_4 (
    .a(mux1bit_15data_4_out_4), .b(in_5[19:5]), .eq(comparator_4_eq));  // open: gt, lt
  Multiplexer #(.select(2), .enable("false")) multiplexer_1 (
    .in0(mux1bit_4data_1_out_4[0]), .in1(mux1bit_4data_1_out_4[1]), .in2(mux1bit_4data_1_out_4[2]),
    .in3(mux1bit_4data_1_out_4[3]), .out(Val0), .sel(in_5[3:2]));
  Multiplexer #(.select(2), .enable("false")) multiplexer_2 (
    .in0(mux1bit_4data_2_out_4[0]), .in1(mux1bit_4data_2_out_4[1]), .in2(mux1bit_4data_2_out_4[2]),
    .in3(mux1bit_4data_2_out_4[3]), .out(Val1), .sel(in_5[3:2]));
  Multiplexer #(.select(2), .enable("false")) multiplexer_3 (
    .in0(mux1bit_4data_3_out_4[0]), .in1(mux1bit_4data_3_out_4[1]), .in2(mux1bit_4data_3_out_4[2]),
    .in3(mux1bit_4data_3_out_4[3]), .out(Val2), .sel(in_5[3:2]));
  Multiplexer #(.select(2), .enable("false")) multiplexer_4 (
    .in0(mux1bit_4data_4_out_4[0]), .in1(mux1bit_4data_4_out_4[1]), .in2(mux1bit_4data_4_out_4[2]),
    .in3(mux1bit_4data_4_out_4[3]), .out(Val3), .sel(in_5[3:2]));
  assign or_1_out = DirtIn | mux1bit_4data_5_out_4;  // OR_Gate or_1, 4 bits wide
  assign or_2_out = DirtIn | mux1bit_4data_6_out_4;  // OR_Gate or_2, 4 bits wide
  assign or_3_out = DirtIn | mux1bit_4data_7_out_4;  // OR_Gate or_3, 4 bits wide
  assign or_4_out = DirtIn | mux1bit_4data_8_out_4;  // OR_Gate or_4, 4 bits wide
  assign or_5_out = DirtIn | mux1bit_4data_9_out_4;  // OR_Gate or_5, 4 bits wide
  assign or_6_out = DirtIn | mux1bit_4data_10_out_4;  // OR_Gate or_6, 4 bits wide
  assign or_7_out = DirtIn | mux1bit_4data_11_out_4;  // OR_Gate or_7, 4 bits wide
  assign or_8_out = DirtIn | mux1bit_4data_12_out_4;  // OR_Gate or_8, 4 bits wide
  Switcher switcher_1 (.in_1(RAM_0), .out_2(RAM_OUTPUT_0));
  Register #(.width(4)) Dirty0A (.D(or_1_out), .en(L1A), .Q(Dirt0A), .clk(Clock), .clr(Clear));
  Register #(.width(4)) Diry1A (.D(or_2_out), .en(L2A), .Q(Dirt1A), .clk(Clock), .clr(Clear));
  Register #(.width(4)) Dirty2A (.D(or_3_out), .en(L3A), .Q(Dirt2A), .clk(Clock), .clr(Clear));
  Register #(.width(4)) Dirty3A (.D(or_4_out), .en(L4A), .Q(Dirt3A), .clk(Clock), .clr(Clear));
  Register #(.width(4)) Dirty0B (.D(or_5_out), .en(L1B), .Q(Dirt0B), .clk(Clock), .clr(Clear));
  Register #(.width(4)) Dirty1B (.D(or_6_out), .en(L2B), .Q(Dirt1B), .clk(Clock), .clr(Clear));
  Register #(.width(4)) Dirty2B (.D(or_7_out), .en(L3B), .Q(Dirt2B), .clk(Clock), .clr(Clear));
  Register #(.width(4)) Dirty3B (.D(or_8_out), .en(L4B), .Q(Dirt3B), .clk(Clock), .clr(Clear));
  and and_1 (and_1_out, Val0, comparator_1_eq);
  and and_2 (and_2_out, Val1, comparator_2_eq);
  and and_3 (and_3_out, Val2, comparator_3_eq);
  and and_4 (and_4_out, Val3, comparator_4_eq);
  Switcher switcher_2 (.in_1(RAM_1), .out_2(RAM_OUTPUT_1));
  ExactlyOne xor_1 (.out(Hit), .in0(and_1_out), .in1(and_2_out), .in2(and_3_out), .in3(and_4_out));
  MUX1bit_4Data mux1bit_4data_13 (.out_4(DirtIn), .in_2(4'b0000), .in_3(RAM_MASK_W), .in_1(Writer_Enable));
  MUX1bit_4Data mux1bit_4data_14 (.out_4(ValIn), .in_2(4'b1111), .in_3(RAM_MASK_W), .in_1(Writer_Enable));
  MUX1bit_4Data mux1bit_4data_15 (.out_4(mux1bit_4data_15_out_4), .in_2(4'b0000), .in_3(Val0A), .in_1(WriteHit));
  MUX1bit_4Data mux1bit_4data_16 (.out_4(mux1bit_4data_16_out_4), .in_2(4'b0000), .in_3(Val1A), .in_1(WriteHit));
  MUX1bit_4Data mux1bit_4data_17 (.out_4(mux1bit_4data_17_out_4), .in_2(4'b0000), .in_3(Val2A), .in_1(WriteHit));
  MUX1bit_4Data mux1bit_4data_18 (.out_4(mux1bit_4data_18_out_4), .in_2(4'b0000), .in_3(Val3A), .in_1(WriteHit));
  MUX1bit_4Data mux1bit_4data_19 (.out_4(mux1bit_4data_19_out_4), .in_2(4'b0000), .in_3(Val0B), .in_1(WriteHit));
  MUX1bit_4Data mux1bit_4data_20 (.out_4(mux1bit_4data_20_out_4), .in_2(4'b0000), .in_3(Val1B), .in_1(WriteHit));
  MUX1bit_4Data mux1bit_4data_21 (.out_4(mux1bit_4data_21_out_4), .in_2(4'b0000), .in_3(Val2B), .in_1(WriteHit));
  MUX1bit_4Data mux1bit_4data_22 (.out_4(mux1bit_4data_22_out_4), .in_2(4'b0000), .in_3(Val3B), .in_1(WriteHit));
  Multiplexer #(.width(2), .enable("false")) multiplexer_5 (
    .in0(2'b00), .in1(priority_encoder_1_out), .out(LineSel), .sel(Hit));
  Priority_Encoder #(.select(2)) priority_encoder_1 (
    .in0(and_1_out), .in1(and_2_out), .in2(and_3_out), .in3(and_4_out), .out(priority_encoder_1_out));  // open: gs, en_out, en_in
  assign or_9_out = ValIn | mux1bit_4data_15_out_4;  // OR_Gate or_9, 4 bits wide
  assign or_10_out = ValIn | mux1bit_4data_16_out_4;  // OR_Gate or_10, 4 bits wide
  assign or_11_out = ValIn | mux1bit_4data_17_out_4;  // OR_Gate or_11, 4 bits wide
  assign or_12_out = ValIn | mux1bit_4data_18_out_4;  // OR_Gate or_12, 4 bits wide
  assign or_13_out = ValIn | mux1bit_4data_19_out_4;  // OR_Gate or_13, 4 bits wide
  assign or_14_out = ValIn | mux1bit_4data_20_out_4;  // OR_Gate or_14, 4 bits wide
  assign or_15_out = ValIn | mux1bit_4data_21_out_4;  // OR_Gate or_15, 4 bits wide
  assign or_16_out = ValIn | mux1bit_4data_22_out_4;  // OR_Gate or_16, 4 bits wide
  Switcher switcher_3 (.in_1(RAM_2), .out_2(RAM_OUTPUT_2));
  Register #(.width(4)) Valid0A (.D(or_9_out), .en(L1A), .Q(Val0A), .clk(Clock), .clr(Clear));
  Register #(.width(4)) Valid1A (.D(or_10_out), .en(L2A), .Q(Val1A), .clk(Clock), .clr(Clear));
  Register #(.width(4)) Valid2A (.D(or_11_out), .en(L3A), .Q(Val2A), .clk(Clock), .clr(Clear));
  Register #(.width(4)) Valid3A (.D(or_12_out), .en(L4A), .Q(Val3A), .clk(Clock), .clr(Clear));
  Register #(.width(4)) Valid0B (.D(or_13_out), .en(L1B), .Q(Val0B), .clk(Clock), .clr(Clear));
  Register #(.width(4)) Valid1B (.D(or_14_out), .en(L2B), .Q(Val1B), .clk(Clock), .clr(Clear));
  Register #(.width(4)) Valid2B (.D(or_15_out), .en(L3B), .Q(Val2B), .clk(Clock), .clr(Clear));
  Register #(.width(4)) Valid3B (.D(or_16_out), .en(L4B), .Q(Val3B), .clk(Clock), .clr(Clear));
  Switcher switcher_4 (.in_1(RAM_3), .out_2(RAM_OUTPUT_3));
  MUX3bits_Transistors mux3bits_transistors_1 (
    .out_10(COL_0), .in_1(R0), .in_9({in_5[4], LineSel}), .in_2(R4), .in_3(R8), .in_4(R12), .in_5(R16),
    .in_6(R20), .in_7(R24), .in_8(R28));
  MUX3bits_Transistors mux3bits_transistors_2 (
    .out_10(COL_2), .in_1(R2), .in_9({in_5[4], LineSel}), .in_2(R6), .in_3(R10), .in_4(R14), .in_5(R18),
    .in_6(R22), .in_7(R26), .in_8(R30));
  MUX1bit mux1bit_1 (.out_4(In0), .in_2(RAM_OUTPUT_0), .in_3(Write_Data), .in_1(Writer_Enable));
  MUX1bit mux1bit_2 (.out_4(In2), .in_2(RAM_OUTPUT_2), .in_3(Write_Data), .in_1(Writer_Enable));
  Register #(.width(15), .trigger("falling")) Tag0A (.D(in_5[19:5]), .en(L1A), .Q(RT0A), .clk(Clock), .clr(Clear));
  Register #(.width(15)) Tag1A (.D(in_5[19:5]), .en(L2A), .Q(RT1A), .clk(Clock), .clr(Clear));
  Register #(.width(15)) Tag2A (.D(in_5[19:5]), .en(L3A), .Q(RT2A), .clk(Clock), .clr(Clear));
  Register #(.width(15)) Tag3A (.D(in_5[19:5]), .en(L4A), .Q(RT3A), .clk(Clock), .clr(Clear));
  Register #(.width(15)) Tag0B (.D(in_5[19:5]), .en(L1B), .Q(RT0B), .clk(Clock), .clr(Clear));
  Register #(.width(15)) Tag1B (.D(in_5[19:5]), .en(L2B), .Q(RT1B), .clk(Clock), .clr(Clear));
  Register #(.width(15)) Tag2B (.D(in_5[19:5]), .en(L3B), .Q(RT2B), .clk(Clock), .clr(Clear));
  Register #(.width(15)) Tag3B (.D(in_5[19:5]), .en(L4B), .Q(RT3B), .clk(Clock), .clr(Clear));
  MemoryReader memoryreader_1 (
    .Address_32bits(in_5), .Read_Time(Read_Time), .Enable(Reader), .Clock(Clock), .Add16(Add16_Read),
    .Ready(Read_Flag), .C_S(CS_1), .Clear(Clear));
  and and_5 (and_5_out, L1A, M0);
  and and_6 (and_6_out, L2A, M0);
  and and_7 (and_7_out, L3A, M0);
  and and_8 (and_8_out, L4A, M0);
  and and_9 (and_9_out, L1B, M0);
  and and_10 (and_10_out, L2B, M0);
  and and_11 (and_11_out, L3B, M0);
  and and_12 (and_12_out, L4B, M0);
  MUX1bit mux1bit_3 (.out_4(In1), .in_2(RAM_OUTPUT_1), .in_3(Write_Data), .in_1(Writer_Enable));
  MUX1bit mux1bit_4 (.out_4(In3), .in_2(RAM_OUTPUT_3), .in_3(Write_Data), .in_1(Writer_Enable));
  Register #(.width(32)) u_R0 (.D(In0), .en(and_5_out), .Q(R0), .clk(Clock), .clr(Clear));
  Register #(.width(32)) u_R4 (.D(In0), .en(and_6_out), .Q(R4), .clk(Clock), .clr(Clear));
  Register #(.width(32)) u_R8 (.D(In0), .en(and_7_out), .Q(R8), .clk(Clock), .clr(Clear));
  Register #(.width(32)) u_R12 (.D(In0), .en(and_8_out), .Q(R12), .clk(Clock), .clr(Clear));
  Register #(.width(32)) u_R16 (.D(In0), .en(and_9_out), .Q(R16), .clk(Clock), .clr(Clear));
  Register #(.width(32)) u_R20 (.D(In0), .en(and_10_out), .Q(R20), .clk(Clock), .clr(Clear));
  Register #(.width(32)) u_R24 (.D(In0), .en(and_11_out), .Q(R24), .clk(Clock), .clr(Clear));
  Register #(.width(32)) u_R28 (.D(In0), .en(and_12_out), .Q(R28), .clk(Clock), .clr(Clear));
  MUX3bits_Transistors mux3bits_transistors_3 (
    .out_10(COL_1), .in_1(R1), .in_9({in_5[4], LineSel}), .in_2(R5), .in_3(R9), .in_4(R13), .in_5(R17),
    .in_6(R21), .in_7(R25), .in_8(R29));
  MUX3bits_Transistors mux3bits_transistors_4 (
    .out_10(COL_3), .in_1(R3), .in_9({in_5[4], LineSel}), .in_2(R7), .in_3(R11), .in_4(R15), .in_5(R19),
    .in_6(R23), .in_7(R27), .in_8(R31));
  and and_13 (and_13_out, L1A, M1);
  and and_14 (and_14_out, L2A, M1);
  and and_15 (and_15_out, L3A, M1);
  and and_16 (and_16_out, L4A, M1);
  and and_17 (and_17_out, L1B, M1);
  and and_18 (and_18_out, L2B, M1);
  and and_19 (and_19_out, L3B, M1);
  and and_20 (and_20_out, L4B, M1);
  Register #(.width(32)) u_R1 (.D(In1), .en(and_13_out), .Q(R1), .clk(Clock), .clr(Clear));
  Register #(.width(32)) u_R5 (.D(In1), .en(and_14_out), .Q(R5), .clk(Clock), .clr(Clear));
  Register #(.width(32)) u_R9 (.D(In1), .en(and_15_out), .Q(R9), .clk(Clock), .clr(Clear));
  Register #(.width(32)) u_R13 (.D(In1), .en(and_16_out), .Q(R13), .clk(Clock), .clr(Clear));
  Register #(.width(32)) u_R17 (.D(In1), .en(and_17_out), .Q(R17), .clk(Clock), .clr(Clear));
  Register #(.width(32)) u_R21 (.D(In1), .en(and_18_out), .Q(R21), .clk(Clock), .clr(Clear));
  Register #(.width(32)) u_R25 (.D(In1), .en(and_19_out), .Q(R25), .clk(Clock), .clr(Clear));
  Register #(.width(32)) u_R29 (.D(In1), .en(and_20_out), .Q(R29), .clk(Clock), .clr(Clear));
  MemoryWriter memorywriter_1 (
    .Address_32bits({undriven[31:20], Write_Tag, in_5[4:2], undriven[1:0]}), .R_W(R_W),
    .Write_Time(Write_Time), .Enable(Writer), .Clock(Clock), .Add16(Add16_Write), .Ready(Write_Flag),
    .C_S(CS_2), .Mask(RAM_MASK_W), .Clear(Clear));
  and and_21 (and_21_out, L1A, M2);
  and and_22 (and_22_out, L2A, M2);
  and and_23 (and_23_out, L3A, M2);
  and and_24 (and_24_out, L4A, M2);
  and and_25 (and_25_out, L1B, M2);
  and and_26 (and_26_out, L2B, M2);
  and and_27 (and_27_out, L3B, M2);
  and and_28 (and_28_out, L4B, M2);
  MUX2bits mux2bits_1 (.out_6(Data_if_Hit), .in_2(COL_0), .in_3(COL_1), .in_4(COL_2), .in_5(COL_3), .in_1(in_5[3:2]));
  MUX2bits mux2bits_2 (
    .out_6(Data_if_NO_Hit), .in_2(RAM_INPUT_0), .in_3(RAM_INPUT_1), .in_4(RAM_INPUT_2), .in_5(RAM_INPUT_3),
    .in_1(in_5[3:2]));
  Register #(.width(32)) u_R2 (.D(In2), .en(and_21_out), .Q(R2), .clk(Clock), .clr(Clear));
  Register #(.width(32)) u_R6 (.D(In2), .en(and_22_out), .Q(R6), .clk(Clock), .clr(Clear));
  Register #(.width(32)) u_R10 (.D(In2), .en(and_23_out), .Q(R10), .clk(Clock), .clr(Clear));
  Register #(.width(32)) u_R14 (.D(In2), .en(and_24_out), .Q(R14), .clk(Clock), .clr(Clear));
  Register #(.width(32)) u_R18 (.D(In2), .en(and_25_out), .Q(R18), .clk(Clock), .clr(Clear));
  Register #(.width(32)) u_R22 (.D(In2), .en(and_26_out), .Q(R22), .clk(Clock), .clr(Clear));
  Register #(.width(32)) u_R26 (.D(In2), .en(and_27_out), .Q(R26), .clk(Clock), .clr(Clear));
  Register #(.width(32)) u_R30 (.D(In2), .en(and_28_out), .Q(R30), .clk(Clock), .clr(Clear));
  MUX1bit_4Data mux1bit_4data_23 (.out_4({M3, M2, M1, M0}), .in_2(4'b1111), .in_3(RAM_MASK_W), .in_1(Writer_Enable));
  and and_29 (and_29_out, L1A, M3);
  and and_30 (and_30_out, L2A, M3);
  and and_31 (and_31_out, L3A, M3);
  and and_32 (and_32_out, L4A, M3);
  and and_33 (and_33_out, L1B, M3);
  and and_34 (and_34_out, L2B, M3);
  and and_35 (and_35_out, L3B, M3);
  and and_36 (and_36_out, L4B, M3);
  Register #(.width(32)) u_R3 (.D(In3), .en(and_29_out), .Q(R3), .clk(Clock), .clr(Clear));
  Register #(.width(32)) u_R7 (.D(In3), .en(and_30_out), .Q(R7), .clk(Clock), .clr(Clear));
  Register #(.width(32)) u_R11 (.D(In3), .en(and_31_out), .Q(R11), .clk(Clock), .clr(Clear));
  Register #(.width(32)) u_R15 (.D(In3), .en(and_32_out), .Q(R15), .clk(Clock), .clr(Clear));
  Register #(.width(32)) u_R19 (.D(In3), .en(and_33_out), .Q(R19), .clk(Clock), .clr(Clear));
  Register #(.width(32)) u_R23 (.D(In3), .en(and_34_out), .Q(R23), .clk(Clock), .clr(Clear));
  Register #(.width(32)) u_R27 (.D(In3), .en(and_35_out), .Q(R27), .clk(Clock), .clr(Clear));
  Register #(.width(32)) u_R31 (.D(In3), .en(and_36_out), .Q(R31), .clk(Clock), .clr(Clear));
  MUX1bit mux1bit_5 (.out_4(ReadOutput), .in_2(Data_if_NO_Hit), .in_3(Data_if_Hit), .in_1(Hit));
  Switcher switcher_5 (.in_1(RAM_INPUT_0), .out_2(RAM_0_2));
  Multiplexer #(.select(3), .width(15), .enable("false")) multiplexer_6 (
    .in0(RT0A), .in1(RT1A), .in2(RT2A), .in3(RT3A), .in4(RT0B), .in5(RT1B), .in6(RT2B), .in7(RT3B),
    .out(Write_Tag), .sel({in_5[4], Rnd}));
  Comparator #(.width(15)) comparator_5 (.a(Write_Tag), .b(in_5[19:5]), .eq(Tag_Match));  // open: gt, lt
  Switcher switcher_6 (.in_1(RAM_INPUT_1), .out_2(RAM_1_2));
  Switcher switcher_7 (.in_1(RAM_INPUT_2), .out_2(RAM_2_2));
  MUX3bits_Transistors mux3bits_transistors_5 (
    .out_10(RAM_INPUT_0), .in_1(R0), .in_9({in_5[4], Rnd}), .in_2(R4), .in_3(R8), .in_4(R12), .in_5(R16),
    .in_6(R20), .in_7(R24), .in_8(R28));
  MUX3bits_Transistors mux3bits_transistors_6 (
    .out_10(RAM_INPUT_2), .in_1(R2), .in_9({in_5[4], Rnd}), .in_2(R6), .in_3(R10), .in_4(R14), .in_5(R18),
    .in_6(R22), .in_7(R26), .in_8(R30));
  Switcher switcher_8 (.in_1(RAM_INPUT_3), .out_2(RAM_3_2));
  MUX3bits_4Data mux3bits_4data_1 (
    .out_10(Mask), .in_1(Dirt0A), .in_9({in_5[4], Rnd}), .in_2(Dirt1A), .in_3(Dirt2A), .in_4(Dirt3A),
    .in_5(Dirt0B), .in_6(Dirt1B), .in_7(Dirt2B), .in_8(Dirt3B));
  or or_17 (DirtyFlag, Mask[0], Mask[1], Mask[2], Mask[3]);
  MUX3bits_Transistors mux3bits_transistors_7 (
    .out_10(RAM_INPUT_1), .in_1(R1), .in_9({in_5[4], Rnd}), .in_2(R5), .in_3(R9), .in_4(R13), .in_5(R17),
    .in_6(R21), .in_7(R25), .in_8(R29));
  MUX3bits_Transistors mux3bits_transistors_8 (
    .out_10(RAM_INPUT_3), .in_1(R3), .in_9({in_5[4], Rnd}), .in_2(R7), .in_3(R11), .in_4(R15), .in_5(R19),
    .in_6(R23), .in_7(R27), .in_8(R31));
  or or_18 (or_18_out, a, WriteReady, c, d);
  Random #(.width(2)) random_1 (.clk(Rnd_En), .out(Rnd));  // open: next, clr
  D_Flip_Flop START (.clk(Clock), .D(or_18_out), .Q(START_q), .preset(Clear));  // open: Qn, en, reset
  Demultiplexer #(.select(3), .enable("false")) demultiplexer_1 (
    .out0(L1A_O), .out1(L2A_O), .out2(L3A_O), .out3(L4A_O), .out4(L1B_O), .out5(L2B_O), .out6(L3B_O),
    .out7(L4B_O), .in(CacheWrite), .sel({in_5[4], Rnd}));
  Demultiplexer #(.select(2), .enable("false")) demultiplexer_2 (
    .out0(a), .out1(Rnd_En0), .out2(demultiplexer_2_out2), .in(START_q), .sel({Reader_Enable, Writer_Enable}));  // open: out3
  Multiplexer #(.width(16), .enable("false")) multiplexer_7 (
    .in0(Add16_Read), .in1(Add16_Write), .out(RAM_A), .sel(Writer));
  or or_19 (C_S, CS_1, CS_2);
  Demultiplexer #(.enable("false")) demultiplexer_3 (
    .out0(Rnd_En1), .out1(demultiplexer_3_out1), .in(demultiplexer_2_out2), .sel(Hit));
  or or_20 (or_20_out, Hit, Tag_Match, ~DirtyFlag);  // OR_Gate
  Demultiplexer #(.enable("false")) demultiplexer_4 (
    .out0(demultiplexer_4_out0), .out1(WriteHit), .in(Rnd_En0), .sel(or_20_out));
  Demultiplexer #(.select(3), .enable("false")) demultiplexer_5 (
    .out0(L1A_W), .out1(L2A_W), .out2(L3A_W), .out3(L4A_W), .out4(L1B_W), .out5(L2B_W), .out6(L3B_W),
    .out7(L4B_W), .in(CacheWrite), .sel({in_5[4], LineSel}));
  Demultiplexer #(.enable("false")) demultiplexer_6 (
    .out0(demultiplexer_6_out0), .out1(demultiplexer_6_out1), .in(Rnd_En1), .sel(DirtyFlag));
  D_Flip_Flop READ (.clk(Clock), .D(demultiplexer_3_out1), .Q(c), .reset(Clear));  // open: Qn, preset, en
  or or_21 (Writer0, demultiplexer_4_out0, w);
  D_Flip_Flop WRITE_D (.clk(Clock), .D(Writer0), .Q(WRITE_D_q), .reset(Clear));  // open: Qn, preset, en
  or or_22 (or_22_out, z, x, demultiplexer_6_out0);
  or or_23 (Writer1, demultiplexer_6_out1, y);
  Multiplexer #(.enable("false")) multiplexer_8 (.in0(L1A_O), .in1(L1A_W), .out(L1A), .sel(Hit));
  Multiplexer #(.enable("false")) multiplexer_9 (.in0(L2A_O), .in1(L2A_W), .out(L2A), .sel(Hit));
  Multiplexer #(.enable("false")) multiplexer_10 (.in0(L3A_O), .in1(L3A_W), .out(L3A), .sel(Hit));
  Multiplexer #(.enable("false")) multiplexer_11 (.in0(L4A_O), .in1(L4A_W), .out(L4A), .sel(Hit));
  Demultiplexer #(.enable("false")) demultiplexer_7 (
    .out0(w), .out1(demultiplexer_7_out1), .in(WRITE_D_q), .sel(Write_Flag));
  D_Flip_Flop READ_M (.clk(Clock), .D(or_22_out), .Q(Reader), .reset(Clear));  // open: Qn, preset, en
  D_Flip_Flop WRITE_D_2 (.clk(Clock), .D(Writer1), .Q(WRITE_D_2_q), .reset(Clear));  // open: Qn, preset, en
  Demultiplexer #(.enable("false")) demultiplexer_8 (.out0(x), .out1(CacheWrite1), .in(Reader), .sel(Read_Flag));
  Demultiplexer #(.enable("false")) demultiplexer_9 (.out0(y), .out1(z), .in(WRITE_D_2_q), .sel(Write_Flag));
  or or_24 (CacheWrite0, WriteHit, demultiplexer_7_out1);
  Multiplexer #(.enable("false")) multiplexer_12 (.in0(L1B_O), .in1(L1B_W), .out(L1B), .sel(Hit));
  Multiplexer #(.enable("false")) multiplexer_13 (.in0(L2B_O), .in1(L2B_W), .out(L2B), .sel(Hit));
  Multiplexer #(.enable("false")) multiplexer_14 (.in0(L3B_O), .in1(L3B_W), .out(L3B), .sel(Hit));
  Multiplexer #(.enable("false")) multiplexer_15 (.in0(L4B_O), .in1(L4B_W), .out(L4B), .sel(Hit));
  D_Flip_Flop WRITE (.clk(Clock), .D(CacheWrite0), .Q(WriteReady), .reset(Clear));  // open: Qn, preset, en
  D_Flip_Flop WRITE_B (.clk(Clock), .D(CacheWrite1), .Q(d), .reset(Clear));  // open: Qn, preset, en
  or or_25 (Writer, Writer0, Writer1);
  or or_26 (ReadReady, c, d);
  or or_27 (CacheWrite, CacheWrite0, CacheWrite1);
  or or_28 (Rnd_En, Rnd_En0, Rnd_En1);

  // Other names for the same wires on the sheet: Write_En = Writer_Enable; Read_En = Reader_Enable;
  //   Address[31:0] = in_5; Index = in_5[4]; b = WriteReady; ReadReady0 = c; CLR = Clear; ReadReady1 = d;
  //   Data[31:0] = Write_Data; Offset[1:0] = in_5[3:2]; Dirty[3:0] = Mask; RAM_MASK[3:0] = Mask;
  //   RAM_MASK_R[3:0] = {M3, M2, M1, M0}; Read_Data[31:0] = ReadOutput; ReadTime[3:0] = Read_Time; RW = R_W;
  //   Tag[14:0] = in_5[19:5]; WriteTime[3:0] = Write_Time

  // Notes on the sheet:
  //   INPUTS
  //   SPLITTING THE ADDRESS
  //   READER INPUTS
  //   GRUPO 1
  //   GRUPO 2
  //   WRITER INPUTS
  //   READER OUTPUTS
  //   OUTPUTS
  //   WRITER OUTPUTS
endmodule

module ControlUnit (
  input  Reader_Flag,
  input  Instruction_Flag,
  input  Clock,
  input  Clear,
  input  Halt,
  output Reader_Enable,
  output ID_Load,
  output Execute,
  output Read_Selector
);

  wire demultiplexer_2_out0, demultiplexer_2_out1, EXECUTE_q, ID_Load_0, or_1_out, or_3_out, READ_q, x, y;

  or or_1 (or_1_out, x, Execute);
  D_Flip_Flop READ (.clk(Clock), .D(or_1_out), .Q(READ_q), .preset(Clear));  // open: Qn, en, reset
  and and_1 (Read_Selector, READ_q, ~Clear);  // AND_Gate
  Demultiplexer #(.enable("false")) demultiplexer_1 (.out0(x), .out1(ID_Load_0), .in(Read_Selector), .sel(Reader_Flag));
  or or_2 (ID_Load, ID_Load_0, Execute);
  or or_3 (or_3_out, ID_Load_0, y);
  D_Flip_Flop u_EXECUTE (.clk(Clock), .D(or_3_out), .Q(EXECUTE_q), .reset(Clear));  // open: Qn, preset, en
  Demultiplexer #(.enable("false")) demultiplexer_2 (
    .out0(demultiplexer_2_out0), .out1(demultiplexer_2_out1), .in(EXECUTE_q), .sel(Halt));
  Demultiplexer #(.enable("false")) demultiplexer_3 (
    .out0(y), .out1(Execute), .in(demultiplexer_2_out0), .sel(Instruction_Flag));
  D_Flip_Flop u_HALT (.clk(Clock), .D(demultiplexer_2_out1), .reset(Clear));  // open: Q, Qn, preset, en

  assign Reader_Enable = Read_Selector;

  // Other names for the same wires on the sheet: CLR = Clear; InstFlag = Instruction_Flag; Read_Sel = Read_Selector;
  //   Reader_En = Read_Selector; ReadFlag = Reader_Flag; ID_Load_1 = Execute; z = Execute
endmodule

module MUX1bit (
  input  in_1,
  input  [31:0] in_2,
  input  [31:0] in_3,
  output [31:0] out_4
);

  wire L0, L1;

  Decoder #(.enable("false")) decoder_1 (.out0(L0), .out1(L1), .sel(in_1));
  assign out_4 = L0 ? in_2 : 32'bz;  // Controlled_Buffer controlled_buffer_1
  assign out_4 = L1 ? in_3 : 32'bz;  // Controlled_Buffer controlled_buffer_2

  // Other names for the same wires on the sheet: I1[31:0] = in_2; I2[31:0] = in_3; IS = in_1
endmodule

module MUX2bits (
  input  [1:0] in_1,
  input  [31:0] in_2,
  input  [31:0] in_3,
  input  [31:0] in_4,
  input  [31:0] in_5,
  output [31:0] out_6
);

  wire L0, L1, L2, L3;

  Decoder #(.select(2), .enable("false")) decoder_1 (.out0(L0), .out1(L1), .out2(L2), .out3(L3), .sel(in_1));
  assign out_6 = L0 ? in_2 : 32'bz;  // Controlled_Buffer controlled_buffer_1
  assign out_6 = L1 ? in_3 : 32'bz;  // Controlled_Buffer controlled_buffer_2
  assign out_6 = L2 ? in_4 : 32'bz;  // Controlled_Buffer controlled_buffer_3
  assign out_6 = L3 ? in_5 : 32'bz;  // Controlled_Buffer controlled_buffer_4

  // Other names for the same wires on the sheet: I1[31:0] = in_2; I2[31:0] = in_3; I3[31:0] = in_4; I4[31:0] = in_5;
  //   IS[1:0] = in_1
endmodule

module MUX3bits_Transistors (
  input  [31:0] in_1,
  input  [31:0] in_2,
  input  [31:0] in_3,
  input  [31:0] in_4,
  input  [31:0] in_5,
  input  [31:0] in_6,
  input  [31:0] in_7,
  input  [31:0] in_8,
  input  [2:0] in_9,
  output [31:0] out_10
);

  wire L0, L0_n, L1, L1_n, L2, L2_n, L3, L3_n, L4, L4_n, L5, L5_n, L6, L6_n, L7, L7_n;

  Decoder #(.select(3), .enable("false")) decoder_1 (
    .out0(L0), .out1(L1), .out2(L2), .out3(L3), .out4(L4), .out5(L5), .out6(L6), .out7(L7), .sel(in_9));
  assign {L7_n, L6_n, L5_n, L4_n, L3_n, L2_n, L1_n, L0_n} = ~{L7, L6, L5, L4, L3, L2, L1, L0};  // NOT_Gate not_1, 8 bits wide
  Transistor #(.width(32)) transistor_1 (.in(in_1), .out(out_10), .gate(L0_n));
  Transistor #(.width(32)) transistor_2 (.in(in_2), .out(out_10), .gate(L1_n));
  Transistor #(.width(32)) transistor_3 (.in(in_3), .out(out_10), .gate(L2_n));
  Transistor #(.width(32)) transistor_4 (.in(in_4), .out(out_10), .gate(L3_n));
  Transistor #(.width(32)) transistor_5 (.in(in_5), .out(out_10), .gate(L4_n));
  Transistor #(.width(32)) transistor_6 (.in(in_6), .out(out_10), .gate(L5_n));
  Transistor #(.width(32)) transistor_7 (.in(in_7), .out(out_10), .gate(L6_n));
  Transistor #(.width(32)) transistor_8 (.in(in_8), .out(out_10), .gate(L7_n));

  // Other names for the same wires on the sheet: I1[31:0] = in_1; I2[31:0] = in_2; I3[31:0] = in_3; I4[31:0] = in_4;
  //   I5[31:0] = in_5; I6[31:0] = in_6; I7[31:0] = in_7; I8[31:0] = in_8; IS[2:0] = in_9
endmodule

module MUX4bits (
  input  [31:0] in_1,
  input  [31:0] in_2,
  input  [31:0] in_3,
  input  [31:0] in_4,
  input  [31:0] in_5,
  input  [31:0] in_6,
  input  [31:0] in_7,
  input  [31:0] in_8,
  input  [31:0] in_9,
  input  [31:0] in_10,
  input  [31:0] in_11,
  input  [31:0] in_12,
  input  [31:0] in_13,
  input  [31:0] in_14,
  input  [31:0] in_15,
  input  [31:0] in_16,
  input  [3:0] in_17,
  output [31:0] out_18
);

  wire L0, L1, L2, L3, L4, L5, L6, L7, L8, L9, L10, L11, L12, L13, L14, L15;

  Decoder #(.select(4), .enable("false")) decoder_1 (
    .out0(L0), .out1(L1), .out2(L2), .out3(L3), .out4(L4), .out5(L5), .out6(L6), .out7(L7), .out8(L8),
    .out9(L9), .out10(L10), .out11(L11), .out12(L12), .out13(L13), .out14(L14), .out15(L15), .sel(in_17));
  assign out_18 = L0 ? in_1 : 32'bz;  // Controlled_Buffer controlled_buffer_1
  assign out_18 = L1 ? in_2 : 32'bz;  // Controlled_Buffer controlled_buffer_2
  assign out_18 = L2 ? in_3 : 32'bz;  // Controlled_Buffer controlled_buffer_3
  assign out_18 = L3 ? in_4 : 32'bz;  // Controlled_Buffer controlled_buffer_4
  assign out_18 = L4 ? in_5 : 32'bz;  // Controlled_Buffer controlled_buffer_5
  assign out_18 = L5 ? in_6 : 32'bz;  // Controlled_Buffer controlled_buffer_6
  assign out_18 = L6 ? in_7 : 32'bz;  // Controlled_Buffer controlled_buffer_7
  assign out_18 = L7 ? in_8 : 32'bz;  // Controlled_Buffer controlled_buffer_8
  assign out_18 = L8 ? in_9 : 32'bz;  // Controlled_Buffer controlled_buffer_9
  assign out_18 = L9 ? in_10 : 32'bz;  // Controlled_Buffer controlled_buffer_10
  assign out_18 = L10 ? in_11 : 32'bz;  // Controlled_Buffer controlled_buffer_11
  assign out_18 = L11 ? in_12 : 32'bz;  // Controlled_Buffer controlled_buffer_12
  assign out_18 = L12 ? in_13 : 32'bz;  // Controlled_Buffer controlled_buffer_13
  assign out_18 = L13 ? in_14 : 32'bz;  // Controlled_Buffer controlled_buffer_14
  assign out_18 = L14 ? in_15 : 32'bz;  // Controlled_Buffer controlled_buffer_15
  assign out_18 = L15 ? in_16 : 32'bz;  // Controlled_Buffer controlled_buffer_16

  // Other names for the same wires on the sheet: I1[31:0] = in_1; I2[31:0] = in_2; I3[31:0] = in_3; I4[31:0] = in_4;
  //   I5[31:0] = in_5; I6[31:0] = in_6; I7[31:0] = in_7; I8[31:0] = in_8; I9[31:0] = in_9; I10[31:0] = in_10;
  //   I11[31:0] = in_11; I12[31:0] = in_12; I13[31:0] = in_13; I14[31:0] = in_14; I15[31:0] = in_15;
  //   I16[31:0] = in_16; IS[3:0] = in_17
endmodule

module MUX5bits (
  input  [31:0] in_1,
  input  [31:0] in_2,
  input  [31:0] in_3,
  input  [31:0] in_4,
  input  [31:0] in_5,
  input  [31:0] in_6,
  input  [31:0] in_7,
  input  [31:0] in_8,
  input  [31:0] in_9,
  input  [31:0] in_10,
  input  [31:0] in_11,
  input  [31:0] in_12,
  input  [31:0] in_13,
  input  [31:0] in_14,
  input  [31:0] in_15,
  input  [31:0] in_16,
  input  [31:0] in_17,
  input  [31:0] in_18,
  input  [31:0] in_19,
  input  [31:0] in_20,
  input  [31:0] in_21,
  input  [31:0] in_22,
  input  [31:0] in_23,
  input  [31:0] in_24,
  input  [31:0] in_25,
  input  [31:0] in_26,
  input  [31:0] in_27,
  input  [31:0] in_28,
  input  [31:0] in_29,
  input  [31:0] in_30,
  input  [31:0] in_31,
  input  [31:0] in_32,
  input  [4:0] in_33,
  output [31:0] out_34
);

  wire L0, L1, L2, L3, L4, L5, L6, L7, L8, L9, L10, L11, L12, L13, L14, L15, L16, L17, L18, L19, L20, L21,
       L22, L23, L24, L25, L26, L27, L28, L29, L30, L31;

  Decoder #(.select(5), .enable("false")) decoder_1 (
    .out0(L0), .out1(L1), .out2(L2), .out3(L3), .out4(L4), .out5(L5), .out6(L6), .out7(L7), .out8(L8),
    .out9(L9), .out10(L10), .out11(L11), .out12(L12), .out13(L13), .out14(L14), .out15(L15), .out16(L16),
    .out17(L17), .out18(L18), .out19(L19), .out20(L20), .out21(L21), .out22(L22), .out23(L23), .out24(L24),
    .out25(L25), .out26(L26), .out27(L27), .out28(L28), .out29(L29), .out30(L30), .out31(L31), .sel(in_33));
  assign out_34 = L0 ? in_1 : 32'bz;  // Controlled_Buffer controlled_buffer_1
  assign out_34 = L1 ? in_2 : 32'bz;  // Controlled_Buffer controlled_buffer_2
  assign out_34 = L2 ? in_3 : 32'bz;  // Controlled_Buffer controlled_buffer_3
  assign out_34 = L3 ? in_4 : 32'bz;  // Controlled_Buffer controlled_buffer_4
  assign out_34 = L4 ? in_5 : 32'bz;  // Controlled_Buffer controlled_buffer_5
  assign out_34 = L5 ? in_6 : 32'bz;  // Controlled_Buffer controlled_buffer_6
  assign out_34 = L6 ? in_7 : 32'bz;  // Controlled_Buffer controlled_buffer_7
  assign out_34 = L7 ? in_8 : 32'bz;  // Controlled_Buffer controlled_buffer_8
  assign out_34 = L8 ? in_9 : 32'bz;  // Controlled_Buffer controlled_buffer_9
  assign out_34 = L9 ? in_10 : 32'bz;  // Controlled_Buffer controlled_buffer_10
  assign out_34 = L10 ? in_11 : 32'bz;  // Controlled_Buffer controlled_buffer_11
  assign out_34 = L11 ? in_12 : 32'bz;  // Controlled_Buffer controlled_buffer_12
  assign out_34 = L12 ? in_13 : 32'bz;  // Controlled_Buffer controlled_buffer_13
  assign out_34 = L13 ? in_14 : 32'bz;  // Controlled_Buffer controlled_buffer_14
  assign out_34 = L14 ? in_15 : 32'bz;  // Controlled_Buffer controlled_buffer_15
  assign out_34 = L15 ? in_16 : 32'bz;  // Controlled_Buffer controlled_buffer_16
  assign out_34 = L16 ? in_17 : 32'bz;  // Controlled_Buffer controlled_buffer_17
  assign out_34 = L17 ? in_18 : 32'bz;  // Controlled_Buffer controlled_buffer_18
  assign out_34 = L18 ? in_19 : 32'bz;  // Controlled_Buffer controlled_buffer_19
  assign out_34 = L19 ? in_20 : 32'bz;  // Controlled_Buffer controlled_buffer_20
  assign out_34 = L20 ? in_21 : 32'bz;  // Controlled_Buffer controlled_buffer_21
  assign out_34 = L21 ? in_22 : 32'bz;  // Controlled_Buffer controlled_buffer_22
  assign out_34 = L22 ? in_23 : 32'bz;  // Controlled_Buffer controlled_buffer_23
  assign out_34 = L23 ? in_24 : 32'bz;  // Controlled_Buffer controlled_buffer_24
  assign out_34 = L24 ? in_25 : 32'bz;  // Controlled_Buffer controlled_buffer_25
  assign out_34 = L25 ? in_26 : 32'bz;  // Controlled_Buffer controlled_buffer_26
  assign out_34 = L26 ? in_27 : 32'bz;  // Controlled_Buffer controlled_buffer_27
  assign out_34 = L27 ? in_28 : 32'bz;  // Controlled_Buffer controlled_buffer_28
  assign out_34 = L28 ? in_29 : 32'bz;  // Controlled_Buffer controlled_buffer_29
  assign out_34 = L29 ? in_30 : 32'bz;  // Controlled_Buffer controlled_buffer_30
  assign out_34 = L30 ? in_31 : 32'bz;  // Controlled_Buffer controlled_buffer_31
  assign out_34 = L31 ? in_32 : 32'bz;  // Controlled_Buffer controlled_buffer_32

  // Other names for the same wires on the sheet: I1[31:0] = in_1; I2[31:0] = in_2; I3[31:0] = in_3; I4[31:0] = in_4;
  //   I5[31:0] = in_5; I6[31:0] = in_6; I7[31:0] = in_7; I8[31:0] = in_8; I9[31:0] = in_9; I10[31:0] = in_10;
  //   I11[31:0] = in_11; I12[31:0] = in_12; I13[31:0] = in_13; I14[31:0] = in_14; I15[31:0] = in_15;
  //   I16[31:0] = in_16; I17[31:0] = in_17; I18[31:0] = in_18; I19[31:0] = in_19; I20[31:0] = in_20;
  //   I21[31:0] = in_21; I22[31:0] = in_22; I23[31:0] = in_23; I24[31:0] = in_24; I25[31:0] = in_25;
  //   I26[31:0] = in_26; I27[31:0] = in_27; I28[31:0] = in_28; I29[31:0] = in_29; I30[31:0] = in_30;
  //   I31[31:0] = in_31; I32[31:0] = in_32; IS[4:0] = in_33
endmodule

module MUX1bit_4Data (
  input  in_1,
  input  [3:0] in_2,
  input  [3:0] in_3,
  output [3:0] out_4
);

  wire L0, L1;

  Decoder #(.enable("false")) decoder_1 (.out0(L0), .out1(L1), .sel(in_1));
  assign out_4 = L0 ? in_2 : 4'bz;  // Controlled_Buffer controlled_buffer_1
  assign out_4 = L1 ? in_3 : 4'bz;  // Controlled_Buffer controlled_buffer_2

  // Other names for the same wires on the sheet: I1[3:0] = in_2; I2[3:0] = in_3; IS = in_1
endmodule

module MUX3bits_4Data (
  input  [3:0] in_1,
  input  [3:0] in_2,
  input  [3:0] in_3,
  input  [3:0] in_4,
  input  [3:0] in_5,
  input  [3:0] in_6,
  input  [3:0] in_7,
  input  [3:0] in_8,
  input  [2:0] in_9,
  output [3:0] out_10
);

  wire L0, L1, L2, L3, L4, L5, L6, L7;

  Decoder #(.select(3), .enable("false")) decoder_1 (
    .out0(L0), .out1(L1), .out2(L2), .out3(L3), .out4(L4), .out5(L5), .out6(L6), .out7(L7), .sel(in_9));
  assign out_10 = L0 ? in_1 : 4'bz;  // Controlled_Buffer controlled_buffer_1
  assign out_10 = L1 ? in_2 : 4'bz;  // Controlled_Buffer controlled_buffer_2
  assign out_10 = L2 ? in_3 : 4'bz;  // Controlled_Buffer controlled_buffer_3
  assign out_10 = L3 ? in_4 : 4'bz;  // Controlled_Buffer controlled_buffer_4
  assign out_10 = L4 ? in_5 : 4'bz;  // Controlled_Buffer controlled_buffer_5
  assign out_10 = L5 ? in_6 : 4'bz;  // Controlled_Buffer controlled_buffer_6
  assign out_10 = L6 ? in_7 : 4'bz;  // Controlled_Buffer controlled_buffer_7
  assign out_10 = L7 ? in_8 : 4'bz;  // Controlled_Buffer controlled_buffer_8

  // Other names for the same wires on the sheet: I1[3:0] = in_1; I2[3:0] = in_2; I3[3:0] = in_3; I4[3:0] = in_4;
  //   I5[3:0] = in_5; I6[3:0] = in_6; I7[3:0] = in_7; I8[3:0] = in_8; IS[2:0] = in_9
endmodule

module MUX1bit_15Data (
  input  in_1,
  input  [14:0] in_2,
  input  [14:0] in_3,
  output [14:0] out_4
);

  wire L0, L1;

  Decoder #(.enable("false")) decoder_1 (.out0(L0), .out1(L1), .sel(in_1));
  assign out_4 = L0 ? in_2 : 15'bz;  // Controlled_Buffer controlled_buffer_1
  assign out_4 = L1 ? in_3 : 15'bz;  // Controlled_Buffer controlled_buffer_2

  // Other names for the same wires on the sheet: I1[14:0] = in_2; I2[14:0] = in_3; IS = in_1
endmodule

module Switcher (
  input  [31:0] in_1,
  output [31:0] out_2
);


  assign out_2 = {in_1[7:0], in_1[15:8], in_1[23:16], in_1[31:24]};

  // Other names for the same wires on the sheet: In[31:0] = in_1;
  //   Out[31:0] = {in_1[7:0], in_1[15:8], in_1[23:16], in_1[31:24]}
endmodule

module StoreWord (
  input  in_1,
  input  in_2,
  input  in_3,
  input  in_4,
  output out_5,
  output out_6
);

  wire demultiplexer_1_out1, or_1_out, or_2_out, START_q, x, y;

  or or_1 (or_1_out, x, out_5);
  D_Flip_Flop START (.clk(in_3), .D(or_1_out), .Q(START_q), .preset(in_4));  // open: Qn, en, reset
  Demultiplexer #(.enable("false")) demultiplexer_1 (.out0(x), .out1(demultiplexer_1_out1), .in(START_q), .sel(in_1));
  or or_2 (or_2_out, y, demultiplexer_1_out1);
  D_Flip_Flop WRITE (.clk(in_3), .D(or_2_out), .Q(out_6), .reset(in_4));  // open: Qn, preset, en
  Demultiplexer #(.enable("false")) demultiplexer_2 (.out0(y), .out1(out_5), .in(out_6), .sel(in_2));

  // Other names for the same wires on the sheet: Clock = in_3; CLR = in_4; Start = in_1; Write_En = out_6;
  //   Write_Flag = in_2; Ready = out_5; z = out_5
endmodule

module StoreWord_Push (
  input  in_1,
  input  in_2,
  input  in_3,
  input  in_4,
  output out_5,
  output out_6,
  output out_7,
  output out_8,
  output out_9
);

  wire or_1_out, or_2_out, START_q, x, y;

  or or_1 (or_1_out, x, out_5);
  D_Flip_Flop START (.clk(in_3), .D(or_1_out), .Q(START_q), .preset(in_4));  // open: Qn, en, reset
  Demultiplexer #(.enable("false")) demultiplexer_1 (.out0(x), .out1(out_7), .in(START_q), .sel(in_1));
  or or_2 (or_2_out, y, out_7);
  Demultiplexer #(.enable("false")) demultiplexer_2 (.out0(y), .out1(out_5), .in(out_6), .sel(in_2));
  D_Flip_Flop WRITE (.clk(in_3), .D(or_2_out), .Q(out_6), .reset(in_4));  // open: Qn, preset, en

  assign out_8 = out_7;
  assign out_9 = out_7;

  // Other names for the same wires on the sheet: Clock = in_3; CLR = in_4; L_R31_1 = out_7; PP1_2 = out_7;
  //   PP2 = out_7; Start = in_1; Write_En = out_6; Write_Flag = in_2; Ready = out_5; z = out_5
endmodule

module LoadWord (
  input  in_1,
  input  in_2,
  input  in_3,
  input  in_4,
  output out_5,
  output out_6
);

  wire demultiplexer_1_out1, or_1_out, READ_q, START_q, x, y;

  D_Flip_Flop START (.clk(in_3), .D(or_1_out), .Q(START_q), .preset(in_4));  // open: Qn, en, reset
  or or_1 (or_1_out, x, out_5);
  Demultiplexer #(.enable("false")) demultiplexer_1 (.out0(x), .out1(demultiplexer_1_out1), .in(START_q), .sel(in_1));
  or or_2 (out_6, y, demultiplexer_1_out1);
  D_Flip_Flop READ (.clk(in_3), .D(out_6), .Q(READ_q), .reset(in_4));  // open: Qn, preset, en
  Demultiplexer #(.enable("false")) demultiplexer_2 (.out0(y), .out1(out_5), .in(READ_q), .sel(in_2));

  // Other names for the same wires on the sheet: Clock = in_3; CLR = in_4; Read_En = out_6; Read_Flag = in_2;
  //   Start = in_1; Ready = out_5; z = out_5
endmodule

module MemoryReader (
  input  Enable,
  input  Clock,
  input  Clear,
  input  [3:0] Read_Time,
  input  [31:0] Address_32bits,
  output Ready,
  output C_S,
  output [15:0] Add16
);

  wire C_S0, C_S1, demultiplexer_1_out1, or_1_out, START_q, tunnel, x, y;
  wire [3:0] Counter;

  Counter #(.width(4), .max('hf)) counter_1 (
    .load(Ready), .D(4'b0000), .count(C_S0), .Q(Counter), .clk(Clock));  // open: carry, clr
  or or_1 (or_1_out, x, Ready);
  D_Flip_Flop START (.clk(Clock), .D(or_1_out), .Q(START_q), .preset(Clear));  // open: Qn, en, reset
  Demultiplexer #(.enable("false")) demultiplexer_1 (.out0(x), .out1(demultiplexer_1_out1), .in(START_q), .sel(Enable));
  or or_2 (C_S0, y, demultiplexer_1_out1);
  Comparator #(.width(4), .mode("unsigned")) comparator_1 (.a(Counter), .b(Read_Time), .eq(tunnel));  // open: gt, lt
  D_Flip_Flop READ (.clk(Clock), .D(C_S0), .Q(C_S1), .reset(Clear));  // open: Qn, preset, en
  Demultiplexer #(.enable("false")) demultiplexer_2 (.out0(y), .out1(Ready), .in(C_S1), .sel(tunnel));
  or or_3 (C_S, C_S0, C_S1);

  assign Add16 = Address_32bits[19:4];

  // Other names for the same wires on the sheet: Add32[31:0] = Address_32bits; CLR = Clear; En = Enable; Inc = C_S0;
  //   Offset[1:0] = Address_32bits[3:2]; ReadTime[3:0] = Read_Time; Ld = Ready; z = Ready
endmodule

module MemoryWriter (
  input  Enable,
  input  Clock,
  input  Clear,
  input  [3:0] Write_Time,
  input  [31:0] Address_32bits,
  output Ready,
  output C_S,
  output [3:0] Mask,
  output [15:0] Add16,
  output R_W
);

  wire C_S0, C_S1, demultiplexer_1_out1, or_1_out, START_q, tunnel, x, y;
  wire [3:0] Counter;

  Counter #(.width(4), .max('hf)) counter_1 (
    .load(Ready), .D(4'b0000), .count(C_S0), .Q(Counter), .clk(Clock));  // open: carry, clr
  or or_1 (or_1_out, x, Ready);
  D_Flip_Flop START (.clk(Clock), .D(or_1_out), .Q(START_q), .preset(Clear));  // open: Qn, en, reset
  Demultiplexer #(.enable("false")) demultiplexer_1 (.out0(x), .out1(demultiplexer_1_out1), .in(START_q), .sel(Enable));
  or or_2 (C_S0, y, demultiplexer_1_out1);
  Comparator #(.width(4), .mode("unsigned")) comparator_1 (.a(Counter), .b(Write_Time), .eq(tunnel));  // open: gt, lt
  D_Flip_Flop READ (.clk(Clock), .D(C_S0), .Q(C_S1), .reset(Clear));  // open: Qn, preset, en
  Demultiplexer #(.enable("false")) demultiplexer_2 (.out0(y), .out1(Ready), .in(C_S1), .sel(tunnel));
  or or_3 (C_S, C_S0, C_S1);
  Decoder #(.select(2), .enable("false")) decoder_1 (
    .out0(Mask[0]), .out1(Mask[1]), .out2(Mask[2]), .out3(Mask[3]), .sel(Address_32bits[3:2]));
  or or_4 (R_W, C_S0, C_S1);

  assign Add16 = Address_32bits[19:4];

  // Other names for the same wires on the sheet: Add32[31:0] = Address_32bits; CLR = Clear; En = Enable;
  //   Offset[1:0] = Address_32bits[3:2]; Inc = C_S0; R_W0 = C_S0; R_W1 = C_S1; WriteTime[3:0] = Write_Time;
  //   Ld = Ready; z = Ready
endmodule

module test (
  input  in_1,
  input  [3:0] in_2,
  output [3:0] out_3
);

  Transistor #(.width(4)) transistor_1 (.in(in_2), .out(out_3), .gate(in_1));
  // NOT_Gate not_1 is placed but not wired
  Controlled_Buffer #(.width(32)) controlled_buffer_1 ();  // open: in, out, en
endmodule
